// Logisim project cpu21-riscv.circ as structural Verilog: 25 circuits, main circuit ◇单周期RISC-V
module \单周期RISC_V  (
  input  IR1,
  input  IR2,
  input  IR3,
  output RegWrite,
  output MemWrite,
  output [31:0] PC,
  output [31:0] IR,
  output [31:0] RDin,
  output [31:0] MDin,
  output [31:0] LedData
);

  wire alu_1_equal, alu_1_out_4, and_1_out, and_2_out, and_3_out, and_4_out, B, CLK, clock_1_out,
       comparator_1_eq, comparator_2_eq, comparator_2_lt, d_ff_1_p1, d_ff_2_q, ecall, Go, halt, IR1_t, IR2_t,
       IR3_t, IRA, IRB, IRC, JAL, JALR, MemToReg, nand_1_out, not_1_out, not_2_out, or_4_out, or_6_out, RST,
       S_type, SB, URET, W1, W2, W3, \单周期硬布线控制器_1_alu_src , \单周期硬布线控制器_1_beq , \单周期硬布线控制器_1_bge ,
       \单周期硬布线控制器_1_bne ;
  wire [1:0] priority_encoder_1_out, priority_encoder_2_out;
  wire [3:0] \单周期硬布线控制器_1_alu_op ;
  wire [4:0] multiplexer_2_out, multiplexer_3_out;
  wire [11:0] multiplexer_4_out;
  wire [12:0] CNT_num;
  wire [15:0] multiplexer_7_out, \总周期数 ;
  wire [31:0] adder_2_out, adder_3_out, alu_res, B_bias, bit_extender_1_out, bit_extender_2_out,
       bit_extender_3_out, bit_extender_4_out, J_bias, MDout, multiplexer_1_out, multiplexer_5_out, PC_1, R1,
       R2out, SBin;

  Button \u_继续运行  (.out(Go));
  Button _1 (.out(IRA));
  Button _2 (.out(IRB));
  Button _3 (.out(IRC));
  LED #(.active("true")) led_1 (.in(W1));
  LED #(.active("true")) led_2 (.in(W2));
  LED #(.active("true")) led_3 (.in(W3));
  Adder #(.width(32)) adder_1 (.a(PC), .b(32'h4), .out(PC_1));  // open: cin, cout
  Adder #(.width(32)) adder_2 (.a(PC), .b(B_bias), .out(adder_2_out));  // open: cin, cout
  Adder #(.width(32)) adder_3 (.a(PC), .b(J_bias), .out(adder_3_out));  // open: cin, cout
  Hex_Digit_Display hex_digit_display_1 (.value(LedData[31:28]));  // open: dp
  Priority_Encoder #(.select(2), .disabled("Z")) priority_encoder_1 (
    .in0(1'b1), .in1(B), .in2(JAL), .in3(JALR), .out(priority_encoder_1_out));  // open: gs, en_out, en_in
  Multiplexer #(.select(2), .width(32), .disabled("Z"), .enable("false")) multiplexer_1 (
    .in0(PC_1), .in1(adder_2_out), .in2(adder_3_out), .in3(alu_res), .out(multiplexer_1_out),
    .sel(priority_encoder_1_out));
  not not_1 (not_1_out, halt);
  Hex_Digit_Display hex_digit_display_2 (.value(LedData[23:20]));  // open: dp
  Hex_Digit_Display hex_digit_display_3 (.value(LedData[27:24]));  // open: dp
  not not_2 (not_2_out, halt);
  Register #(.width(32), .trigger("rising"), .Select("low")) u_PC (
    .D(multiplexer_1_out), .en(not_1_out), .Q(PC), .clk(CLK), .clr(RST));
  Comparator #(.width(32), .mode("unsigned")) comparator_1 (.a(R1), .b(32'h22), .eq(comparator_1_eq));  // open: gt, lt
  Hex_Digit_Display hex_digit_display_4 (.value(LedData[15:12]));  // open: dp
  Hex_Digit_Display hex_digit_display_5 (.value(LedData[19:16]));  // open: dp
  Counter #(.width(16), .max('hffff), .ongoal("wrap"), .trigger("rising"), .behavior("new")) counter_1 (
    .count(not_2_out), .Q(\总周期数 ), .clk(CLK));  // open: load, D, carry, clr, preset, down
  // RiscV_Probe riscv_probe_1: pin names not known; wires that end beside it: PC[11:2], IR
  // D_Flip_Flop #(.trigger("latch"), .Pre_Clr_Positions("ABOVE_BELOW"), .NegatePresetClear("false"), .enable("true"), .NewFFLayout("true")) d_ff_1: pin names not known; wires that end beside it: d_ff_1_p1, ecall, Go, halt
  not not_3 (d_ff_1_p1, comparator_1_eq);
  Register #(.width(32), .trigger("rising"), .Select("low")) register_1 (
    .D(MDin), .en(and_1_out), .Q(LedData), .clk(CLK));  // open: clr
  and and_1 (and_1_out, comparator_1_eq, ecall);
  Hex_Digit_Display hex_digit_display_6 (.value(LedData[7:4]));  // open: dp
  Hex_Digit_Display hex_digit_display_7 (.value(LedData[11:8]));  // open: dp
  // Probe on \总周期数 
  ROM #(.addrWidth(10), .dataWidth(32), .Select("high")) rom_1 (.addr(PC[11:2]), .data(IR));
  Hex_Digit_Display hex_digit_display_8 (.value(LedData[3:0]));  // open: dp
  \单周期硬布线控制器  \u_单周期硬布线控制器_1  (
    .Funct({IR[30], IR[25], IR[14:12]}), .OP(IR[6:2]), .ALU_OP(\单周期硬布线控制器_1_alu_op ), .MemToReg(MemToReg),
    .MemWrite(MemWrite), .ALU_SRC(\单周期硬布线控制器_1_alu_src ), .RegWrite(RegWrite), .ecall(ecall),
    .S_type(S_type), .Jalr(JALR), .Beq(\单周期硬布线控制器_1_beq ), .JAL(JAL), .Bne(\单周期硬布线控制器_1_bne ), .in_3(IR[21]),
    .uret(URET), .BGE(\单周期硬布线控制器_1_bge ), .SB(SB));  // open: rs1, rs2, csrrsi, csrrci
  Multiplexer #(.select(1), .width(5), .disabled("Z"), .enable("false")) multiplexer_2 (
    .in0(IR[19:15]), .in1(5'b10001), .out(multiplexer_2_out), .sel(ecall));
  Multiplexer #(.select(1), .width(5), .disabled("Z"), .enable("false")) multiplexer_3 (
    .in0(IR[24:20]), .in1(5'b01010), .out(multiplexer_3_out), .sel(ecall));
  Multiplexer #(.select(1), .width(12), .disabled("Z"), .enable("false")) multiplexer_4 (
    .in0(IR[31:20]), .in1({IR[31:25], IR[11:7]}), .out(multiplexer_4_out), .sel(S_type));
  or or_1 (IR1_t, IR1, IRA);
  assign bit_extender_1_out = {{20{multiplexer_4_out[11]}}, multiplexer_4_out};  // Bit_Extender bit_extender_1
  assign bit_extender_2_out = {{20{IR[31]}}, {IR[31], IR[7], IR[30:25], IR[11:8]}};  // Bit_Extender bit_extender_2
  assign bit_extender_3_out = {{12{IR[31]}}, {IR[31], IR[19:12], IR[20], IR[30:21]}};  // Bit_Extender bit_extender_3
  or or_2 (IR2_t, IR2, IRB);
  Regifile regifile_1 (
    .Din(RDin), .Clk(CLK), .R1(R1), .R2(R2out), .WE(RegWrite), .W_num(IR[11:7]), .R1_num(multiplexer_2_out),
    .R2_num(multiplexer_3_out));
  Shifter #(.width(32), .shift("ll")) shifter_1 (.in(bit_extender_2_out), .\dist (5'b00001), .out(B_bias));
  Shifter #(.width(32), .shift("ll")) shifter_2 (.in(bit_extender_3_out), .\dist (5'b00001), .out(J_bias));
  Multiplexer #(.select(1), .width(32), .disabled("Z"), .enable("false")) multiplexer_5 (
    .in0(R2out), .in1(bit_extender_1_out), .out(multiplexer_5_out), .sel(\单周期硬布线控制器_1_alu_src ));
  or or_3 (IR3_t, IR3, IRC);
  Multiplexer #(.select(1), .width(32), .disabled("Z"), .enable("false")) multiplexer_6 (
    .in0(R2out), .in1(SBin), .out(MDin), .sel(SB));
  ALU alu_1 (
    .X(R1), .Y(multiplexer_5_out), .AluOP(\单周期硬布线控制器_1_alu_op ), .Equal(alu_1_equal), .Result(alu_res),
    .out_4(alu_1_out_4));  // open: Result_2, out_6
  or or_4 (or_4_out, MemWrite, SB);
  and and_2 (and_2_out, \单周期硬布线控制器_1_beq , alu_1_equal);
  and and_3 (and_3_out, \单周期硬布线控制器_1_bne , ~alu_1_equal);  // AND_Gate
  and and_4 (and_4_out, \单周期硬布线控制器_1_bge , alu_1_out_4);
  RAM #(.addrWidth(10), .dataWidth(32), .bus("separate"), .Select("high")) ram_1 (
    .addr(alu_res[11:2]), .din(MDin), .data(MDout), .str(or_4_out), .sel(1'b1), .clk(CLK), .ld(1'b1),
    .clr(RST));
  or or_5 (B, and_2_out, and_3_out, and_4_out);
  Multiplexer #(.select(1), .width(16), .disabled("Z"), .enable("false")) multiplexer_7 (
    .in0(MDout[15:0]), .in1(MDout[31:16]), .out(multiplexer_7_out), .sel(alu_res[1]));
  Multiplexer #(.select(2), .width(32), .disabled("Z"), .enable("false")) multiplexer_8 (
    .in0({MDout[31:8], R2out[7:0]}), .in1({MDout[31:16], R2out[7:0], MDout[7:0]}),
    .in2({MDout[31:24], R2out[7:0], MDout[15:0]}), .in3({R2out[7:0], MDout[23:0]}), .out(SBin),
    .sel(alu_res[1:0]));
  or or_6 (or_6_out, JAL, JALR);
  Priority_Encoder #(.select(2), .disabled("Z")) priority_encoder_2 (
    .in0(1'b1), .in1(MemToReg), .in3(or_6_out), .out(priority_encoder_2_out));  // open: in2, gs, en_out, en_in
  assign bit_extender_4_out = {{16{1'b0}}, multiplexer_7_out};  // Bit_Extender bit_extender_4
  Multiplexer #(.select(2), .width(32), .disabled("Z"), .enable("false")) multiplexer_9 (
    .in0(alu_res), .in1(MDout), .in2(bit_extender_4_out), .in3(PC_1), .out(RDin), .sel(priority_encoder_2_out));
  D_Flip_Flop #(.trigger("high"), .Pre_Clr_Positions("LEGACY"), .NegatePresetClear("false"), .enable("true"), .NewFFLayout("false")) d_ff_2 (.Q(d_ff_2_q));  // open: clk, D, Qn, preset, en, reset
  // Probe on 13'h609
  Comparator #(.width(13), .mode("twosComplement")) comparator_2 (
    .a(CNT_num), .b(13'h609), .eq(comparator_2_eq), .lt(comparator_2_lt));  // open: gt
  Clock #(.highDuration(1), .lowDuration(1)) clock_1 (.out(clock_1_out));
  Counter #(.width(13), .max('h1fff), .ongoal("stay"), .trigger("rising"), .behavior("old")) counter_2 (
    .count(comparator_2_lt), .Q(CNT_num), .clk(clock_1_out));  // open: load, D, carry, clr, preset
  nand nand_1 (nand_1_out, d_ff_2_q, comparator_2_eq);
  assign CLK = nand_1_out ? clock_1_out : 1'bz;  // Controlled_Buffer controlled_buffer_1
  Pull_Resistor #(.pull(1)) pull_resistor_1 (.node(CLK));

  // Other names for the same wires on the sheet: sel[1:0] = alu_res[1:0]

  // Notes on the sheet:
  //   中断源
  //   LED显示模块
  //   中断等待指示
  //   数码管输出应该用寄存器锁存，否则显示数据只能一闪而过
  //   数码管输出
  //   指令探针
  //   指令存储器
  //   指令字
  //   contents of rom_1 (hex, n*v repeats v):
  //   100493 100006f 100493 200913 300993 100006f 100493 200913 300993 100006f 100493 200913 300993
  //   100006f 100493 200913 300993 394000ef 100413 100493 1f49493 900533 2200893 73 24d493 48463 fedff06f
  //   900533 2200893 73 100493 249493 900533 2200893 73 48463 fedff06f 100493 1f49493 900533 2200893 73
  //   4034d493 900533 2200893 73 4044d493 900533 2200893 73 4044d493 900533 2200893 73 4044d493 900533
  //   2200893 73 4044d493 900533 2200893 73 4044d493 900533 2200893 73 4044d493 900533 2200893 73 4044d493
  //   900533 2200893 73 100413 1f41993 41f9d993 433 c00913 300b13 140413 f47413 800293 100313 499993
  //   89e9b3 1300533 2200893 73 406282b3 fe0294e3 140413 f00f93 1f47433 1c41413 800293 100313 49d993
  //   89e9b3 1300533 2200893 73 406282b3 fe0294e3 1c45413 406b0b33 b0463 f95ff06f 2b3 fff2c293 829293
  //   ff2e293 500533 2200893 73 fff00413 493 84a023 140413 448493 84a023 140413 448493 84a023 140413
  //   448493 84a023 140413 448493 84a023 140413 448493 84a023 140413 448493 84a023 140413 448493 84a023
  //   140413 448493 84a023 140413 448493 84a023 140413 448493 84a023 140413 448493 84a023 140413 448493
  //   84a023 140413 448493 84a023 140413 448493 84a023 140413 448493 84a023 140413 448493 140413 433
  //   3c00493 42983 4aa03 149a2b3 28663 134a023 1442023 ffc48493 fe9412e3 800533 2200893 73 440413 3c00493
  //   fc9416e3 a00893 73 100293 300313 800493 849493 7648493 900533 2200893 73 800e13 5494b3 6494b3 900533
  //   2200893 73 fffe0e13 fe0e14e3 100293 300313 800493 849493 7648493 1449493 900533 2200893 73 800e13
  //   4054d4b3 4064d4b3 900533 2200893 73 fffe0e13 fe0e14e3 313 2000e13 493 100913 930023 900533 2200893
  //   73 12484b3 130313 fffe0e13 fe0e12e3 800e13 313 32483 900533 2200893 73 430313 fffe0e13 fe0e14e3
  //   f00493 900533 2200893 73 fff48493 fe04d8e3 a00893 73 413 140413 800533 2200893 73 240413 800533
  //   2200893 73 340413 800533 2200893 73 440413 800533 2200893 73 540413 800533 2200893 73 640413 800533
  //   2200893 73 740413 800533 2200893 73 840413 800533 2200893 2200893 73 8067
  //   JAL
  //   JALR
  //   URET
  //   SB
  //   B.Inst. Imm
  //   J.Inst. Imm
  //   Beq
  //   Bge
  //   Bne
  //   MemToReg
  //   MemWrite
  //   AluOP
  //   AluSrcB
  //   RegWrite
  //   SB指令模块
  //   数据存储器
  //   为方便自动评测，需要输出PC，IR，寄存器堆写如数据RDin
  //   RAM写使能MemWrite、RAM写入数据MDin等信号
  //   控制位
  //   暂停节拍，不能为0
  //   戳工具置1进入计数暂停模式，ctrl+k时钟自动运行到对应节拍暂停
  //   ctrl+k关闭时钟连续运行，将控制位置零，进入单步调试模式调试
  //   用这个时钟源需要去掉电路中的其他时钟源
  //   可计数暂停的时钟源
endmodule

// 单周期硬布线控制器
module \单周期硬布线控制器  (
  input  [4:0] OP,
  input  [4:0] Funct,
  input  in_3,
  output [3:0] ALU_OP,
  output uret,
  output rs1,
  output rs2,
  output MemToReg,
  output ecall,
  output MemWrite,
  output ALU_SRC,
  output RegWrite,
  output S_type,
  output Beq,
  output Bne,
  output Jalr,
  output JAL,
  output BGE,
  output SB,
  output csrrsi,
  output csrrci
);

  wire \控制信号自动生成_1_ecall ;

  \运算控制器自动生成  \u_运算控制器自动生成_1  (
    .OP2(OP[0]), .OP3(OP[1]), .OP4(OP[2]), .OP5(OP[3]), .OP6(OP[4]), .F12(Funct[0]), .F13(Funct[1]),
    .F14(Funct[2]), .F25(Funct[3]), .F30(Funct[4]), .S0(ALU_OP[0]), .S1(ALU_OP[1]), .S2(ALU_OP[2]),
    .S3(ALU_OP[3]));
  \控制信号自动生成  \u_控制信号自动生成_1  (
    .OP2(OP[0]), .OP3(OP[1]), .MemToReg(MemToReg), .OP4(OP[2]), .OP5(OP[3]), .OP6(OP[4]), .F12(Funct[0]),
    .F13(Funct[1]), .MemWrite(MemWrite), .F14(Funct[2]), .F25(Funct[3]), .F30(Funct[4]), .ALU_SRC(ALU_SRC),
    .RegWrite(RegWrite), .ecall(\控制信号自动生成_1_ecall ), .S_Type(S_type), .BEQ(Beq), .BNE(Bne), .JALR(Jalr),
    .JAL(JAL), .BGE(BGE), .SB(SB), .rs1(rs1), .rs2(rs2), .csrrsi(csrrsi), .csrrci(csrrci));
  and and_1 (uret, in_3, \控制信号自动生成_1_ecall );
  and and_2 (ecall, ~in_3, \控制信号自动生成_1_ecall );  // AND_Gate

  // Other names for the same wires on the sheet: IR21 = in_3; OP_CODE[4:0] = OP

  // Notes on the sheet:
  //   运算器控制器，根据指令生成运算器功能选择信号
  //   控制信号生成，产生数据通路需要的其他控制信号
endmodule

// 运算器控制器
module \运算控制器自动生成  (
  input  OP2,
  input  OP3,
  input  OP4,
  input  OP5,
  input  OP6,
  input  F12,
  input  F13,
  input  F14,
  input  F25,
  input  F30,
  output S0,
  output S1,
  output S2,
  output S3
);

  wire and_1_out, and_2_out, and_3_out, and_4_out, and_5_out, and_6_out, and_7_out, and_8_out, and_9_out,
       and_10_out, and_11_out, and_12_out, and_13_out, and_14_out, and_15_out, and_16_out, and_17_out,
       and_18_out, and_19_out, and_20_out, and_21_out, and_22_out, and_23_out, and_24_out, and_25_out,
       and_26_out, and_27_out, and_28_out, and_29_out, and_30_out, and_31_out, and_32_out, and_33_out,
       and_34_out, and_35_out, and_36_out, not_1_out, not_2_out, not_3_out, not_4_out, not_5_out, not_6_out,
       not_7_out, not_8_out, not_9_out, not_10_out, not_11_out, not_12_out, not_13_out, not_14_out,
       not_15_out, not_16_out, not_17_out, not_18_out, not_19_out, not_20_out, not_21_out, not_22_out,
       not_23_out, not_24_out, not_25_out, not_26_out, not_27_out, not_28_out, not_29_out, not_30_out,
       not_31_out, not_32_out, not_33_out, not_34_out, not_35_out, not_36_out, not_37_out, not_38_out,
       not_39_out, not_40_out, not_41_out, not_42_out, not_43_out, not_44_out, not_45_out, not_46_out,
       not_47_out, not_48_out, not_49_out, not_50_out, not_51_out, not_52_out, not_53_out, not_54_out,
       not_55_out, not_56_out, not_57_out, not_58_out, not_59_out, not_60_out, not_61_out, not_62_out,
       not_63_out, not_64_out, not_65_out, not_66_out, not_67_out, not_68_out, not_69_out, not_70_out,
       not_71_out, not_72_out, not_73_out, not_74_out, not_75_out, not_76_out, not_77_out, not_78_out,
       not_79_out, not_80_out, not_81_out, not_82_out, not_83_out, not_84_out, not_85_out, not_86_out,
       not_87_out, not_88_out, not_89_out, not_90_out, not_91_out, not_92_out, not_93_out, not_94_out,
       not_95_out, not_96_out, not_97_out, not_98_out, not_99_out, not_100_out, not_101_out, not_102_out,
       not_103_out, not_104_out, not_105_out, not_106_out, not_107_out, not_108_out, not_109_out,
       not_110_out, not_111_out, not_112_out, not_113_out, not_114_out, not_115_out, not_116_out,
       not_117_out, not_118_out, not_119_out, not_120_out, not_121_out, not_122_out, not_123_out,
       not_124_out, not_125_out, not_126_out, not_127_out, not_128_out, not_129_out, not_130_out,
       not_131_out, not_132_out, not_133_out, not_134_out, not_135_out, not_136_out, not_137_out,
       not_138_out, not_139_out, not_140_out, not_141_out, not_142_out, not_143_out, not_144_out,
       not_145_out, not_146_out, not_147_out, not_148_out, not_149_out, not_150_out, not_151_out,
       not_152_out, not_153_out, not_154_out, not_155_out, not_156_out, not_157_out, not_158_out,
       not_159_out, not_160_out, not_161_out, not_162_out, not_163_out, not_164_out, not_165_out,
       not_166_out, not_167_out, not_168_out, not_169_out, not_170_out, not_171_out, not_172_out,
       not_173_out, not_174_out, not_175_out, not_176_out, not_177_out, not_178_out, not_179_out,
       not_180_out, not_181_out, not_182_out, not_183_out, not_184_out, not_185_out, not_186_out,
       not_187_out, not_188_out, not_189_out, not_190_out, not_191_out, not_192_out, not_193_out,
       not_194_out, not_195_out, not_196_out, not_197_out, not_198_out, not_199_out, not_200_out,
       not_201_out, not_202_out, not_203_out, not_204_out, not_205_out, not_206_out, not_207_out,
       not_208_out, not_209_out, not_210_out, not_211_out, not_212_out, not_213_out, not_214_out, not_215_out;

  not not_1 (not_1_out, F30);
  not not_2 (not_2_out, F25);
  not not_3 (not_3_out, F14);
  not not_4 (not_4_out, F13);
  not not_5 (not_5_out, F12);
  not not_6 (not_6_out, OP6);
  not not_7 (not_7_out, OP3);
  not not_8 (not_8_out, OP2);
  not not_9 (not_9_out, F30);
  not not_10 (not_10_out, F25);
  not not_11 (not_11_out, OP6);
  not not_12 (not_12_out, OP3);
  not not_13 (not_13_out, OP2);
  not not_14 (not_14_out, F30);
  not not_15 (not_15_out, F25);
  not not_16 (not_16_out, F14);
  not not_17 (not_17_out, F12);
  not not_18 (not_18_out, OP6);
  not not_19 (not_19_out, OP3);
  not not_20 (not_20_out, OP2);
  not not_21 (not_21_out, F14);
  not not_22 (not_22_out, F13);
  not not_23 (not_23_out, F12);
  not not_24 (not_24_out, OP6);
  not not_25 (not_25_out, OP5);
  not not_26 (not_26_out, OP3);
  not not_27 (not_27_out, OP2);
  not not_28 (not_28_out, OP6);
  not not_29 (not_29_out, OP5);
  not not_30 (not_30_out, OP3);
  not not_31 (not_31_out, OP2);
  not not_32 (not_32_out, F13);
  not not_33 (not_33_out, F12);
  not not_34 (not_34_out, OP6);
  not not_35 (not_35_out, OP5);
  not not_36 (not_36_out, OP3);
  not not_37 (not_37_out, OP2);
  not not_38 (not_38_out, F14);
  not not_39 (not_39_out, F12);
  not not_40 (not_40_out, OP6);
  not not_41 (not_41_out, OP5);
  not not_42 (not_42_out, OP3);
  not not_43 (not_43_out, OP2);
  not not_44 (not_44_out, F25);
  not not_45 (not_45_out, F13);
  not not_46 (not_46_out, OP6);
  not not_47 (not_47_out, OP5);
  not not_48 (not_48_out, OP3);
  not not_49 (not_49_out, OP2);
  not not_50 (not_50_out, F14);
  not not_51 (not_51_out, F12);
  not not_52 (not_52_out, OP6);
  not not_53 (not_53_out, OP5);
  not not_54 (not_54_out, OP4);
  not not_55 (not_55_out, OP3);
  not not_56 (not_56_out, OP2);
  not not_57 (not_57_out, F14);
  not not_58 (not_58_out, F12);
  not not_59 (not_59_out, OP6);
  not not_60 (not_60_out, OP4);
  not not_61 (not_61_out, OP3);
  not not_62 (not_62_out, OP2);
  not not_63 (not_63_out, F25);
  not not_64 (not_64_out, F13);
  not not_65 (not_65_out, OP6);
  not not_66 (not_66_out, OP3);
  not not_67 (not_67_out, OP2);
  not not_68 (not_68_out, F14);
  not not_69 (not_69_out, F13);
  not not_70 (not_70_out, F12);
  not not_71 (not_71_out, OP6);
  not not_72 (not_72_out, OP4);
  not not_73 (not_73_out, OP3);
  not not_74 (not_74_out, OP2);
  not not_75 (not_75_out, F13);
  not not_76 (not_76_out, OP4);
  not not_77 (not_77_out, OP3);
  not not_78 (not_78_out, OP2);
  not not_79 (not_79_out, F25);
  not not_80 (not_80_out, F14);
  not not_81 (not_81_out, F13);
  not not_82 (not_82_out, F12);
  not not_83 (not_83_out, OP6);
  not not_84 (not_84_out, OP3);
  not not_85 (not_85_out, OP2);
  not not_86 (not_86_out, F30);
  not not_87 (not_87_out, F25);
  not not_88 (not_88_out, OP6);
  not not_89 (not_89_out, OP3);
  not not_90 (not_90_out, OP2);
  not not_91 (not_91_out, F30);
  not not_92 (not_92_out, F25);
  not not_93 (not_93_out, F14);
  not not_94 (not_94_out, F12);
  not not_95 (not_95_out, OP6);
  not not_96 (not_96_out, OP3);
  not not_97 (not_97_out, OP2);
  not not_98 (not_98_out, OP6);
  not not_99 (not_99_out, OP5);
  not not_100 (not_100_out, OP3);
  not not_101 (not_101_out, OP2);
  not not_102 (not_102_out, F14);
  not not_103 (not_103_out, F12);
  not not_104 (not_104_out, OP6);
  not not_105 (not_105_out, OP5);
  not not_106 (not_106_out, OP3);
  not not_107 (not_107_out, OP2);
  not not_108 (not_108_out, F30);
  not not_109 (not_109_out, F25);
  not not_110 (not_110_out, F13);
  not not_111 (not_111_out, OP6);
  not not_112 (not_112_out, OP5);
  not not_113 (not_113_out, OP3);
  not not_114 (not_114_out, OP2);
  not not_115 (not_115_out, F13);
  not not_116 (not_116_out, OP4);
  not not_117 (not_117_out, OP3);
  not not_118 (not_118_out, OP2);
  not not_119 (not_119_out, F30);
  not not_120 (not_120_out, F25);
  not not_121 (not_121_out, F14);
  not not_122 (not_122_out, F13);
  not not_123 (not_123_out, F12);
  not not_124 (not_124_out, OP6);
  not not_125 (not_125_out, OP3);
  not not_126 (not_126_out, OP2);
  not not_127 (not_127_out, F25);
  not not_128 (not_128_out, F14);
  not not_129 (not_129_out, F13);
  not not_130 (not_130_out, F12);
  not not_131 (not_131_out, OP6);
  not not_132 (not_132_out, OP3);
  not not_133 (not_133_out, OP2);
  not not_134 (not_134_out, F30);
  not not_135 (not_135_out, F25);
  not not_136 (not_136_out, OP6);
  not not_137 (not_137_out, OP3);
  not not_138 (not_138_out, OP2);
  not not_139 (not_139_out, F30);
  not not_140 (not_140_out, F25);
  not not_141 (not_141_out, F14);
  not not_142 (not_142_out, OP6);
  not not_143 (not_143_out, OP3);
  not not_144 (not_144_out, OP2);
  not not_145 (not_145_out, F14);
  not not_146 (not_146_out, F13);
  not not_147 (not_147_out, F12);
  not not_148 (not_148_out, OP6);
  not not_149 (not_149_out, OP5);
  not not_150 (not_150_out, OP3);
  not not_151 (not_151_out, OP2);
  not not_152 (not_152_out, OP6);
  not not_153 (not_153_out, OP5);
  not not_154 (not_154_out, OP3);
  not not_155 (not_155_out, OP2);
  not not_156 (not_156_out, F14);
  not not_157 (not_157_out, F12);
  not not_158 (not_158_out, OP6);
  not not_159 (not_159_out, OP5);
  not not_160 (not_160_out, OP4);
  not not_161 (not_161_out, OP3);
  not not_162 (not_162_out, OP2);
  not not_163 (not_163_out, F14);
  not not_164 (not_164_out, F12);
  not not_165 (not_165_out, OP6);
  not not_166 (not_166_out, OP4);
  not not_167 (not_167_out, OP3);
  not not_168 (not_168_out, OP2);
  not not_169 (not_169_out, F14);
  not not_170 (not_170_out, F13);
  not not_171 (not_171_out, F12);
  not not_172 (not_172_out, OP6);
  not not_173 (not_173_out, OP4);
  not not_174 (not_174_out, OP3);
  not not_175 (not_175_out, OP2);
  not not_176 (not_176_out, F30);
  not not_177 (not_177_out, F25);
  not not_178 (not_178_out, F12);
  not not_179 (not_179_out, OP6);
  not not_180 (not_180_out, OP3);
  not not_181 (not_181_out, OP2);
  not not_182 (not_182_out, F30);
  not not_183 (not_183_out, F25);
  not not_184 (not_184_out, F14);
  not not_185 (not_185_out, F12);
  not not_186 (not_186_out, OP6);
  not not_187 (not_187_out, OP3);
  not not_188 (not_188_out, OP2);
  not not_189 (not_189_out, F30);
  not not_190 (not_190_out, F25);
  not not_191 (not_191_out, F14);
  not not_192 (not_192_out, OP6);
  not not_193 (not_193_out, OP3);
  not not_194 (not_194_out, OP2);
  not not_195 (not_195_out, F12);
  not not_196 (not_196_out, OP6);
  not not_197 (not_197_out, OP5);
  not not_198 (not_198_out, OP3);
  not not_199 (not_199_out, OP2);
  not not_200 (not_200_out, F13);
  not not_201 (not_201_out, F12);
  not not_202 (not_202_out, OP6);
  not not_203 (not_203_out, OP5);
  not not_204 (not_204_out, OP3);
  not not_205 (not_205_out, OP2);
  not not_206 (not_206_out, F14);
  not not_207 (not_207_out, F12);
  not not_208 (not_208_out, OP6);
  not not_209 (not_209_out, OP5);
  not not_210 (not_210_out, OP3);
  not not_211 (not_211_out, OP2);
  not not_212 (not_212_out, F13);
  not not_213 (not_213_out, OP4);
  not not_214 (not_214_out, OP3);
  not not_215 (not_215_out, OP2);
  and and_1 (and_1_out, not_1_out, not_2_out, not_3_out, not_4_out, not_5_out, not_6_out, OP5, OP4, not_7_out, not_8_out);
  and and_2 (and_2_out, not_9_out, not_10_out, F14, F13, F12, not_11_out, OP5, OP4, not_12_out, not_13_out);
  and and_3 (and_3_out, not_14_out, not_15_out, not_16_out, F13, not_17_out, not_18_out, OP5, OP4, not_19_out, not_20_out);
  and and_4 (and_4_out, not_21_out, not_22_out, not_23_out, not_24_out, not_25_out, OP4, not_26_out, not_27_out);
  and and_5 (and_5_out, F14, F13, F12, not_28_out, not_29_out, OP4, not_30_out, not_31_out);
  and and_6 (and_6_out, F14, not_32_out, not_33_out, not_34_out, not_35_out, OP4, not_36_out, not_37_out);
  and and_7 (and_7_out, not_38_out, F13, not_39_out, not_40_out, not_41_out, OP4, not_42_out, not_43_out);
  and and_8 (and_8_out, F30, not_44_out, F14, not_45_out, F12, not_46_out, not_47_out, OP4, not_48_out, not_49_out);
  and and_9 (and_9_out, not_50_out, F13, not_51_out, not_52_out, not_53_out, not_54_out, not_55_out, not_56_out);
  and and_10 (and_10_out, not_57_out, F13, not_58_out, not_59_out, OP5, not_60_out, not_61_out, not_62_out);
  and and_11 (and_11_out, F30, not_63_out, F14, not_64_out, F12, not_65_out, OP5, OP4, not_66_out, not_67_out);
  and and_12 (and_12_out, not_68_out, not_69_out, not_70_out, not_71_out, OP5, not_72_out, not_73_out, not_74_out);
  and and_13 (and_13_out, F14, not_75_out, F12, OP6, OP5, not_76_out, not_77_out, not_78_out);
  and and_14 (and_14_out, F30, not_79_out, not_80_out, not_81_out, not_82_out, not_83_out, OP5, OP4, not_84_out, not_85_out);
  and and_15 (and_15_out, not_86_out, not_87_out, F14, F13, F12, not_88_out, OP5, OP4, not_89_out, not_90_out);
  and and_16 (and_16_out, not_91_out, not_92_out, not_93_out, F13, not_94_out, not_95_out, OP5, OP4, not_96_out, not_97_out);
  and and_17 (and_17_out, F14, F13, F12, not_98_out, not_99_out, OP4, not_100_out, not_101_out);
  and and_18 (and_18_out, not_102_out, F13, not_103_out, not_104_out, not_105_out, OP4, not_106_out, not_107_out);
  and and_19 (and_19_out, not_108_out, not_109_out, F14, not_110_out, F12, not_111_out, not_112_out, OP4, not_113_out, not_114_out);
  and and_20 (and_20_out, F14, not_115_out, F12, OP6, OP5, not_116_out, not_117_out, not_118_out);
  and and_21 (and_21_out, not_119_out, not_120_out, not_121_out, not_122_out, not_123_out, not_124_out, OP5, OP4, not_125_out, not_126_out);
  and and_22 (and_22_out, F30, not_127_out, not_128_out, not_129_out, not_130_out, not_131_out, OP5, OP4, not_132_out, not_133_out);
  and and_23 (and_23_out, not_134_out, not_135_out, F14, F13, F12, not_136_out, OP5, OP4, not_137_out, not_138_out);
  and and_24 (and_24_out, not_139_out, not_140_out, not_141_out, F13, F12, not_142_out, OP5, OP4, not_143_out, not_144_out);
  and and_25 (and_25_out, not_145_out, not_146_out, not_147_out, not_148_out, not_149_out, OP4, not_150_out, not_151_out);
  and and_26 (and_26_out, F14, F13, F12, not_152_out, not_153_out, OP4, not_154_out, not_155_out);
  and and_27 (and_27_out, not_156_out, F13, not_157_out, not_158_out, not_159_out, not_160_out, not_161_out, not_162_out);
  and and_28 (and_28_out, not_163_out, F13, not_164_out, not_165_out, OP5, not_166_out, not_167_out, not_168_out);
  and and_29 (and_29_out, not_169_out, not_170_out, not_171_out, not_172_out, OP5, not_173_out, not_174_out, not_175_out);
  and and_30 (and_30_out, not_176_out, not_177_out, F14, F13, not_178_out, not_179_out, OP5, OP4, not_180_out, not_181_out);
  and and_31 (and_31_out, not_182_out, not_183_out, not_184_out, F13, not_185_out, not_186_out, OP5, OP4, not_187_out, not_188_out);
  and and_32 (and_32_out, not_189_out, not_190_out, not_191_out, F13, F12, not_192_out, OP5, OP4, not_193_out, not_194_out);
  and and_33 (and_33_out, F14, F13, not_195_out, not_196_out, not_197_out, OP4, not_198_out, not_199_out);
  and and_34 (and_34_out, F14, not_200_out, not_201_out, not_202_out, not_203_out, OP4, not_204_out, not_205_out);
  and and_35 (and_35_out, not_206_out, F13, not_207_out, not_208_out, not_209_out, OP4, not_210_out, not_211_out);
  and and_36 (and_36_out, F14, not_212_out, F12, OP6, OP5, not_213_out, not_214_out, not_215_out);
  or or_1 (S0, and_1_out, and_2_out, and_3_out, and_4_out, and_5_out, and_6_out, and_7_out, and_8_out, and_9_out, and_10_out, and_11_out, and_12_out, and_13_out);
  or or_2 (S1, and_14_out, and_15_out, and_16_out, and_17_out, and_18_out, and_19_out, and_20_out);
  or or_3 (S2, and_21_out, and_22_out, and_23_out, and_24_out, and_25_out, and_26_out, and_27_out, and_28_out, and_29_out);
  or or_4 (S3, and_30_out, and_31_out, and_32_out, and_33_out, and_34_out, and_35_out, and_36_out);
endmodule

// 控制信号生成
module \控制信号自动生成  (
  input  OP2,
  input  OP3,
  input  OP4,
  input  OP5,
  input  OP6,
  input  F12,
  input  F13,
  input  F14,
  input  F25,
  input  F30,
  output MemToReg,
  output MemWrite,
  output ALU_SRC,
  output RegWrite,
  output ecall,
  output S_Type,
  output BEQ,
  output BNE,
  output JALR,
  output JAL,
  output BGE,
  output SB,
  output rs1,
  output rs2,
  output csrrsi,
  output csrrci
);

  wire and_3_out, and_4_out, and_5_out, and_6_out, and_7_out, and_8_out, and_9_out, and_10_out, and_11_out,
       and_12_out, and_13_out, and_14_out, and_15_out, and_16_out, and_17_out, and_18_out, and_19_out,
       and_28_out, and_29_out, and_30_out, and_31_out, and_32_out, and_33_out, and_34_out, and_35_out,
       and_36_out, and_37_out, and_38_out, and_39_out, and_40_out, and_41_out, and_42_out, and_43_out,
       and_44_out, and_45_out, not_1_out, not_2_out, not_3_out, not_4_out, not_5_out, not_6_out, not_7_out,
       not_8_out, not_9_out, not_10_out, not_11_out, not_12_out, not_13_out, not_14_out, not_15_out,
       not_16_out, not_17_out, not_18_out, not_19_out, not_20_out, not_21_out, not_22_out, not_23_out,
       not_24_out, not_25_out, not_26_out, not_27_out, not_28_out, not_29_out, not_30_out, not_31_out,
       not_32_out, not_33_out, not_34_out, not_35_out, not_36_out, not_37_out, not_38_out, not_39_out,
       not_40_out, not_41_out, not_42_out, not_43_out, not_44_out, not_45_out, not_46_out, not_47_out,
       not_48_out, not_49_out, not_50_out, not_51_out, not_52_out, not_53_out, not_54_out, not_55_out,
       not_56_out, not_57_out, not_58_out, not_59_out, not_60_out, not_61_out, not_62_out, not_63_out,
       not_64_out, not_65_out, not_66_out, not_67_out, not_68_out, not_69_out, not_70_out, not_71_out,
       not_72_out, not_73_out, not_74_out, not_75_out, not_76_out, not_77_out, not_78_out, not_79_out,
       not_80_out, not_81_out, not_82_out, not_83_out, not_84_out, not_85_out, not_86_out, not_87_out,
       not_88_out, not_89_out, not_90_out, not_91_out, not_92_out, not_93_out, not_94_out, not_95_out,
       not_96_out, not_97_out, not_98_out, not_99_out, not_100_out, not_101_out, not_102_out, not_103_out,
       not_104_out, not_105_out, not_106_out, not_107_out, not_108_out, not_109_out, not_110_out,
       not_111_out, not_112_out, not_113_out, not_114_out, not_115_out, not_116_out, not_117_out,
       not_118_out, not_119_out, not_120_out, not_121_out, not_122_out, not_123_out, not_124_out,
       not_125_out, not_126_out, not_127_out, not_128_out, not_129_out, not_130_out, not_131_out,
       not_132_out, not_133_out, not_134_out, not_135_out, not_136_out, not_137_out, not_138_out,
       not_139_out, not_140_out, not_141_out, not_142_out, not_143_out, not_144_out, not_145_out,
       not_146_out, not_147_out, not_148_out, not_149_out, not_150_out, not_151_out, not_152_out,
       not_153_out, not_154_out, not_155_out, not_156_out, not_157_out, not_158_out, not_159_out,
       not_160_out, not_161_out, not_162_out, not_163_out, not_164_out, not_165_out, not_166_out,
       not_167_out, not_168_out, not_169_out, not_170_out, not_171_out, not_172_out, not_173_out,
       not_174_out, not_175_out, not_176_out, not_177_out, not_178_out, not_179_out, not_180_out,
       not_181_out, not_182_out, not_183_out, not_184_out, not_185_out, not_186_out, not_187_out,
       not_188_out, not_189_out, not_190_out, not_191_out, not_192_out, not_193_out, not_194_out,
       not_195_out, not_196_out, not_197_out, not_198_out, not_199_out, not_200_out, not_201_out,
       not_202_out, not_203_out, not_204_out, not_205_out, not_206_out, not_207_out, not_208_out,
       not_209_out, not_210_out, not_211_out, not_212_out, not_213_out, not_214_out, not_215_out,
       not_216_out, not_217_out, not_218_out, not_219_out, not_220_out, not_221_out, not_222_out,
       not_223_out, not_224_out, not_225_out, not_226_out, not_227_out, not_228_out, not_229_out,
       not_230_out, not_231_out, not_232_out, not_233_out, not_234_out, not_235_out, not_236_out,
       not_237_out, not_238_out, not_239_out, not_240_out, not_241_out, not_242_out, not_243_out,
       not_244_out, not_245_out, not_246_out, not_247_out, not_248_out;

  not not_1 (not_1_out, OP2);
  not not_2 (not_2_out, OP3);
  not not_3 (not_3_out, OP4);
  not not_4 (not_4_out, OP5);
  not not_5 (not_5_out, OP6);
  not not_6 (not_6_out, F12);
  not not_7 (not_7_out, F14);
  not not_8 (not_8_out, OP2);
  not not_9 (not_9_out, OP3);
  not not_10 (not_10_out, OP4);
  not not_11 (not_11_out, OP6);
  not not_12 (not_12_out, F12);
  not not_13 (not_13_out, F14);
  not not_14 (not_14_out, OP2);
  not not_15 (not_15_out, OP3);
  not not_16 (not_16_out, OP5);
  not not_17 (not_17_out, OP6);
  not not_18 (not_18_out, F12);
  not not_19 (not_19_out, F14);
  not not_20 (not_20_out, OP2);
  not not_21 (not_21_out, OP3);
  not not_22 (not_22_out, OP4);
  not not_23 (not_23_out, OP6);
  not not_24 (not_24_out, F12);
  not not_25 (not_25_out, F14);
  not not_26 (not_26_out, OP2);
  not not_27 (not_27_out, OP3);
  not not_28 (not_28_out, OP5);
  not not_29 (not_29_out, OP6);
  not not_30 (not_30_out, F12);
  not not_31 (not_31_out, OP2);
  not not_32 (not_32_out, OP3);
  not not_33 (not_33_out, OP5);
  not not_34 (not_34_out, OP6);
  not not_35 (not_35_out, F13);
  not not_36 (not_36_out, F25);
  not not_37 (not_37_out, F30);
  not not_38 (not_38_out, OP2);
  not not_39 (not_39_out, OP3);
  not not_40 (not_40_out, OP5);
  not not_41 (not_41_out, OP6);
  not not_42 (not_42_out, F25);
  not not_43 (not_43_out, OP2);
  not not_44 (not_44_out, OP3);
  not not_45 (not_45_out, OP5);
  not not_46 (not_46_out, OP6);
  not not_47 (not_47_out, OP2);
  not not_48 (not_48_out, OP3);
  not not_49 (not_49_out, OP5);
  not not_50 (not_50_out, OP6);
  not not_51 (not_51_out, F12);
  not not_52 (not_52_out, F14);
  not not_53 (not_53_out, OP2);
  not not_54 (not_54_out, OP3);
  not not_55 (not_55_out, OP4);
  not not_56 (not_56_out, OP6);
  not not_57 (not_57_out, F12);
  not not_58 (not_58_out, F13);
  not not_59 (not_59_out, F14);
  not not_60 (not_60_out, OP2);
  not not_61 (not_61_out, OP3);
  not not_62 (not_62_out, OP5);
  not not_63 (not_63_out, OP6);
  not not_64 (not_64_out, F12);
  not not_65 (not_65_out, OP2);
  not not_66 (not_66_out, OP3);
  not not_67 (not_67_out, OP5);
  not not_68 (not_68_out, OP6);
  not not_69 (not_69_out, F13);
  not not_70 (not_70_out, F25);
  not not_71 (not_71_out, F30);
  not not_72 (not_72_out, OP2);
  not not_73 (not_73_out, OP3);
  not not_74 (not_74_out, OP6);
  not not_75 (not_75_out, F12);
  not not_76 (not_76_out, F13);
  not not_77 (not_77_out, F14);
  not not_78 (not_78_out, F25);
  not not_79 (not_79_out, OP2);
  not not_80 (not_80_out, OP3);
  not not_81 (not_81_out, OP5);
  not not_82 (not_82_out, OP6);
  not not_83 (not_83_out, OP2);
  not not_84 (not_84_out, OP3);
  not not_85 (not_85_out, OP6);
  not not_86 (not_86_out, F13);
  not not_87 (not_87_out, F25);
  not not_88 (not_88_out, OP2);
  not not_89 (not_89_out, OP3);
  not not_90 (not_90_out, OP6);
  not not_91 (not_91_out, F14);
  not not_92 (not_92_out, F25);
  not not_93 (not_93_out, F30);
  not not_94 (not_94_out, OP2);
  not not_95 (not_95_out, OP3);
  not not_96 (not_96_out, OP6);
  not not_97 (not_97_out, F25);
  not not_98 (not_98_out, F30);
  not not_99 (not_99_out, OP4);
  not not_100 (not_100_out, F12);
  not not_101 (not_101_out, F13);
  not not_102 (not_102_out, F14);
  not not_103 (not_103_out, OP4);
  not not_104 (not_104_out, OP2);
  not not_105 (not_105_out, OP3);
  not not_106 (not_106_out, F12);
  not not_107 (not_107_out, F13);
  not not_108 (not_108_out, F14);
  not not_109 (not_109_out, F25);
  not not_110 (not_110_out, F30);
  not not_111 (not_111_out, OP2);
  not not_112 (not_112_out, OP3);
  not not_113 (not_113_out, OP4);
  not not_114 (not_114_out, OP6);
  not not_115 (not_115_out, F12);
  not not_116 (not_116_out, F14);
  not not_117 (not_117_out, OP2);
  not not_118 (not_118_out, OP3);
  not not_119 (not_119_out, OP4);
  not not_120 (not_120_out, F12);
  not not_121 (not_121_out, F13);
  not not_122 (not_122_out, F14);
  not not_123 (not_123_out, OP2);
  not not_124 (not_124_out, OP3);
  not not_125 (not_125_out, OP4);
  not not_126 (not_126_out, F13);
  not not_127 (not_127_out, F14);
  not not_128 (not_128_out, OP3);
  not not_129 (not_129_out, OP4);
  not not_130 (not_130_out, F12);
  not not_131 (not_131_out, F13);
  not not_132 (not_132_out, F14);
  not not_133 (not_133_out, OP4);
  not not_134 (not_134_out, OP2);
  not not_135 (not_135_out, OP3);
  not not_136 (not_136_out, OP4);
  not not_137 (not_137_out, F13);
  not not_138 (not_138_out, OP2);
  not not_139 (not_139_out, OP3);
  not not_140 (not_140_out, OP4);
  not not_141 (not_141_out, OP6);
  not not_142 (not_142_out, F12);
  not not_143 (not_143_out, F13);
  not not_144 (not_144_out, F14);
  not not_145 (not_145_out, OP2);
  not not_146 (not_146_out, OP3);
  not not_147 (not_147_out, OP5);
  not not_148 (not_148_out, OP6);
  not not_149 (not_149_out, F12);
  not not_150 (not_150_out, F14);
  not not_151 (not_151_out, OP2);
  not not_152 (not_152_out, OP3);
  not not_153 (not_153_out, OP4);
  not not_154 (not_154_out, OP6);
  not not_155 (not_155_out, F12);
  not not_156 (not_156_out, F14);
  not not_157 (not_157_out, OP3);
  not not_158 (not_158_out, OP4);
  not not_159 (not_159_out, F12);
  not not_160 (not_160_out, F13);
  not not_161 (not_161_out, F14);
  not not_162 (not_162_out, OP2);
  not not_163 (not_163_out, OP3);
  not not_164 (not_164_out, OP4);
  not not_165 (not_165_out, F13);
  not not_166 (not_166_out, OP2);
  not not_167 (not_167_out, OP3);
  not not_168 (not_168_out, OP5);
  not not_169 (not_169_out, OP6);
  not not_170 (not_170_out, F12);
  not not_171 (not_171_out, OP2);
  not not_172 (not_172_out, OP3);
  not not_173 (not_173_out, OP5);
  not not_174 (not_174_out, OP6);
  not not_175 (not_175_out, F13);
  not not_176 (not_176_out, F25);
  not not_177 (not_177_out, F30);
  not not_178 (not_178_out, OP2);
  not not_179 (not_179_out, OP3);
  not not_180 (not_180_out, OP6);
  not not_181 (not_181_out, F12);
  not not_182 (not_182_out, F13);
  not not_183 (not_183_out, F14);
  not not_184 (not_184_out, F25);
  not not_185 (not_185_out, OP2);
  not not_186 (not_186_out, OP3);
  not not_187 (not_187_out, OP5);
  not not_188 (not_188_out, OP6);
  not not_189 (not_189_out, OP2);
  not not_190 (not_190_out, OP3);
  not not_191 (not_191_out, OP6);
  not not_192 (not_192_out, F13);
  not not_193 (not_193_out, F25);
  not not_194 (not_194_out, OP2);
  not not_195 (not_195_out, OP3);
  not not_196 (not_196_out, OP6);
  not not_197 (not_197_out, F14);
  not not_198 (not_198_out, F25);
  not not_199 (not_199_out, F30);
  not not_200 (not_200_out, OP2);
  not not_201 (not_201_out, OP3);
  not not_202 (not_202_out, OP6);
  not not_203 (not_203_out, F25);
  not not_204 (not_204_out, F30);
  not not_205 (not_205_out, OP2);
  not not_206 (not_206_out, OP3);
  not not_207 (not_207_out, OP4);
  not not_208 (not_208_out, OP6);
  not not_209 (not_209_out, F12);
  not not_210 (not_210_out, F14);
  not not_211 (not_211_out, OP2);
  not not_212 (not_212_out, OP3);
  not not_213 (not_213_out, OP4);
  not not_214 (not_214_out, F12);
  not not_215 (not_215_out, F13);
  not not_216 (not_216_out, F14);
  not not_217 (not_217_out, OP2);
  not not_218 (not_218_out, OP3);
  not not_219 (not_219_out, OP6);
  not not_220 (not_220_out, F12);
  not not_221 (not_221_out, F13);
  not not_222 (not_222_out, F14);
  not not_223 (not_223_out, F25);
  not not_224 (not_224_out, OP2);
  not not_225 (not_225_out, OP3);
  not not_226 (not_226_out, OP4);
  not not_227 (not_227_out, F13);
  not not_228 (not_228_out, OP2);
  not not_229 (not_229_out, OP3);
  not not_230 (not_230_out, OP6);
  not not_231 (not_231_out, F14);
  not not_232 (not_232_out, F25);
  not not_233 (not_233_out, F30);
  not not_234 (not_234_out, OP2);
  not not_235 (not_235_out, OP3);
  not not_236 (not_236_out, OP6);
  not not_237 (not_237_out, F25);
  not not_238 (not_238_out, F30);
  not not_239 (not_239_out, OP2);
  not not_240 (not_240_out, OP3);
  not not_241 (not_241_out, OP6);
  not not_242 (not_242_out, F13);
  not not_243 (not_243_out, F25);
  not not_244 (not_244_out, F12);
  not not_245 (not_245_out, OP3);
  not not_246 (not_246_out, OP2);
  not not_247 (not_247_out, OP3);
  not not_248 (not_248_out, OP2);
  and and_1 (MemToReg, not_1_out, not_2_out, not_3_out, not_4_out, not_5_out, not_6_out, F13, not_7_out);
  and and_2 (MemWrite, not_8_out, not_9_out, not_10_out, OP5, not_11_out, not_12_out, F13, not_13_out);
  and and_3 (and_3_out, not_14_out, not_15_out, not_16_out, not_17_out, not_18_out, F13, not_19_out);
  and and_4 (and_4_out, not_20_out, not_21_out, not_22_out, OP5, not_23_out, not_24_out, not_25_out);
  and and_5 (and_5_out, not_26_out, not_27_out, OP4, not_28_out, not_29_out, not_30_out);
  and and_6 (and_6_out, not_31_out, not_32_out, OP4, not_33_out, not_34_out, not_35_out, not_36_out, not_37_out);
  and and_7 (and_7_out, not_38_out, not_39_out, OP4, not_40_out, not_41_out, F14, not_42_out);
  and and_8 (and_8_out, not_43_out, not_44_out, OP4, not_45_out, not_46_out, F13, F14);
  and and_9 (and_9_out, not_47_out, not_48_out, not_49_out, not_50_out, not_51_out, F13, not_52_out);
  and and_10 (and_10_out, not_53_out, not_54_out, not_55_out, OP5, not_56_out, not_57_out, not_58_out, not_59_out);
  and and_11 (and_11_out, not_60_out, not_61_out, OP4, not_62_out, not_63_out, not_64_out);
  and and_12 (and_12_out, not_65_out, not_66_out, OP4, not_67_out, not_68_out, not_69_out, not_70_out, not_71_out);
  and and_13 (and_13_out, not_72_out, not_73_out, OP4, not_74_out, not_75_out, not_76_out, not_77_out, not_78_out);
  and and_14 (and_14_out, not_79_out, not_80_out, OP4, not_81_out, not_82_out, F13, F14);
  and and_15 (and_15_out, not_83_out, not_84_out, OP4, not_85_out, F12, not_86_out, F14, not_87_out, F30);
  and and_16 (and_16_out, not_88_out, not_89_out, OP4, OP5, not_90_out, not_91_out, not_92_out, not_93_out);
  and and_17 (and_17_out, not_94_out, not_95_out, OP4, OP5, not_96_out, F13, not_97_out, not_98_out);
  and and_18 (and_18_out, OP2, not_99_out, OP5, OP6, not_100_out, not_101_out, not_102_out);
  and and_19 (and_19_out, OP2, OP3, not_103_out, OP5, OP6);
  and and_20 (ecall, not_104_out, not_105_out, OP4, OP5, OP6, not_106_out, not_107_out, not_108_out, not_109_out, not_110_out);
  and and_21 (S_Type, not_111_out, not_112_out, not_113_out, OP5, not_114_out, not_115_out, not_116_out);
  and and_22 (BEQ, not_117_out, not_118_out, not_119_out, OP5, OP6, not_120_out, not_121_out, not_122_out);
  and and_23 (BNE, not_123_out, not_124_out, not_125_out, OP5, OP6, F12, not_126_out, not_127_out);
  and and_24 (JALR, OP2, not_128_out, not_129_out, OP5, OP6, not_130_out, not_131_out, not_132_out);
  and and_25 (JAL, OP2, OP3, not_133_out, OP5, OP6);
  and and_26 (BGE, not_134_out, not_135_out, not_136_out, OP5, OP6, F12, not_137_out, F14);
  and and_27 (SB, not_138_out, not_139_out, not_140_out, OP5, not_141_out, not_142_out, not_143_out, not_144_out);
  and and_28 (and_28_out, not_145_out, not_146_out, not_147_out, not_148_out, not_149_out, F13, not_150_out);
  and and_29 (and_29_out, not_151_out, not_152_out, not_153_out, OP5, not_154_out, not_155_out, not_156_out);
  and and_30 (and_30_out, not_157_out, not_158_out, OP5, OP6, not_159_out, not_160_out, not_161_out);
  and and_31 (and_31_out, not_162_out, not_163_out, not_164_out, OP5, OP6, F12, not_165_out);
  and and_32 (and_32_out, not_166_out, not_167_out, OP4, not_168_out, not_169_out, not_170_out);
  and and_33 (and_33_out, not_171_out, not_172_out, OP4, not_173_out, not_174_out, not_175_out, not_176_out, not_177_out);
  and and_34 (and_34_out, not_178_out, not_179_out, OP4, not_180_out, not_181_out, not_182_out, not_183_out, not_184_out);
  and and_35 (and_35_out, not_185_out, not_186_out, OP4, not_187_out, not_188_out, F13, F14);
  and and_36 (and_36_out, not_189_out, not_190_out, OP4, not_191_out, F12, not_192_out, F14, not_193_out, F30);
  and and_37 (and_37_out, not_194_out, not_195_out, OP4, OP5, not_196_out, not_197_out, not_198_out, not_199_out);
  and and_38 (and_38_out, not_200_out, not_201_out, OP4, OP5, not_202_out, F13, not_203_out, not_204_out);
  and and_39 (and_39_out, not_205_out, not_206_out, not_207_out, OP5, not_208_out, not_209_out, not_210_out);
  and and_40 (and_40_out, not_211_out, not_212_out, not_213_out, OP5, not_214_out, not_215_out, not_216_out);
  and and_41 (and_41_out, not_217_out, not_218_out, OP5, not_219_out, not_220_out, not_221_out, not_222_out, not_223_out);
  and and_42 (and_42_out, not_224_out, not_225_out, not_226_out, OP5, OP6, F12, not_227_out);
  and and_43 (and_43_out, not_228_out, not_229_out, OP4, OP5, not_230_out, not_231_out, not_232_out, not_233_out);
  and and_44 (and_44_out, not_234_out, not_235_out, OP4, OP5, not_236_out, F13, not_237_out, not_238_out);
  and and_45 (and_45_out, not_239_out, not_240_out, OP4, OP5, not_241_out, F12, not_242_out, F14, not_243_out, F30);
  and and_46 (csrrsi, F14, F13, not_244_out, OP6, OP5, OP4, not_245_out, not_246_out);
  and and_47 (csrrci, F14, F13, F12, OP6, OP5, OP4, not_247_out, not_248_out);
  or or_1 (ALU_SRC, and_3_out, and_4_out, and_5_out, and_6_out, and_7_out, and_8_out);
  or or_2 (RegWrite, and_9_out, and_10_out, and_11_out, and_12_out, and_13_out, and_14_out, and_15_out, and_16_out, and_17_out, and_18_out, and_19_out);
  or or_3 (rs1, and_28_out, and_29_out, and_30_out, and_31_out, and_32_out, and_33_out, and_34_out, and_35_out, and_36_out, and_37_out, and_38_out);
  or or_4 (rs2, and_39_out, and_40_out, and_41_out, and_42_out, and_43_out, and_44_out, and_45_out);
endmodule

// ALU
module ALU (
  input  [31:0] X,
  input  [31:0] Y,
  input  [3:0] AluOP,
  output out_4,
  output Equal,
  output out_6,
  output [31:0] Result,
  output [31:0] Result_2
);

  wire [0:0] comparator_1_lt, comparator_2_lt;
  wire [31:0] adder_1_out, AND_out, divider_1_out, divider_1_rem, multiplier_1_cout, multiplier_1_out,
       NOR_out, OR_out, shifter_1_out, shifter_2_out, shifter_3_out, subtractor_1_out, XOR_out;

  assign AND_out = X & Y;  // AND_Gate AND, 32 bits wide
  assign OR_out = X | Y;  // OR_Gate OR, 32 bits wide
  Shifter #(.width(32), .shift("ll")) shifter_1 (.in(X), .\dist (Y[4:0]), .out(shifter_1_out));
  Shifter #(.width(32), .shift("ar")) shifter_2 (.in(X), .\dist (Y[4:0]), .out(shifter_2_out));
  Shifter #(.width(32), .shift("lr")) shifter_3 (.in(X), .\dist (Y[4:0]), .out(shifter_3_out));
  Multiplier #(.width(32)) multiplier_1 (.a(X), .b(Y), .out(multiplier_1_out), .cout(multiplier_1_cout));  // open: cin
  Divider #(.width(32)) divider_1 (.a(X), .b(Y), .out(divider_1_out), .rem(divider_1_rem));  // open: upper
  Adder #(.width(32)) adder_1 (.a(X), .b(Y), .out(adder_1_out));  // open: cin, cout
  Subtractor #(.width(32)) subtractor_1 (.a(X), .b(Y), .out(subtractor_1_out));  // open: bin, bout
  assign XOR_out = X ^ Y;  // XOR_Gate XOR, 32 bits wide
  assign NOR_out = ~(X | Y);  // NOR_Gate NOR, 32 bits wide
  Comparator #(.width(32), .mode("twosComplement")) comparator_1 (
    .a(X), .b(Y), .eq(Equal), .lt(comparator_1_lt[0]));  // open: gt
  Comparator #(.width(32), .mode("unsigned")) comparator_2 (.a(X), .b(Y), .lt(comparator_2_lt[0]));  // open: gt, eq
  Multiplexer #(.select(4), .width(32), .disabled("Z"), .enable("false")) multiplexer_1 (
    .in0(shifter_1_out), .in1(shifter_2_out), .in2(shifter_3_out), .in3(multiplier_1_out),
    .in4(divider_1_out), .in5(adder_1_out), .in6(subtractor_1_out), .in7(AND_out), .in8(OR_out),
    .in9(XOR_out), .in10(NOR_out), .in11({{31{1'b0}}, comparator_1_lt[0]}),
    .in12({{31{1'b0}}, comparator_2_lt[0]}), .in13({32{1'b0}}), .in14({32{1'b0}}), .in15({32{1'b0}}),
    .out(Result), .sel(AluOP));
  Multiplexer #(.select(4), .width(32), .disabled("Z"), .enable("false")) multiplexer_2 (
    .in0({32{1'b0}}), .in1({32{1'b0}}), .in2({32{1'b0}}), .in3(multiplier_1_cout), .in4(divider_1_rem),
    .in5({32{1'b0}}), .in6({32{1'b0}}), .in7({32{1'b0}}), .in8({32{1'b0}}), .in9({32{1'b0}}),
    .in10({32{1'b0}}), .in11({32{1'b0}}), .in12({32{1'b0}}), .in13({32{1'b0}}), .in14({32{1'b0}}),
    .in15({32{1'b0}}), .out(Result_2), .sel(AluOP));
  Multiplexer #(.select(4), .width(1), .disabled("Z"), .enable("false")) multiplexer_3 (
    .in0(1'b0), .in1(1'b0), .in2(1'b0), .in3(1'b0), .in4(1'b0), .in5(1'b0), .in6(1'b0), .in7(1'b0),
    .in8(1'b0), .in9(1'b0), .in10(1'b0), .in11(comparator_1_lt[0]), .in12(comparator_2_lt[0]), .in13(1'b0),
    .in14(1'b0), .in15(1'b0), .out(out_6), .sel(AluOP));
  not not_1 (out_4, out_6);

  // Other names for the same wires on the sheet: Result2[31:0] = Result_2; S[3:0] = AluOP; tunnel = out_6;
  //   tunnel_t = out_4

  // Notes on the sheet:
  //   不要改变此引脚区域内容，也不要改变ALU封装形式
  //   输入引脚
  //   输出引脚
endmodule

module Regifile (
  input  [31:0] Din,
  input  Clk,
  input  WE,
  input  [4:0] R1_num,
  input  [4:0] W_num,
  input  [4:0] R2_num,
  output [31:0] R1,
  output [31:0] R2
);

  // RegisterFile registerfile_1: pin names not known; wires that end beside it: Din, Clk, WE, W_num, R1_num, R2_num, R1, R2
endmodule

module \理想流水线  (
  output RegWrite,
  output MemWrite,
  output [31:0] IF_PC,
  output [31:0] ID_PC,
  output [31:0] EX_PC,
  output [31:0] M_PC,
  output [31:0] WB_PC,
  output [31:0] RDin,
  output [31:0] MDin,
  output [31:0] LedData
);

  wire alu_1_equal, alu_1_out_4, and_1_out, and_2_out, and_3_out, and_4_out, beq, bge, bne, CLK, clock_1_out,
       comparator_1_eq, comparator_1_lt, d_ff_1_q, ecall, EX_ecall, EX_halt, EX_Jal, EX_Jalr, EX_MEM_halt_2,
       EX_MEM_jal_2, EX_MEM_jalr_2, EX_MEM_memtoreg_2, EX_MEM_regwrite_2, Go, halt, ID_EX_alusrcb_2,
       ID_EX_memtoreg_2, ID_EX_memwrite_2, ID_EX_regwrite_2, IR1, IR2, IR3, JAL, MEM_WB_halt_2, MEM_WB_jal_2,
       MEM_WB_jalr_2, nand_1_out, not_1_out, not_2_out, RST, S, S_type, SB, W1, W2, W3,
       \单周期硬布线控制器_1_alu_src , \单周期硬布线控制器_1_beq , \单周期硬布线控制器_1_bge , \单周期硬布线控制器_1_bne , \单周期硬布线控制器_1_jalr ,
       \单周期硬布线控制器_1_memtoreg , \单周期硬布线控制器_1_memwrite , \单周期硬布线控制器_1_regwrite ;
  wire [1:0] MEM_WB_memtoreg_2;
  wire [3:0] ID_EX_aluop_2, \单周期硬布线控制器_1_alu_op ;
  wire [4:0] EX_MEM_rd_2, ID_EX_rd_2, multiplexer_2_out, multiplexer_3_out, WB_rd;
  wire [11:0] multiplexer_4_out;
  wire [12:0] CNT_num;
  wire [15:0] \LoadUse次数 , \总周期数 , \插入气泡数 , \无条件分支数 , \条件分支成功数 ;
  wire [31:0] ALU_addr, bit_extender_1_out, bit_extender_2_out, bit_extender_3_out, Branch_addr, EX_IR,
       EX_MEM_pc_4_2, EX_MEM_result_2, EX_PC_4, ID_EX_imm1_2, ID_EX_imm2_2, ID_EX_r1_2, ID_EX_r2_2, ID_IR,
       ID_PC_4, IF_IR, IF_PC_4, MEM_IR, MEM_WB_pc_4_2, MEM_WB_readdata_2, MEM_WB_result_2, multiplexer_1_out,
       multiplexer_5_out, multiplexer_6_out, ram_1_data, regifile_1_r1, regifile_1_r2, shifter_1_out, WB_IR;

  Button \u_总复位  (.out(RST));
  Button _1 (.out(IR1));
  Button _2 (.out(IR2));
  Button _3 (.out(IR3));
  // Probe on \总周期数 
  // Probe on \总周期数 
  not not_1 (not_1_out, halt);
  Multiplexer #(.select(2), .width(32), .disabled("Z"), .enable("false")) multiplexer_1 (
    .in0(IF_PC_4), .in1(ALU_addr), .in2(Branch_addr), .out(multiplexer_1_out), .sel({S, EX_Jalr}));  // open: in3
  not not_2 (not_2_out, halt);
  Button \u_继续运行  (.out(Go));
  LED #(.active("true")) led_1 (.in(W1));
  LED #(.active("true")) led_2 (.in(W2));
  LED #(.active("true")) led_3 (.in(W3));
  Counter #(.width(16), .max('hffff), .ongoal("wrap"), .trigger("rising"), .behavior("new")) counter_1 (
    .count(not_1_out), .Q(\总周期数 ), .clk(CLK));  // open: load, D, carry, clr, preset, down
  Register #(.width(32), .trigger("rising"), .Select("low")) PC (
    .D(multiplexer_1_out), .en(not_2_out), .Q(IF_PC), .clk(CLK), .clr(RST));
  Hex_Digit_Display hex_digit_display_1 (.value(LedData[31:28]));  // open: dp
  // Probe on IF_PC[19:0]
  // RiscV_Probe riscv_probe_1: pin names not known; wires that end beside it: IF_IR, \总周期数 
  Adder #(.width(32)) adder_1 (.a(IF_PC), .b(32'h4), .out(IF_PC_4));  // open: cin, cout
  Hex_Digit_Display hex_digit_display_2 (.value(LedData[27:24]));  // open: dp
  Hex_Digit_Display hex_digit_display_3 (.value(LedData[23:20]));  // open: dp
  // Probe on ID_PC[19:0]
  // RiscV_Probe riscv_probe_2: pin names not known; wires that end beside it: ID_IR
  ROM #(.addrWidth(10), .dataWidth(32), .Select("high")) \u_指令存储器  (.addr(IF_PC[11:2]), .data(IF_IR));
  Hex_Digit_Display hex_digit_display_4 (.value(LedData[19:16]));  // open: dp
  Hex_Digit_Display hex_digit_display_5 (.value(LedData[15:12]));  // open: dp
  Hex_Digit_Display hex_digit_display_6 (.value(LedData[11:8]));  // open: dp
  Hex_Digit_Display hex_digit_display_7 (.value(LedData[7:4]));  // open: dp
  // Probe on EX_PC[19:0]
  // RiscV_Probe riscv_probe_3: pin names not known; wires that end beside it: EX_IR
  IF_ID IF_ID (
    .IR(IF_IR), .PC(IF_PC), .PC_4(IF_PC_4), .IR_2(ID_IR), .PC_2(ID_PC), .PC_4_2(ID_PC_4), .Reset(RST),
    .BranchTaken(1'b0), .En(1'b1), .CLK(CLK));  // open: PredictJump, PredictJump_2
  Hex_Digit_Display hex_digit_display_8 (.value(LedData[3:0]));  // open: dp
  // Probe on \总周期数 
  // Probe on M_PC[19:0]
  // RiscV_Probe riscv_probe_4: pin names not known; wires that end beside it: MEM_IR
  \单周期硬布线控制器  \u_单周期硬布线控制器_1  (
    .Funct({ID_IR[30], ID_IR[25], ID_IR[14:12]}), .OP(ID_IR[6:2]), .ALU_OP(\单周期硬布线控制器_1_alu_op ),
    .MemToReg(\单周期硬布线控制器_1_memtoreg ), .MemWrite(\单周期硬布线控制器_1_memwrite ), .ALU_SRC(\单周期硬布线控制器_1_alu_src ),
    .RegWrite(\单周期硬布线控制器_1_regwrite ), .ecall(ecall), .S_type(S_type), .Jalr(\单周期硬布线控制器_1_jalr ),
    .Beq(\单周期硬布线控制器_1_beq ), .JAL(JAL), .Bne(\单周期硬布线控制器_1_bne ), .in_3(ID_IR[21]), .BGE(\单周期硬布线控制器_1_bge ),
    .SB(SB));  // open: uret, rs1, rs2, csrrsi, csrrci
  Multiplexer #(.select(1), .width(5), .disabled("Z"), .enable("false")) multiplexer_2 (
    .in0(ID_IR[19:15]), .in1(5'b10001), .out(multiplexer_2_out), .sel(ecall));
  Multiplexer #(.select(1), .width(5), .disabled("Z"), .enable("false")) multiplexer_3 (
    .in0(ID_IR[24:20]), .in1(5'b01010), .out(multiplexer_3_out), .sel(ecall));
  assign bit_extender_1_out = {{20{multiplexer_4_out[11]}}, multiplexer_4_out};  // Bit_Extender bit_extender_1
  Multiplexer #(.select(1), .width(12), .disabled("Z"), .enable("false")) multiplexer_4 (
    .in0(ID_IR[31:20]), .in1({ID_IR[31:25], ID_IR[11:7]}), .out(multiplexer_4_out), .sel(S_type));
  assign bit_extender_2_out = {{20{ID_IR[31]}}, {ID_IR[31], ID_IR[7], ID_IR[30:25], ID_IR[11:8]}};  // Bit_Extender bit_extender_2
  assign bit_extender_3_out = {{12{ID_IR[31]}}, {ID_IR[31], ID_IR[19:12], ID_IR[20], ID_IR[30:21]}};  // Bit_Extender bit_extender_3
  // Probe on \总周期数 
  // Probe on \无条件分支数 
  // Probe on \条件分支成功数 
  // Probe on \插入气泡数 
  // Probe on \LoadUse次数 
  Multiplexer #(.select(1), .width(32), .disabled("Z"), .enable("false")) multiplexer_5 (
    .in0(bit_extender_2_out), .in1(bit_extender_3_out), .out(multiplexer_5_out), .sel(JAL));
  // Probe on IF_PC[11:0]
  // Probe on WB_PC[19:0]
  // RiscV_Probe riscv_probe_5: pin names not known; wires that end beside it: WB_IR
  Regifile regifile_1 (
    .Din(RDin), .Clk(CLK), .R1(regifile_1_r1), .R2(regifile_1_r2), .WE(RegWrite), .W_num(WB_rd),
    .R1_num(multiplexer_2_out), .R2_num(multiplexer_3_out));
  // Probe on EX_PC[11:0]
  // Probe on ID_PC[11:0]
  // Probe on M_PC[11:0]
  D_Flip_Flop #(.trigger("high"), .Pre_Clr_Positions("LEGACY"), .NegatePresetClear("false"), .enable("true"), .NewFFLayout("false")) d_ff_1 (.Q(d_ff_1_q));  // open: clk, D, Qn, preset, en, reset
  // Probe on 13'hc
  // Probe on WB_PC[11:0]
  Comparator #(.width(13), .mode("twosComplement")) comparator_1 (
    .a(CNT_num), .b(13'hc), .eq(comparator_1_eq), .lt(comparator_1_lt));  // open: gt
  Clock #(.highDuration(1), .lowDuration(1)) clock_1 (.out(clock_1_out));
  ID_EX ID_EX (
    .Beq(\单周期硬布线控制器_1_beq ), .Beq_2(beq), .Bne(\单周期硬布线控制器_1_bne ), .Bne_2(bne), .Bge(\单周期硬布线控制器_1_bge ),
    .Bge_2(bge), .MemToReg(\单周期硬布线控制器_1_memtoreg ), .MemToReg_2(ID_EX_memtoreg_2),
    .MemWrite(\单周期硬布线控制器_1_memwrite ), .MemWrite_2(ID_EX_memwrite_2), .AluSrcB(\单周期硬布线控制器_1_alu_src ),
    .AluSrcB_2(ID_EX_alusrcb_2), .RegWrite_2(ID_EX_regwrite_2), .RegWrite(\单周期硬布线控制器_1_regwrite ),
    .Ecall(ecall), .Ecall_2(EX_ecall), .Jal_2(EX_Jal), .Jal(JAL), .Jalr(\单周期硬布线控制器_1_jalr ),
    .Jalr_2(EX_Jalr), .SB(SB), .Reset(RST), .flush(1'b0), .En(1'b1), .CLK(CLK), .AluOp(\单周期硬布线控制器_1_alu_op ),
    .AluOp_2(ID_EX_aluop_2), .rd(ID_IR[11:7]), .rd_2(ID_EX_rd_2), .R1(regifile_1_r1), .R1_2(ID_EX_r1_2),
    .R2(regifile_1_r2), .R2_2(ID_EX_r2_2), .imm1(bit_extender_1_out), .imm1_2(ID_EX_imm1_2),
    .imm2(multiplexer_5_out), .imm2_2(ID_EX_imm2_2), .PC(ID_PC), .PC_2(EX_PC), .PC_4(ID_PC_4),
    .PC_4_2(EX_PC_4), .IR(ID_IR), .IR_2(EX_IR));  // open: PredictJump, PredictJump_2, SB_2, rs1forward, rs1forward_2, rs2forward, rs2forward_2, branch, branch_2
  Multiplexer #(.select(1), .width(32), .disabled("Z"), .enable("false")) multiplexer_6 (
    .in0(ID_EX_r2_2), .in1(ID_EX_imm1_2), .out(multiplexer_6_out), .sel(ID_EX_alusrcb_2));
  nand nand_1 (nand_1_out, d_ff_1_q, comparator_1_eq);
  Counter #(.width(13), .max('h1fff), .ongoal("stay"), .trigger("rising"), .behavior("old")) counter_2 (
    .count(comparator_1_lt), .Q(CNT_num), .clk(clock_1_out));  // open: load, D, carry, clr, preset
  Shifter #(.width(32), .shift("ll")) shifter_1 (.in(ID_EX_imm2_2), .\dist (5'b00001), .out(shifter_1_out));
  Comparator #(.width(32), .mode("unsigned")) comparator_2 (.a(ID_EX_r1_2), .b(32'ha), .eq(EX_halt));  // open: gt, lt
  and and_1 (and_1_out, EX_ecall, ~EX_halt);  // AND_Gate
  assign CLK = nand_1_out ? clock_1_out : 1'bz;  // Controlled_Buffer controlled_buffer_1
  ALU alu_1 (
    .X(ID_EX_r1_2), .Y(multiplexer_6_out), .AluOP(ID_EX_aluop_2), .Equal(alu_1_equal), .Result(ALU_addr),
    .out_4(alu_1_out_4));  // open: Result_2, out_6
  Register #(.width(32), .trigger("rising"), .Select("low")) register_1 (
    .D(ID_EX_r2_2), .en(and_1_out), .Q(LedData), .clk(CLK));  // open: clr
  Pull_Resistor #(.pull(1)) pull_resistor_1 (.node(CLK));
  and and_2 (and_2_out, alu_1_equal, beq);
  and and_3 (and_3_out, ~alu_1_equal, bne);  // AND_Gate
  and and_4 (and_4_out, alu_1_out_4, bge);
  or or_1 (S, and_4_out, and_3_out, and_2_out);
  Adder #(.width(32)) adder_2 (.a(shifter_1_out), .b(EX_PC), .out(Branch_addr));  // open: cin, cout
  EX_MEM EX_MEM (
    .MemToReg(ID_EX_memtoreg_2), .MemToReg_2(EX_MEM_memtoreg_2), .MemWrite(ID_EX_memwrite_2),
    .MemWrite_2(MemWrite), .RegWrite(ID_EX_regwrite_2), .RegWrite_2(EX_MEM_regwrite_2), .Jal(EX_Jal),
    .Jal_2(EX_MEM_jal_2), .Jalr(EX_Jalr), .Jalr_2(EX_MEM_jalr_2), .rd(ID_EX_rd_2), .rd_2(EX_MEM_rd_2),
    .Reset(RST), .En(1'b1), .CLK(CLK), .PC(EX_PC), .PC_2(M_PC), .PC_4(EX_PC_4), .PC_4_2(EX_MEM_pc_4_2),
    .IR(EX_IR), .IR_2(MEM_IR), .WriteData(ID_EX_r2_2), .WriteData_2(MDin), .result(ALU_addr),
    .result_2(EX_MEM_result_2), .halt(EX_halt), .halt_2(EX_MEM_halt_2));  // open: SB, SB_2
  RAM #(.addrWidth(10), .dataWidth(32), .bus("separate"), .Select("high")) ram_1 (
    .addr(EX_MEM_result_2[11:2]), .din(MDin), .data(ram_1_data), .str(MemWrite), .sel(1'b1), .clk(CLK),
    .ld(1'b1), .clr(RST));
  MEM_WB MEM_WB (
    .result(EX_MEM_result_2), .result_2(MEM_WB_result_2), .MemToReg(EX_MEM_memtoreg_2),
    .ReadData(ram_1_data), .MemToReg_2(MEM_WB_memtoreg_2[0]), .ReadData_2(MEM_WB_readdata_2), .PC(M_PC),
    .RegWrite(EX_MEM_regwrite_2), .PC_2(WB_PC), .RegWrite_2(RegWrite), .Jal(EX_MEM_jal_2),
    .Jal_2(MEM_WB_jal_2), .PC_4(EX_MEM_pc_4_2), .Jalr(EX_MEM_jalr_2), .PC_4_2(MEM_WB_pc_4_2),
    .Jalr_2(MEM_WB_jalr_2), .IR(MEM_IR), .IR_2(WB_IR), .rd(EX_MEM_rd_2), .rd_2(WB_rd), .Reset(RST),
    .En(1'b1), .CLK(CLK), .halt(EX_MEM_halt_2), .halt_2(MEM_WB_halt_2));
  or or_2 (MEM_WB_memtoreg_2[1], MEM_WB_jal_2, MEM_WB_jalr_2);
  Multiplexer #(.select(2), .width(32), .disabled("Z"), .enable("false")) multiplexer_7 (
    .in0(MEM_WB_result_2), .in1(MEM_WB_readdata_2), .in2(MEM_WB_pc_4_2), .out(RDin), .sel(MEM_WB_memtoreg_2));  // open: in3
  D_Flip_Flop #(.trigger("rising"), .Pre_Clr_Positions("ABOVE_BELOW"), .NegatePresetClear("false"), .enable("true"), .NewFFLayout("true")) d_ff_2 (
    .clk(MEM_WB_halt_2), .D(1'b1), .Q(halt), .en(1'b1), .reset(Go));  // open: Qn, preset

  // Other names for the same wires on the sheet: MEM_PC[31:0] = M_PC; WB_RegWrite = RegWrite

  // Notes on the sheet:
  //   中断源
  //   时空图监测，可删除
  //   En
  //   中断等待指示
  //   contents of 指令存储器 (hex, n*v repeats v):
  //   413 493 913 993 46413 14e493 296913 39e993 842023 942223 1242423 1342623 a00893 493 913 993 73
  //   数码管输出
  //   指令字
  //   JAL
  //   JALR
  //   URET
  //   SB
  //   B.Inst. Imm
  //   J.Inst. Imm
  //   rd
  //   Beq
  //   Bge
  //   Bne
  //   MemToReg
  //   MemWrite
  //   AluOP
  //   AluSrcB
  //   RegWrite
  //   控制位
  //   流水调试日志用
  //   暂停节拍，不能为0
  //   戳工具置1进入计数暂停模式，ctrl+k时钟自动运行到对应节拍暂停
  //   ctrl+k关闭时钟连续运行，将控制位置零，进入单步调试模式调试
  //   用这个时钟源需要去掉电路中的其他时钟源
  //   可计数暂停的时钟源
  //   为方便自动评测，需要输出流水线各段保存的PC值，注意是PC不是PC+4，另外ID段寄存器写入信息，Mem段内存写入信息也要输出
endmodule

module \气泡流水线  (
  output RegWrite,
  output MemWrite,
  output [31:0] IF_PC,
  output [31:0] ID_PC,
  output [31:0] EX_PC,
  output [31:0] M_PC,
  output [31:0] WB_PC,
  output [31:0] RDin,
  output [31:0] MDin,
  output [31:0] LedData
);

  wire alu_1_equal, alu_1_out_4, and_1_out, and_2_out, and_4_out, and_5_out, and_6_out, and_7_out, and_8_out,
       and_9_out, beq, bge, bne, Branch_BT, BranchTaken, CLK, clock_1_out, comparator_1_eq, comparator_1_lt,
       comparator_2_eq, d_ff_1_q, ecall, EX_ecall, EX_halt, EX_J, EX_Jal, EX_Jalr, EX_MEM_halt_2,
       EX_MEM_jal_2, EX_MEM_jalr_2, EX_MEM_memtoreg_2, EX_RegWrite, EX_SB, flush, Go, halt, ID_EX_alusrcb_2,
       ID_EX_memtoreg_2, ID_EX_memwrite_2, IR1, IR2, IR3, JAL, MEM_RegWrite, MEM_SB, MEM_WB_halt_2,
       MEM_WB_jal_2, MEM_WB_jalr_2, nand_1_out, not_1_out, not_2_out, not_3_out, or_6_out, RST, S, S_type,
       SB, stall, W1, W2, W3, \单周期硬布线控制器_1_alu_src , \单周期硬布线控制器_1_beq , \单周期硬布线控制器_1_bge , \单周期硬布线控制器_1_bne ,
       \单周期硬布线控制器_1_jalr , \单周期硬布线控制器_1_memtoreg , \单周期硬布线控制器_1_memwrite , \单周期硬布线控制器_1_regwrite ,
       \单周期硬布线控制器_1_rs1 , \单周期硬布线控制器_1_rs2 ;
  wire [1:0] MEM_WB_memtoreg_2, SB_sel;
  wire [3:0] ID_EX_aluop_2, \单周期硬布线控制器_1_alu_op ;
  wire [4:0] EX_MEM_rd_2, ID_EX_rd_2, multiplexer_2_out, multiplexer_3_out, WB_rd;
  wire [11:0] multiplexer_4_out;
  wire [12:0] CNT_num;
  wire [15:0] \LoadUse次数 , \总周期数 , \插入气泡数 , \无条件分支数 , \条件分支成功数 ;
  wire [31:0] ALU_addr, bit_extender_1_out, bit_extender_2_out, bit_extender_3_out, Branch_addr, EX_IR,
       EX_MEM_pc_4_2, EX_PC_4, ID_EX_imm1_2, ID_EX_imm2_2, ID_EX_r1_2, ID_EX_r2_2, ID_IR, ID_PC_4, IF_IR,
       IF_PC_4, MDout, MEM_Din, MEM_IR, MEM_WB_pc_4_2, MEM_WB_readdata_2, MEM_WB_result_2, multiplexer_1_out,
       multiplexer_5_out, multiplexer_6_out, regifile_1_r1, regifile_1_r2, SBin, shifter_1_out, WB_IR;
  wire [31:2] EX_MEM_result_2;

  Button \u_总复位  (.out(RST));
  Button _1 (.out(IR1));
  Button _2 (.out(IR2));
  Button _3 (.out(IR3));
  // Probe on \总周期数 
  // Probe on \总周期数 
  Button \u_继续运行  (.out(Go));
  LED #(.active("true")) led_1 (.in(W1));
  LED #(.active("true")) led_2 (.in(W2));
  LED #(.active("true")) led_3 (.in(W3));
  Multiplexer #(.select(2), .width(32), .disabled("Z"), .enable("false")) multiplexer_1 (
    .in0(IF_PC_4), .in1(ALU_addr), .in2(Branch_addr), .out(multiplexer_1_out), .sel({S, EX_Jalr}));  // open: in3
  and and_1 (and_1_out, ~stall, ~halt);  // AND_Gate
  Hex_Digit_Display hex_digit_display_1 (.value(LedData[31:28]));  // open: dp
  // Probe on IF_PC[19:0]
  // RiscV_Probe riscv_probe_1: pin names not known; wires that end beside it: IF_IR
  Register #(.width(32), .trigger("rising"), .Select("low")) PC (
    .D(multiplexer_1_out), .en(and_1_out), .Q(IF_PC), .clk(CLK), .clr(RST));
  Hex_Digit_Display hex_digit_display_2 (.value(LedData[27:24]));  // open: dp
  Hex_Digit_Display hex_digit_display_3 (.value(LedData[23:20]));  // open: dp
  // Probe on ID_PC[19:0]
  // RiscV_Probe riscv_probe_2: pin names not known; wires that end beside it: ID_IR
  or or_1 (EX_J, EX_Jal, EX_Jalr);
  Adder #(.width(32)) adder_1 (.a(IF_PC), .b(32'h4), .out(IF_PC_4));  // open: cin, cout
  Hex_Digit_Display hex_digit_display_4 (.value(LedData[19:16]));  // open: dp
  Hex_Digit_Display hex_digit_display_5 (.value(LedData[15:12]));  // open: dp
  ROM #(.addrWidth(10), .dataWidth(32), .Select("high")) \u_指令存储器  (.addr(IF_PC[11:2]), .data(IF_IR));
  Hex_Digit_Display hex_digit_display_6 (.value(LedData[7:4]));  // open: dp
  Hex_Digit_Display hex_digit_display_7 (.value(LedData[11:8]));  // open: dp
  // Probe on EX_PC[19:0]
  // RiscV_Probe riscv_probe_3: pin names not known; wires that end beside it: EX_IR
  or or_2 (BranchTaken, S, EX_Jalr);
  Hex_Digit_Display hex_digit_display_8 (.value(LedData[3:0]));  // open: dp
  IF_ID IF_ID (
    .IR(IF_IR), .PC(IF_PC), .PC_4(IF_PC_4), .IR_2(ID_IR), .PC_2(ID_PC), .PC_4_2(ID_PC_4), .Reset(RST),
    .BranchTaken(BranchTaken), .En(and_1_out), .CLK(CLK));  // open: PredictJump, PredictJump_2
  // Probe on \总周期数 
  // Probe on M_PC[19:0]
  // RiscV_Probe riscv_probe_4: pin names not known; wires that end beside it: MEM_IR
  // Probe on \总周期数 
  // Probe on \无条件分支数 
  // Probe on \条件分支成功数 
  // Probe on \插入气泡数 
  // Probe on \LoadUse次数 
  \单周期硬布线控制器  \u_单周期硬布线控制器_1  (
    .Funct({ID_IR[30], ID_IR[25], ID_IR[14:12]}), .OP(ID_IR[6:2]), .ALU_OP(\单周期硬布线控制器_1_alu_op ),
    .MemToReg(\单周期硬布线控制器_1_memtoreg ), .MemWrite(\单周期硬布线控制器_1_memwrite ), .ALU_SRC(\单周期硬布线控制器_1_alu_src ),
    .RegWrite(\单周期硬布线控制器_1_regwrite ), .ecall(ecall), .S_type(S_type), .Jalr(\单周期硬布线控制器_1_jalr ),
    .Beq(\单周期硬布线控制器_1_beq ), .JAL(JAL), .Bne(\单周期硬布线控制器_1_bne ), .in_3(ID_IR[21]), .BGE(\单周期硬布线控制器_1_bge ),
    .SB(SB), .rs1(\单周期硬布线控制器_1_rs1 ), .rs2(\单周期硬布线控制器_1_rs2 ));  // open: uret, csrrsi, csrrci
  Multiplexer #(.select(1), .width(5), .disabled("Z"), .enable("false")) multiplexer_2 (
    .in0(ID_IR[19:15]), .in1(5'b10001), .out(multiplexer_2_out), .sel(ecall));
  Multiplexer #(.select(1), .width(5), .disabled("Z"), .enable("false")) multiplexer_3 (
    .in0(ID_IR[24:20]), .in1(5'b01010), .out(multiplexer_3_out), .sel(ecall));
  Multiplexer #(.select(1), .width(12), .disabled("Z"), .enable("false")) multiplexer_4 (
    .in0(ID_IR[31:20]), .in1({ID_IR[31:25], ID_IR[11:7]}), .out(multiplexer_4_out), .sel(S_type));
  assign bit_extender_1_out = {{20{multiplexer_4_out[11]}}, multiplexer_4_out};  // Bit_Extender bit_extender_1
  assign bit_extender_2_out = {{20{ID_IR[31]}}, {ID_IR[31], ID_IR[7], ID_IR[30:25], ID_IR[11:8]}};  // Bit_Extender bit_extender_2
  assign bit_extender_3_out = {{12{ID_IR[31]}}, {ID_IR[31], ID_IR[19:12], ID_IR[20], ID_IR[30:21]}};  // Bit_Extender bit_extender_3
  // Probe on IF_PC[11:0]
  // Probe on WB_PC[19:0]
  // RiscV_Probe riscv_probe_5: pin names not known; wires that end beside it: WB_IR
  Multiplexer #(.select(1), .width(32), .disabled("Z"), .enable("false")) multiplexer_5 (
    .in0(bit_extender_2_out), .in1(bit_extender_3_out), .out(multiplexer_5_out), .sel(JAL));
  // Probe on EX_PC[11:0]
  // Probe on ID_PC[11:0]
  not not_1 (not_1_out, CLK);
  Regifile regifile_1 (
    .Din(RDin), .Clk(not_1_out), .R1(regifile_1_r1), .R2(regifile_1_r2), .WE(RegWrite), .W_num(WB_rd),
    .R1_num(multiplexer_2_out), .R2_num(multiplexer_3_out));
  not not_2 (not_2_out, halt);
  // Probe on M_PC[11:0]
  D_Flip_Flop #(.trigger("high"), .Pre_Clr_Positions("LEGACY"), .NegatePresetClear("false"), .enable("true"), .NewFFLayout("false")) d_ff_1 (.Q(d_ff_1_q));  // open: clk, D, Qn, preset, en, reset
  // Probe on 13'h1552
  // Probe on WB_PC[11:0]
  Comparator #(.width(13), .mode("twosComplement")) comparator_1 (
    .a(CNT_num), .b(13'h1552), .eq(comparator_1_eq), .lt(comparator_1_lt));  // open: gt
  Clock #(.highDuration(1), .lowDuration(1)) clock_1 (.out(clock_1_out));
  nand nand_1 (nand_1_out, d_ff_1_q, comparator_1_eq);
  Counter #(.width(13), .max('h1fff), .ongoal("stay"), .trigger("rising"), .behavior("old")) counter_1 (
    .count(comparator_1_lt), .Q(CNT_num), .clk(clock_1_out));  // open: load, D, carry, clr, preset
  ID_EX ID_EX (
    .Beq(\单周期硬布线控制器_1_beq ), .Beq_2(beq), .Bne(\单周期硬布线控制器_1_bne ), .Bne_2(bne), .Bge(\单周期硬布线控制器_1_bge ),
    .Bge_2(bge), .MemToReg(\单周期硬布线控制器_1_memtoreg ), .MemToReg_2(ID_EX_memtoreg_2),
    .MemWrite(\单周期硬布线控制器_1_memwrite ), .MemWrite_2(ID_EX_memwrite_2), .AluSrcB(\单周期硬布线控制器_1_alu_src ),
    .AluSrcB_2(ID_EX_alusrcb_2), .RegWrite_2(EX_RegWrite), .RegWrite(\单周期硬布线控制器_1_regwrite ), .Ecall(ecall),
    .Ecall_2(EX_ecall), .Jal_2(EX_Jal), .Jal(JAL), .Jalr(\单周期硬布线控制器_1_jalr ), .Jalr_2(EX_Jalr), .SB(SB),
    .SB_2(EX_SB), .Reset(RST), .flush(flush), .En(not_2_out), .CLK(CLK), .AluOp(\单周期硬布线控制器_1_alu_op ),
    .AluOp_2(ID_EX_aluop_2), .rd(ID_IR[11:7]), .rd_2(ID_EX_rd_2), .R1(regifile_1_r1), .R1_2(ID_EX_r1_2),
    .R2(regifile_1_r2), .R2_2(ID_EX_r2_2), .imm1(bit_extender_1_out), .imm1_2(ID_EX_imm1_2),
    .imm2(multiplexer_5_out), .imm2_2(ID_EX_imm2_2), .PC(ID_PC), .PC_2(EX_PC), .PC_4(ID_PC_4),
    .PC_4_2(EX_PC_4), .IR(ID_IR), .IR_2(EX_IR));  // open: PredictJump, PredictJump_2, rs1forward, rs1forward_2, rs2forward, rs2forward_2, branch, branch_2
  Multiplexer #(.select(1), .width(32), .disabled("Z"), .enable("false")) multiplexer_6 (
    .in0(ID_EX_r2_2), .in1(ID_EX_imm1_2), .out(multiplexer_6_out), .sel(ID_EX_alusrcb_2));
  assign CLK = nand_1_out ? clock_1_out : 1'bz;  // Controlled_Buffer controlled_buffer_1
  Shifter #(.width(32), .shift("ll")) shifter_1 (.in(ID_EX_imm2_2), .\dist (5'b00001), .out(shifter_1_out));
  Comparator #(.width(32), .mode("unsigned")) comparator_2 (
    .a(ID_EX_r1_2), .b(32'ha), .eq(comparator_2_eq));  // open: gt, lt
  and and_2 (and_2_out, EX_ecall, ~comparator_2_eq);  // AND_Gate
  Pull_Resistor #(.pull(1)) pull_resistor_1 (.node(CLK));
  ALU alu_1 (
    .X(ID_EX_r1_2), .Y(multiplexer_6_out), .AluOP(ID_EX_aluop_2), .Equal(alu_1_equal), .Result(ALU_addr),
    .out_4(alu_1_out_4));  // open: Result_2, out_6
  and and_3 (EX_halt, EX_ecall, comparator_2_eq);
  Register #(.width(32), .trigger("rising"), .Select("low")) register_1 (
    .D(ID_EX_r2_2), .en(and_2_out), .Q(LedData), .clk(CLK));  // open: clr
  not not_3 (not_3_out, halt);
  and and_4 (and_4_out, alu_1_equal, beq);
  and and_5 (and_5_out, ~alu_1_equal, bne);  // AND_Gate
  and and_6 (and_6_out, alu_1_out_4, bge);
  or or_3 (Branch_BT, and_6_out, and_5_out, and_4_out);
  Adder #(.width(32)) adder_2 (.a(shifter_1_out), .b(EX_PC), .out(Branch_addr));  // open: cin, cout
  Counter #(.width(16), .max('hffff), .ongoal("wrap"), .trigger("rising"), .behavior("old")) counter_2 (
    .count(not_3_out), .Q(\总周期数 ), .clk(CLK));  // open: load, D, carry, clr, preset
  or or_4 (S, Branch_BT, EX_Jal);
  and and_7 (and_7_out, not_3_out, EX_J);
  EX_MEM EX_MEM (
    .MemToReg(ID_EX_memtoreg_2), .MemToReg_2(EX_MEM_memtoreg_2), .MemWrite(ID_EX_memwrite_2),
    .MemWrite_2(MemWrite), .RegWrite(EX_RegWrite), .RegWrite_2(MEM_RegWrite), .Jal(EX_Jal),
    .Jal_2(EX_MEM_jal_2), .Jalr(EX_Jalr), .Jalr_2(EX_MEM_jalr_2), .SB(EX_SB), .SB_2(MEM_SB), .rd(ID_EX_rd_2),
    .rd_2(EX_MEM_rd_2), .Reset(RST), .En(not_2_out), .CLK(CLK), .PC(EX_PC), .PC_2(M_PC), .PC_4(EX_PC_4),
    .PC_4_2(EX_MEM_pc_4_2), .IR(EX_IR), .IR_2(MEM_IR), .WriteData(ID_EX_r2_2), .WriteData_2(MDin),
    .result(ALU_addr), .result_2({EX_MEM_result_2, SB_sel}), .halt(EX_halt), .halt_2(EX_MEM_halt_2));
  Multiplexer #(.select(1), .width(32), .disabled("Z"), .enable("false")) multiplexer_7 (
    .in0(MDin), .in1(SBin), .out(MEM_Din), .sel(MEM_SB));
  Counter #(.width(16), .max('hffff), .ongoal("wrap"), .trigger("rising"), .behavior("old")) counter_3 (
    .count(and_7_out), .Q(\无条件分支数 ), .clk(CLK));  // open: load, D, carry, clr, preset
  // OR_Gate or_5 has open pins: in0=MemWrite, in1=MEM_SB, out=open
  and and_8 (and_8_out, not_3_out, Branch_BT);
  RAM #(.addrWidth(10), .dataWidth(32), .bus("separate"), .Select("high")) ram_1 (
    .addr(EX_MEM_result_2[11:2]), .din(MEM_Din), .data(MDout), .str(MemWrite), .sel(1'b1), .clk(CLK),
    .ld(1'b1), .clr(RST));
  Counter #(.width(16), .max('hffff), .ongoal("wrap"), .trigger("rising"), .behavior("old")) counter_4 (
    .count(and_8_out), .Q(\条件分支成功数 ), .clk(CLK));  // open: load, D, carry, clr, preset
  \气泡流水线逻辑  \u_气泡流水线逻辑  (
    .BranchTaken(BranchTaken), .IR(ID_IR), .ecall(ecall), .rs1(\单周期硬布线控制器_1_rs1 ), .EX_RegWrite(EX_RegWrite),
    .EX_rd(ID_EX_rd_2), .rs2(\单周期硬布线控制器_1_rs2 ), .MEM_RegWrite(MEM_RegWrite), .MEM_rd(EX_MEM_rd_2),
    .stall(stall), .flush(flush));
  and and_9 (and_9_out, not_3_out, or_6_out);
  or or_6 (or_6_out, stall, BranchTaken);
  Counter #(.width(16), .max('hffff), .ongoal("wrap"), .trigger("rising"), .behavior("old")) counter_5 (
    .count(and_9_out), .Q(\插入气泡数 ), .clk(CLK));  // open: load, D, carry, clr, preset
  Multiplexer #(.select(2), .width(32), .disabled("Z"), .enable("false")) multiplexer_8 (
    .in0({MDout[31:8], MDin[7:0]}), .in1({MDout[31:16], MDin[7:0], MDout[7:0]}),
    .in2({MDout[31:24], MDin[7:0], MDout[15:0]}), .in3({MDin[7:0], MDout[23:0]}), .out(SBin), .sel(SB_sel));
  MEM_WB MEM_WB (
    .result({EX_MEM_result_2, SB_sel}), .result_2(MEM_WB_result_2), .MemToReg(EX_MEM_memtoreg_2),
    .ReadData(MDout), .MemToReg_2(MEM_WB_memtoreg_2[0]), .ReadData_2(MEM_WB_readdata_2), .PC(M_PC),
    .RegWrite(MEM_RegWrite), .PC_2(WB_PC), .RegWrite_2(RegWrite), .Jal(EX_MEM_jal_2), .Jal_2(MEM_WB_jal_2),
    .PC_4(EX_MEM_pc_4_2), .Jalr(EX_MEM_jalr_2), .PC_4_2(MEM_WB_pc_4_2), .Jalr_2(MEM_WB_jalr_2), .IR(MEM_IR),
    .IR_2(WB_IR), .rd(EX_MEM_rd_2), .rd_2(WB_rd), .Reset(RST), .En(not_2_out), .CLK(CLK),
    .halt(EX_MEM_halt_2), .halt_2(MEM_WB_halt_2));
  or or_7 (MEM_WB_memtoreg_2[1], MEM_WB_jal_2, MEM_WB_jalr_2);
  Multiplexer #(.select(2), .width(32), .disabled("Z"), .enable("false")) multiplexer_9 (
    .in0(MEM_WB_result_2), .in1(MEM_WB_readdata_2), .in2(MEM_WB_pc_4_2), .out(RDin), .sel(MEM_WB_memtoreg_2));  // open: in3
  D_Flip_Flop #(.trigger("rising"), .Pre_Clr_Positions("ABOVE_BELOW"), .NegatePresetClear("false"), .enable("true"), .NewFFLayout("true")) d_ff_2 (
    .clk(MEM_WB_halt_2), .D(1'b1), .Q(halt), .en(1'b1), .reset(Go));  // open: Qn, preset

  // Other names for the same wires on the sheet: MEM_PC[31:0] = M_PC; MEM_str = MemWrite; WB_RegWrite = RegWrite

  // Notes on the sheet:
  //   中断源
  //   时空图监测，可删除
  //   中断等待指示
  //   数码管输出
  //   contents of 指令存储器 (hex, n*v repeats v):
  //   100493 100006f 100493 200913 300993 100006f 100493 200913 300993 100006f 100493 200913 300993
  //   100006f 100493 200913 300993 394000ef 100413 100493 1f49493 900533 2200893 73 24d493 48463 fedff06f
  //   900533 2200893 73 100493 249493 900533 2200893 73 48463 fedff06f 100493 1f49493 900533 2200893 73
  //   4034d493 900533 2200893 73 4044d493 900533 2200893 73 4044d493 900533 2200893 73 4044d493 900533
  //   2200893 73 4044d493 900533 2200893 73 4044d493 900533 2200893 73 4044d493 900533 2200893 73 4044d493
  //   900533 2200893 73 100413 1f41993 41f9d993 433 c00913 300b13 140413 f47413 800293 100313 499993
  //   89e9b3 1300533 2200893 73 406282b3 fe0294e3 140413 f00f93 1f47433 1c41413 800293 100313 49d993
  //   89e9b3 1300533 2200893 73 406282b3 fe0294e3 1c45413 406b0b33 b0463 f95ff06f 2b3 fff2c293 829293
  //   ff2e293 500533 2200893 73 fff00413 493 84a023 140413 448493 84a023 140413 448493 84a023 140413
  //   448493 84a023 140413 448493 84a023 140413 448493 84a023 140413 448493 84a023 140413 448493 84a023
  //   140413 448493 84a023 140413 448493 84a023 140413 448493 84a023 140413 448493 84a023 140413 448493
  //   84a023 140413 448493 84a023 140413 448493 84a023 140413 448493 84a023 140413 448493 140413 433
  //   3c00493 42983 4aa03 149a2b3 28663 134a023 1442023 ffc48493 fe9412e3 800533 2200893 73 440413 3c00493
  //   fc9416e3 a00893 73 100293 300313 800493 849493 7648493 900533 2200893 73 800e13 5494b3 6494b3 900533
  //   2200893 73 fffe0e13 fe0e14e3 100293 300313 800493 849493 7648493 1449493 900533 2200893 73 800e13
  //   4054d4b3 4064d4b3 900533 2200893 73 fffe0e13 fe0e14e3 313 2000e13 493 100913 930023 900533 2200893
  //   73 12484b3 130313 fffe0e13 fe0e12e3 800e13 313 32483 900533 2200893 73 430313 fffe0e13 fe0e14e3
  //   f00493 900533 2200893 73 fff48493 fe04d8e3 a00893 73 413 140413 800533 2200893 73 240413 800533
  //   2200893 73 340413 800533 2200893 73 440413 800533 2200893 73 540413 800533 2200893 73 640413 800533
  //   2200893 73 740413 800533 2200893 73 840413 800533 2200893 2200893 73 8067
  //   指令字
  //   JAL
  //   JALR
  //   URET
  //   SB
  //   B.Inst. Imm
  //   J.Inst. Imm
  //   rd
  //   Beq
  //   Bge
  //   Bne
  //   MemToReg
  //   MemWrite
  //   AluOP
  //   AluSrcB
  //   RegWrite
  //   控制位
  //   流水调试日志用
  //   暂停节拍，不能为0
  //   戳工具置1进入计数暂停模式，ctrl+k时钟自动运行到对应节拍暂停
  //   ctrl+k关闭时钟连续运行，将控制位置零，进入单步调试模式调试
  //   可计数暂停的时钟源
  //   为方便自动评测，需要输出流水线各段保存的PC值，注意是PC不是PC+4，另外ID段寄存器写入信息，Mem段内存写入信息也要输出
  //   SB指令模块
endmodule

module \重定向流水线  (
  output RegWrite,
  output MemWrite,
  output [31:0] IF_PC,
  output [31:0] ID_PC,
  output [31:0] EX_PC,
  output [31:0] M_PC,
  output [31:0] WB_PC,
  output [31:0] RDin,
  output [31:0] MDin,
  output [31:0] LedData
);

  wire alu_1_equal, alu_1_out_4, and_1_out, and_2_out, and_4_out, and_5_out, and_6_out, and_7_out, and_8_out,
       and_9_out, and_10_out, beq, bge, bne, Branch_BT, BranchTaken, CLK, clock_1_out, comparator_1_eq,
       comparator_1_lt, comparator_2_eq, d_ff_1_q, ecall, EX_ecall, EX_halt, EX_J, EX_Jal, EX_Jalr,
       EX_MEM_halt_2, EX_MEM_jal_2, EX_MEM_jalr_2, EX_MEM_memtoreg_2, EX_RegWrite, EX_SB, flush, Go, halt,
       ID_EX_alusrcb_2, ID_EX_memtoreg_2, ID_EX_memwrite_2, IR1, IR2, IR3, JAL, MEM_RegWrite, MEM_SB,
       MEM_str, MEM_WB_halt_2, MEM_WB_jal_2, MEM_WB_jalr_2, nand_1_out, not_1_out, not_2_out, or_1_out,
       or_4_out, RST, S, S_type, SB, stall, W1, W2, W3, \单周期硬布线控制器_1_alu_src , \单周期硬布线控制器_1_beq ,
       \单周期硬布线控制器_1_bge , \单周期硬布线控制器_1_bne , \单周期硬布线控制器_1_jalr , \单周期硬布线控制器_1_memtoreg ,
       \单周期硬布线控制器_1_memwrite , \单周期硬布线控制器_1_regwrite , \单周期硬布线控制器_1_rs1 , \单周期硬布线控制器_1_rs2 ;
  wire [1:0] MEM_WB_memtoreg_2, rs_F, rs_next, rt_F, rt_next;
  wire [3:0] ID_EX_aluop_2, \单周期硬布线控制器_1_alu_op ;
  wire [4:0] EX_MEM_rd_2, ID_EX_rd_2, multiplexer_2_out, multiplexer_3_out, WB_rd;
  wire [11:0] multiplexer_4_out;
  wire [12:0] CNT_num;
  wire [15:0] \LoadUse次数 , \总周期数 , \插入气泡数 , \无条件分支数 , \条件分支成功数 ;
  wire [31:0] ALU_addr, bit_extender_1_out, bit_extender_2_out, bit_extender_3_out, Branch_addr, EX_IR,
       EX_MEM_pc_4_2, EX_PC_4, ID_EX_imm1_2, ID_EX_imm2_2, ID_EX_r1_2, ID_EX_r2_2, ID_IR, ID_PC_4, IF_IR,
       IF_PC_4, MDout, MEM_ALUresult, MEM_Din, MEM_IR, MEM_WB_pc_4_2, MEM_WB_readdata_2, MEM_WB_result_2,
       multiplexer_1_out, multiplexer_5_out, multiplexer_6_out, multiplexer_7_out, multiplexer_8_out,
       regifile_1_r1, regifile_1_r2, SBin, shifter_1_out, WB_IR;

  Button \u_总复位  (.out(RST));
  Button _1 (.out(IR1));
  Button _2 (.out(IR2));
  Button _3 (.out(IR3));
  // Probe on \总周期数 
  // Probe on \总周期数 
  Button \u_继续运行  (.out(Go));
  LED #(.active("true")) led_1 (.in(W1));
  LED #(.active("true")) led_2 (.in(W2));
  LED #(.active("true")) led_3 (.in(W3));
  Multiplexer #(.select(2), .width(32), .disabled("Z"), .enable("false")) multiplexer_1 (
    .in0(IF_PC_4), .in1(ALU_addr), .in2(Branch_addr), .out(multiplexer_1_out), .sel({S, EX_Jalr}));  // open: in3
  and and_1 (and_1_out, ~stall, or_1_out);  // AND_Gate
  or or_1 (or_1_out, ~halt, Go);  // OR_Gate
  Hex_Digit_Display hex_digit_display_1 (.value(LedData[31:28]));  // open: dp
  // Probe on IF_PC[19:0]
  // RiscV_Probe riscv_probe_1: pin names not known; wires that end beside it: IF_IR
  Register #(.width(32), .trigger("rising"), .Select("low")) PC (
    .D(multiplexer_1_out), .en(and_1_out), .Q(IF_PC), .clk(CLK), .clr(RST));
  Hex_Digit_Display hex_digit_display_2 (.value(LedData[27:24]));  // open: dp
  Hex_Digit_Display hex_digit_display_3 (.value(LedData[23:20]));  // open: dp
  // Probe on ID_PC[19:0]
  // RiscV_Probe riscv_probe_2: pin names not known; wires that end beside it: ID_IR
  \重定向处理逻辑  \u_重定向处理逻辑_1  (
    .BranchTaken(BranchTaken), .IR(ID_IR), .ecall(ecall), .rs_av(\单周期硬布线控制器_1_rs1 ),
    .EX_RegWrite(EX_RegWrite), .EX_rd(ID_EX_rd_2), .rt_av(\单周期硬布线控制器_1_rs2 ), .MEM_RegWrite(MEM_RegWrite),
    .MEM_rd(EX_MEM_rd_2), .stall(stall), .flush(flush), .EX_MemToReg(ID_EX_memtoreg_2), .rs1Forward(rs_next),
    .rs2Forward(rt_next));
  or or_2 (EX_J, EX_Jal, EX_Jalr);
  Adder #(.width(32)) adder_1 (.a(IF_PC), .b(32'h4), .out(IF_PC_4));  // open: cin, cout
  Hex_Digit_Display hex_digit_display_4 (.value(LedData[19:16]));  // open: dp
  Hex_Digit_Display hex_digit_display_5 (.value(LedData[15:12]));  // open: dp
  ROM #(.addrWidth(10), .dataWidth(32), .Select("high")) \u_指令存储器  (.addr(IF_PC[11:2]), .data(IF_IR));
  Hex_Digit_Display hex_digit_display_6 (.value(LedData[7:4]));  // open: dp
  Hex_Digit_Display hex_digit_display_7 (.value(LedData[11:8]));  // open: dp
  // Probe on EX_PC[19:0]
  // RiscV_Probe riscv_probe_3: pin names not known; wires that end beside it: EX_IR
  or or_3 (BranchTaken, S, EX_Jalr);
  Hex_Digit_Display hex_digit_display_8 (.value(LedData[3:0]));  // open: dp
  IF_ID IF_ID (
    .IR(IF_IR), .PC(IF_PC), .PC_4(IF_PC_4), .IR_2(ID_IR), .PC_2(ID_PC), .PC_4_2(ID_PC_4), .Reset(RST),
    .BranchTaken(BranchTaken), .En(and_1_out), .CLK(CLK));  // open: PredictJump, PredictJump_2
  // Probe on \总周期数 
  // Probe on M_PC[19:0]
  // RiscV_Probe riscv_probe_4: pin names not known; wires that end beside it: MEM_IR
  // Probe on \总周期数 
  // Probe on \无条件分支数 
  // Probe on \条件分支成功数 
  // Probe on \插入气泡数 
  // Probe on \LoadUse次数 
  \单周期硬布线控制器  \u_单周期硬布线控制器_1  (
    .Funct({ID_IR[30], ID_IR[25], ID_IR[14:12]}), .OP(ID_IR[6:2]), .ALU_OP(\单周期硬布线控制器_1_alu_op ),
    .MemToReg(\单周期硬布线控制器_1_memtoreg ), .MemWrite(\单周期硬布线控制器_1_memwrite ), .ALU_SRC(\单周期硬布线控制器_1_alu_src ),
    .RegWrite(\单周期硬布线控制器_1_regwrite ), .ecall(ecall), .S_type(S_type), .Jalr(\单周期硬布线控制器_1_jalr ),
    .Beq(\单周期硬布线控制器_1_beq ), .JAL(JAL), .Bne(\单周期硬布线控制器_1_bne ), .in_3(ID_IR[21]), .BGE(\单周期硬布线控制器_1_bge ),
    .SB(SB), .rs1(\单周期硬布线控制器_1_rs1 ), .rs2(\单周期硬布线控制器_1_rs2 ));  // open: uret, csrrsi, csrrci
  Multiplexer #(.select(1), .width(5), .disabled("Z"), .enable("false")) multiplexer_2 (
    .in0(ID_IR[19:15]), .in1(5'b10001), .out(multiplexer_2_out), .sel(ecall));
  Multiplexer #(.select(1), .width(5), .disabled("Z"), .enable("false")) multiplexer_3 (
    .in0(ID_IR[24:20]), .in1(5'b01010), .out(multiplexer_3_out), .sel(ecall));
  assign bit_extender_1_out = {{20{multiplexer_4_out[11]}}, multiplexer_4_out};  // Bit_Extender bit_extender_1
  Multiplexer #(.select(1), .width(12), .disabled("Z"), .enable("false")) multiplexer_4 (
    .in0(ID_IR[31:20]), .in1({ID_IR[31:25], ID_IR[11:7]}), .out(multiplexer_4_out), .sel(S_type));
  assign bit_extender_2_out = {{20{ID_IR[31]}}, {ID_IR[31], ID_IR[7], ID_IR[30:25], ID_IR[11:8]}};  // Bit_Extender bit_extender_2
  assign bit_extender_3_out = {{12{ID_IR[31]}}, {ID_IR[31], ID_IR[19:12], ID_IR[20], ID_IR[30:21]}};  // Bit_Extender bit_extender_3
  // Probe on IF_PC[11:0]
  // Probe on WB_PC[19:0]
  // RiscV_Probe riscv_probe_5: pin names not known; wires that end beside it: WB_IR
  Multiplexer #(.select(1), .width(32), .disabled("Z"), .enable("false")) multiplexer_5 (
    .in0(bit_extender_2_out), .in1(bit_extender_3_out), .out(multiplexer_5_out), .sel(JAL));
  or or_4 (or_4_out, ~halt, Go);  // OR_Gate
  // Probe on ID_PC[11:0]
  // Probe on EX_PC[11:0]
  not not_1 (not_1_out, CLK);
  Regifile regifile_1 (
    .Din(RDin), .Clk(not_1_out), .R1(regifile_1_r1), .R2(regifile_1_r2), .WE(RegWrite), .W_num(WB_rd),
    .R1_num(multiplexer_2_out), .R2_num(multiplexer_3_out));
  // Probe on M_PC[11:0]
  D_Flip_Flop #(.trigger("high"), .Pre_Clr_Positions("LEGACY"), .NegatePresetClear("false"), .enable("true"), .NewFFLayout("false")) d_ff_1 (.Q(d_ff_1_q));  // open: clk, D, Qn, preset, en, reset
  // Probe on 13'hc
  // Probe on WB_PC[11:0]
  Comparator #(.width(13), .mode("twosComplement")) comparator_1 (
    .a(CNT_num), .b(13'hc), .eq(comparator_1_eq), .lt(comparator_1_lt));  // open: gt
  Clock #(.highDuration(1), .lowDuration(1)) clock_1 (.out(clock_1_out));
  nand nand_1 (nand_1_out, d_ff_1_q, comparator_1_eq);
  Counter #(.width(13), .max('h1fff), .ongoal("stay"), .trigger("rising"), .behavior("old")) counter_1 (
    .count(comparator_1_lt), .Q(CNT_num), .clk(clock_1_out));  // open: load, D, carry, clr, preset
  ID_EX ID_EX (
    .Beq(\单周期硬布线控制器_1_beq ), .Beq_2(beq), .Bne(\单周期硬布线控制器_1_bne ), .Bne_2(bne), .Bge(\单周期硬布线控制器_1_bge ),
    .Bge_2(bge), .MemToReg(\单周期硬布线控制器_1_memtoreg ), .MemToReg_2(ID_EX_memtoreg_2),
    .MemWrite(\单周期硬布线控制器_1_memwrite ), .MemWrite_2(ID_EX_memwrite_2), .AluSrcB(\单周期硬布线控制器_1_alu_src ),
    .AluSrcB_2(ID_EX_alusrcb_2), .RegWrite_2(EX_RegWrite), .RegWrite(\单周期硬布线控制器_1_regwrite ), .Ecall(ecall),
    .Ecall_2(EX_ecall), .Jal_2(EX_Jal), .Jal(JAL), .Jalr(\单周期硬布线控制器_1_jalr ), .Jalr_2(EX_Jalr), .SB(SB),
    .SB_2(EX_SB), .Reset(RST), .flush(flush), .En(or_4_out), .CLK(CLK), .AluOp(\单周期硬布线控制器_1_alu_op ),
    .AluOp_2(ID_EX_aluop_2), .rd(ID_IR[11:7]), .rd_2(ID_EX_rd_2), .R1(regifile_1_r1), .R1_2(ID_EX_r1_2),
    .R2(regifile_1_r2), .R2_2(ID_EX_r2_2), .imm1(bit_extender_1_out), .imm1_2(ID_EX_imm1_2),
    .imm2(multiplexer_5_out), .imm2_2(ID_EX_imm2_2), .PC(ID_PC), .PC_2(EX_PC), .PC_4(ID_PC_4),
    .PC_4_2(EX_PC_4), .IR(ID_IR), .IR_2(EX_IR), .rs1forward(rs_next), .rs1forward_2(rs_F),
    .rs2forward(rt_next), .rs2forward_2(rt_F));  // open: PredictJump, PredictJump_2, branch, branch_2
  assign CLK = nand_1_out ? clock_1_out : 1'bz;  // Controlled_Buffer controlled_buffer_1
  Multiplexer #(.select(2), .width(32), .disabled("Z"), .enable("false")) multiplexer_6 (
    .in0(ID_EX_r1_2), .in1(RDin), .in2(MEM_ALUresult), .out(multiplexer_6_out), .sel(rs_F));  // open: in3
  Multiplexer #(.select(2), .width(32), .disabled("Z"), .enable("false")) multiplexer_7 (
    .in0(ID_EX_r2_2), .in1(RDin), .in2(MEM_ALUresult), .out(multiplexer_7_out), .sel(rt_F));  // open: in3
  Pull_Resistor #(.pull(1)) pull_resistor_1 (.node(CLK));
  Multiplexer #(.select(1), .width(32), .disabled("Z"), .enable("false")) multiplexer_8 (
    .in0(multiplexer_7_out), .in1(ID_EX_imm1_2), .out(multiplexer_8_out), .sel(ID_EX_alusrcb_2));
  Shifter #(.width(32), .shift("ll")) shifter_1 (.in(ID_EX_imm2_2), .\dist (5'b00001), .out(shifter_1_out));
  Comparator #(.width(32), .mode("unsigned")) comparator_2 (
    .a(multiplexer_6_out), .b(32'ha), .eq(comparator_2_eq));  // open: gt, lt
  and and_2 (and_2_out, EX_ecall, ~comparator_2_eq);  // AND_Gate
  not not_2 (not_2_out, halt);
  ALU alu_1 (
    .X(multiplexer_6_out), .Y(multiplexer_8_out), .AluOP(ID_EX_aluop_2), .Equal(alu_1_equal),
    .Result(ALU_addr), .out_4(alu_1_out_4));  // open: Result_2, out_6
  and and_3 (EX_halt, EX_ecall, comparator_2_eq);
  Register #(.width(32), .trigger("rising"), .Select("low")) register_1 (
    .D(multiplexer_7_out), .en(and_2_out), .Q(LedData), .clk(CLK));  // open: clr
  Counter #(.width(16), .max('hffff), .ongoal("wrap"), .trigger("rising"), .behavior("old")) counter_2 (
    .count(not_2_out), .Q(\总周期数 ), .clk(CLK));  // open: load, D, carry, clr, preset
  and and_4 (and_4_out, alu_1_equal, beq);
  and and_5 (and_5_out, ~alu_1_equal, bne);  // AND_Gate
  and and_6 (and_6_out, alu_1_out_4, bge);
  or or_5 (Branch_BT, and_6_out, and_5_out, and_4_out);
  Adder #(.width(32)) adder_2 (.a(shifter_1_out), .b(EX_PC), .out(Branch_addr));  // open: cin, cout
  and and_7 (and_7_out, not_2_out, EX_J);
  or or_6 (S, Branch_BT, EX_Jal);
  Counter #(.width(16), .max('hffff), .ongoal("wrap"), .trigger("rising"), .behavior("old")) counter_3 (
    .count(and_7_out), .Q(\无条件分支数 ), .clk(CLK));  // open: load, D, carry, clr, preset
  EX_MEM EX_MEM (
    .MemToReg(ID_EX_memtoreg_2), .MemToReg_2(EX_MEM_memtoreg_2), .MemWrite(ID_EX_memwrite_2),
    .MemWrite_2(MemWrite), .RegWrite(EX_RegWrite), .RegWrite_2(MEM_RegWrite), .Jal(EX_Jal),
    .Jal_2(EX_MEM_jal_2), .Jalr(EX_Jalr), .Jalr_2(EX_MEM_jalr_2), .SB(EX_SB), .SB_2(MEM_SB), .rd(ID_EX_rd_2),
    .rd_2(EX_MEM_rd_2), .Reset(RST), .En(or_4_out), .CLK(CLK), .PC(EX_PC), .PC_2(M_PC), .PC_4(EX_PC_4),
    .PC_4_2(EX_MEM_pc_4_2), .IR(EX_IR), .IR_2(MEM_IR), .WriteData(multiplexer_7_out), .WriteData_2(MDin),
    .result(ALU_addr), .result_2(MEM_ALUresult), .halt(EX_halt), .halt_2(EX_MEM_halt_2));
  Multiplexer #(.select(1), .width(32), .disabled("Z"), .enable("false")) multiplexer_9 (
    .in0(MDin), .in1(SBin), .out(MEM_Din), .sel(MEM_SB));
  and and_8 (and_8_out, not_2_out, Branch_BT);
  or or_7 (MEM_str, MemWrite, MEM_SB);
  Counter #(.width(16), .max('hffff), .ongoal("wrap"), .trigger("rising"), .behavior("old")) counter_4 (
    .count(and_8_out), .Q(\条件分支成功数 ), .clk(CLK));  // open: load, D, carry, clr, preset
  RAM #(.addrWidth(10), .dataWidth(32), .bus("separate"), .Select("high")) ram_1 (
    .addr(MEM_ALUresult[11:2]), .din(MEM_Din), .data(MDout), .str(MEM_str), .sel(1'b1), .clk(CLK), .ld(1'b1),
    .clr(RST));
  and and_9 (and_9_out, not_2_out, BranchTaken);
  Counter #(.width(16), .max('hffff), .ongoal("wrap"), .trigger("rising"), .behavior("old")) counter_5 (
    .count(and_9_out), .Q(\插入气泡数 ), .clk(CLK));  // open: load, D, carry, clr, preset
  Counter #(.width(16), .max('hffff), .ongoal("wrap"), .trigger("rising"), .behavior("old")) counter_6 (
    .count(and_10_out), .Q(\LoadUse次数 ), .clk(CLK));  // open: load, D, carry, clr, preset
  and and_10 (and_10_out, not_2_out, stall);
  Multiplexer #(.select(2), .width(32), .disabled("Z"), .enable("false")) multiplexer_10 (
    .in0({MDout[31:8], MDin[7:0]}), .in1({MDout[31:16], MDin[7:0], MDout[7:0]}),
    .in2({MDout[31:24], MDin[7:0], MDout[15:0]}), .in3({MDin[7:0], MDout[23:0]}), .out(SBin),
    .sel(MEM_ALUresult[1:0]));
  MEM_WB MEM_WB (
    .result(MEM_ALUresult), .result_2(MEM_WB_result_2), .MemToReg(EX_MEM_memtoreg_2), .ReadData(MDout),
    .MemToReg_2(MEM_WB_memtoreg_2[0]), .ReadData_2(MEM_WB_readdata_2), .PC(M_PC), .RegWrite(MEM_RegWrite),
    .PC_2(WB_PC), .RegWrite_2(RegWrite), .Jal(EX_MEM_jal_2), .Jal_2(MEM_WB_jal_2), .PC_4(EX_MEM_pc_4_2),
    .Jalr(EX_MEM_jalr_2), .PC_4_2(MEM_WB_pc_4_2), .Jalr_2(MEM_WB_jalr_2), .IR(MEM_IR), .IR_2(WB_IR),
    .rd(EX_MEM_rd_2), .rd_2(WB_rd), .Reset(RST), .En(or_4_out), .CLK(CLK), .halt(EX_MEM_halt_2),
    .halt_2(MEM_WB_halt_2));
  or or_8 (MEM_WB_memtoreg_2[1], MEM_WB_jal_2, MEM_WB_jalr_2);
  Multiplexer #(.select(2), .width(32), .disabled("Z"), .enable("false")) multiplexer_11 (
    .in0(MEM_WB_result_2), .in1(MEM_WB_readdata_2), .in2(MEM_WB_pc_4_2), .out(RDin), .sel(MEM_WB_memtoreg_2));  // open: in3
  D_Flip_Flop #(.trigger("rising"), .Pre_Clr_Positions("ABOVE_BELOW"), .NegatePresetClear("false"), .enable("true"), .NewFFLayout("true")) d_ff_2 (
    .clk(MEM_WB_halt_2), .D(1'b1), .Q(halt), .en(1'b1), .reset(Go));  // open: Qn, preset

  // Other names for the same wires on the sheet: SB_sel[1:0] = MEM_ALUresult[1:0]; MEM_PC[31:0] = M_PC;
  //   WB_RegWrite = RegWrite

  // Notes on the sheet:
  //   中断源
  //   时空图监测，可删除
  //   中断等待指示
  //   数码管输出
  //   contents of 指令存储器 (hex, n*v repeats v):
  //   313 2000e13 493 100913 930023 900533 2200893 73 12484b3 130313 fffe0e13 fe0e12e3 800e13 313 32483
  //   900533 2200893 73 430313 fffe0e13 fe0e14e3 a00893 73
  //   指令字
  //   JAL
  //   JALR
  //   URET
  //   SB
  //   B.Inst. Imm
  //   J.Inst. Imm
  //   rd
  //   Beq
  //   Bge
  //   Bne
  //   MemToReg
  //   MemWrite
  //   AluOP
  //   AluSrcB
  //   RegWrite
  //   控制位
  //   流水调试日志用
  //   暂停节拍，不能为0
  //   戳工具置1进入计数暂停模式，ctrl+k时钟自动运行到对应节拍暂停
  //   ctrl+k关闭时钟连续运行，将控制位置零，进入单步调试模式调试
  //   可计数暂停的时钟源
  //   为方便自动评测，需要输出流水线各段保存的PC值，注意是PC不是PC+4，另外ID段寄存器写入信息，Mem段内存写入信息也要输出
  //   SB指令模块
endmodule

module \中断按键参考电路  (
  input  \同步清零信号 ,
  output \与中断屏蔽位与 
);

  wire \_1号中断_out , and_1_out, clock_1_out, d_ff_1_q, or_1_out, or_2_out;

  Clock #(.highDuration(1), .lowDuration(1)) clock_1 (.out(clock_1_out));
  Button \_1号中断  (.out(\_1号中断_out ));
  or or_1 (or_1_out, \与中断屏蔽位与 , d_ff_1_q);
  LED #(.active("true")) \_1号中断等待指示灯  (.in(or_1_out));
  D_Flip_Flop #(.trigger("rising"), .Pre_Clr_Positions("LEGACY"), .NegatePresetClear("false"), .enable("true"), .NewFFLayout("false")) d_ff_1 (
    .clk(\_1号中断_out ), .D(1'b1), .Q(d_ff_1_q), .reset(\与中断屏蔽位与 ));  // open: Qn, preset, en
  or or_2 (or_2_out, d_ff_1_q, \与中断屏蔽位与 );
  and and_1 (and_1_out, or_2_out, ~\同步清零信号 );  // AND_Gate
  D_Flip_Flop #(.trigger("rising"), .Pre_Clr_Positions("LEGACY"), .NegatePresetClear("false"), .enable("true"), .NewFFLayout("false")) IR1 (
    .clk(clock_1_out), .D(and_1_out), .Q(\与中断屏蔽位与 ));  // open: Qn, preset, en, reset

  // Notes on the sheet:
  //   中断信号采样参考电路
  //   Reset 
endmodule
module \单周期_单级中断  (
  input  IR1,
  input  IR2,
  input  IR3,
  output RegWrite,
  output MemWrite,
  output [31:0] PC,
  output [31:0] IR,
  output [31:0] RDin,
  output [31:0] MDin,
  output [31:0] LedData
);

  wire alu_1_equal, alu_1_out_4, and_1_out, and_2_out, and_3_out, and_4_out, and_5_out, and_9_out,
       and_10_out, and_11_out, B, CLK, clock_1_out, comparator_1_eq, comparator_2_eq, comparator_3_eq,
       comparator_4_eq, comparator_5_eq, comparator_6_eq, comparator_6_lt, d_ff_1_q, d_ff_2_q, d_ff_3_q,
       d_ff_4_q, d_ff_5_q, d_ff_6_q, d_ff_8_q, decoder_1_out1, decoder_1_out2, decoder_1_out3, ecall, Go,
       halt, INT, INT_IE, INT_IR, IR1_t, IR2_t, IR3_t, IRA, IRAreset, IRB, IRBreset, IRC, IRCreset, JAL,
       JALR, MemToReg, nand_1_out, not_1_out, not_3_out, or_4_out, or_5_out, or_6_out, or_7_out, or_11_out,
       or_13_out, pull_resistor_1_node, pull_resistor_2_node, pull_resistor_3_node, register_2_q, RST,
       S_type, SB, undriven, URET, W1, W2, W3, \单周期硬布线控制器_1_alu_src , \单周期硬布线控制器_1_beq , \单周期硬布线控制器_1_bge ,
       \单周期硬布线控制器_1_bne ;
  wire [1:0] priority_encoder_1_out, priority_encoder_2_out, priority_encoder_3_out, register_4_q;
  wire [3:0] \单周期硬布线控制器_1_alu_op ;
  wire [4:0] multiplexer_5_out, multiplexer_6_out;
  wire [11:0] multiplexer_7_out;
  wire [12:0] CNT_num;
  wire [15:0] multiplexer_10_out, \总周期数 ;
  wire [31:0] adder_2_out, adder_3_out, alu_res, B_bias, bit_extender_1_out, bit_extender_2_out,
       bit_extender_3_out, bit_extender_4_out, INT_PC, J_bias, MDout, multiplexer_2_out, multiplexer_3_out,
       multiplexer_8_out, next_PC, PC_1, R1, R2out, ret_PC, SBin;

  Button \u_继续运行  (.out(Go));
  Button _1 (.out(IRA));
  Button _2 ();  // open: out
  Button _3 ();  // open: out
  LED #(.active("true")) led_1 (.in(W1));
  LED #(.active("true")) led_2 (.in(W2));
  LED #(.active("true")) led_3 (.in(W3));
  or or_1 (W1, d_ff_1_q, d_ff_4_q);
  or or_2 (W2, d_ff_2_q, d_ff_5_q);
  or or_3 (W3, d_ff_3_q, d_ff_6_q);
  Hex_Digit_Display hex_digit_display_1 (.value(LedData[31:28]));  // open: dp
  Comparator #(.width(16), .mode("twosComplement")) comparator_1 (
    .a(16'h23b), .b(\总周期数 ), .eq(comparator_1_eq));  // open: gt, lt
  Comparator #(.width(16), .mode("twosComplement")) comparator_2 (
    .a(\总周期数 ), .b(16'h1), .eq(comparator_2_eq));  // open: gt, lt
  Comparator #(.width(16), .mode("twosComplement")) comparator_3 (
    .a(\总周期数 ), .b(16'h4), .eq(comparator_3_eq));  // open: gt, lt
  Comparator #(.width(16), .mode("twosComplement")) comparator_4 (
    .a(\总周期数 ), .b(16'h7), .eq(comparator_4_eq));  // open: gt, lt
  Hex_Digit_Display hex_digit_display_2 (.value(LedData[23:20]));  // open: dp
  Hex_Digit_Display hex_digit_display_3 (.value(LedData[27:24]));  // open: dp
  or or_4 (or_4_out, comparator_1_eq, comparator_2_eq);
  Pull_Resistor #(.pull(0)) pull_resistor_1 (.node(pull_resistor_1_node));
  assign pull_resistor_1_node = or_4_out ? ~CLK : 1'bz;  // Controlled_Inverter controlled_inverter_1
  Pull_Resistor #(.pull(0)) pull_resistor_2 (.node(pull_resistor_2_node));
  assign pull_resistor_2_node = comparator_3_eq ? ~CLK : 1'bz;  // Controlled_Inverter controlled_inverter_2
  Pull_Resistor #(.pull(0)) pull_resistor_3 (.node(pull_resistor_3_node));
  assign pull_resistor_3_node = comparator_4_eq ? ~CLK : 1'bz;  // Controlled_Inverter controlled_inverter_3
  and and_1 (and_1_out, INT_IR, INT_IE);
  Register #(.width(1), .trigger("falling"), .Select("low")) register_1 (
    .D(and_1_out), .Q(INT), .clk(CLK));  // open: en, clr
  Hex_Digit_Display hex_digit_display_4 (.value(LedData[15:12]));  // open: dp
  Hex_Digit_Display hex_digit_display_5 (.value(LedData[19:16]));  // open: dp
  D_Flip_Flop #(.trigger("rising"), .Pre_Clr_Positions("LEGACY"), .NegatePresetClear("false"), .enable("true"), .NewFFLayout("false")) d_ff_1 (
    .clk(IRA), .D(1'b1), .Q(d_ff_1_q), .reset(d_ff_4_q));  // open: Qn, preset, en
  or or_5 (or_5_out, d_ff_1_q, d_ff_4_q);
  D_Flip_Flop #(.trigger("rising"), .Pre_Clr_Positions("LEGACY"), .NegatePresetClear("false"), .enable("true"), .NewFFLayout("false")) d_ff_2 (
    .clk(IRB), .D(1'b1), .Q(d_ff_2_q), .reset(d_ff_5_q));  // open: Qn, preset, en
  or or_6 (or_6_out, d_ff_2_q, d_ff_5_q);
  D_Flip_Flop #(.trigger("rising"), .Pre_Clr_Positions("LEGACY"), .NegatePresetClear("false"), .enable("true"), .NewFFLayout("false")) d_ff_3 (
    .clk(IRC), .D(1'b1), .Q(d_ff_3_q), .reset(d_ff_6_q));  // open: Qn, preset, en
  or or_7 (or_7_out, d_ff_3_q, d_ff_6_q);
  Hex_Digit_Display hex_digit_display_6 (.value(LedData[11:8]));  // open: dp
  Hex_Digit_Display hex_digit_display_7 (.value(LedData[7:4]));  // open: dp
  // Probe on \总周期数 
  Adder #(.width(32)) adder_1 (.a(PC), .b(32'h4), .out(PC_1));  // open: cin, cout
  Adder #(.width(32)) adder_2 (.a(PC), .b(B_bias), .out(adder_2_out));  // open: cin, cout
  Adder #(.width(32)) adder_3 (.a(PC), .b(J_bias), .out(adder_3_out));  // open: cin, cout
  Register #(.width(32), .trigger("rising"), .Select("low")) mEPC (
    .D(next_PC), .en(INT), .Q(ret_PC), .clk(CLK));  // open: clr
  and and_2 (and_2_out, or_5_out, ~IRAreset);  // AND_Gate
  and and_3 (and_3_out, or_6_out, ~IRBreset);  // AND_Gate
  and and_4 (and_4_out, or_7_out, ~IRCreset);  // AND_Gate
  Hex_Digit_Display hex_digit_display_8 (.value(LedData[3:0]));  // open: dp
  Multiplexer #(.select(2), .width(32), .disabled("Z"), .enable("false")) multiplexer_1 (
    .in0(PC_1), .in1(adder_2_out), .in2(adder_3_out), .in3(alu_res), .out(next_PC),
    .sel(priority_encoder_1_out));
  D_Flip_Flop #(.trigger("rising"), .Pre_Clr_Positions("LEGACY"), .NegatePresetClear("false"), .enable("true"), .NewFFLayout("false")) d_ff_4 (
    .clk(CLK), .D(and_2_out), .Q(d_ff_4_q));  // open: Qn, preset, en, reset
  D_Flip_Flop #(.trigger("rising"), .Pre_Clr_Positions("LEGACY"), .NegatePresetClear("false"), .enable("true"), .NewFFLayout("false")) d_ff_5 (
    .clk(CLK), .D(and_3_out), .Q(d_ff_5_q));  // open: Qn, preset, en, reset
  D_Flip_Flop #(.trigger("rising"), .Pre_Clr_Positions("LEGACY"), .NegatePresetClear("false"), .enable("true"), .NewFFLayout("false")) d_ff_6 (
    .clk(CLK), .D(and_4_out), .Q(d_ff_6_q));  // open: Qn, preset, en, reset
  Multiplexer #(.select(1), .width(32), .disabled("Z"), .enable("false")) multiplexer_2 (
    .in0(next_PC), .in1(INT_PC), .out(multiplexer_2_out), .sel(INT));
  Register #(.width(1), .trigger("falling"), .Select("low")) register_2 (
    .D(1'b0), .en(URET), .Q(register_2_q), .clk(CLK), .preset(INT));  // open: clr, cs
  or or_8 (IR1_t, IR1, IRA);
  Priority_Encoder #(.select(2), .disabled("Z")) priority_encoder_1 (
    .in0(1'b1), .in1(B), .in2(JAL), .in3(JALR), .out(priority_encoder_1_out));  // open: gs, en_out, en_in
  Multiplexer #(.select(1), .width(32), .disabled("Z"), .enable("false")) multiplexer_3 (
    .in0(multiplexer_2_out), .in1(ret_PC), .out(multiplexer_3_out), .sel(URET));
  not not_1 (not_1_out, halt);
  not not_2 (INT_IE, register_2_q);
  Priority_Encoder #(.select(2), .disabled("Z")) priority_encoder_2 (
    .in0(1'b0), .in1(d_ff_4_q), .in2(d_ff_5_q), .in3(d_ff_6_q), .out(priority_encoder_2_out), .gs(INT_IR));  // open: en_out, en_in
  or or_9 (IR2_t, IR2, IRB);
  Counter #(.width(16), .max('hffff), .ongoal("wrap"), .trigger("rising"), .behavior("new")) counter_1 (
    .count(not_3_out), .Q(\总周期数 ), .clk(CLK));  // open: load, D, carry, clr, preset, down
  not not_3 (not_3_out, halt);
  Register #(.width(32), .trigger("rising"), .Select("low")) u_PC (
    .D(multiplexer_3_out), .en(not_1_out), .Q(PC), .clk(CLK), .clr(RST));
  Comparator #(.width(32), .mode("unsigned")) comparator_5 (.a(R1), .b(32'ha), .eq(comparator_5_eq));  // open: gt, lt
  // RiscV_Probe riscv_probe_1: pin names not known; wires that end beside it: halt, PC[11:2], IR
  D_Flip_Flop #(.trigger("rising"), .Pre_Clr_Positions("ABOVE_BELOW"), .NegatePresetClear("false"), .enable("true"), .NewFFLayout("true")) d_ff_7 (
    .clk(comparator_5_eq), .Q(halt), .en(ecall), .reset(Go));  // open: D, Qn, preset
  Register #(.width(32), .trigger("rising"), .Select("low")) register_3 (
    .D(MDin), .en(and_5_out), .Q(LedData), .clk(CLK));  // open: clr
  and and_5 (and_5_out, ~comparator_5_eq, ecall);  // AND_Gate
  Multiplexer #(.select(2), .width(32), .disabled("Z"), .enable("false")) multiplexer_4 (
    .in1(32'h30ac), .in2(32'h3150), .in3(32'h31f4), .out(INT_PC), .sel(priority_encoder_2_out));  // open: in0
  or or_10 (IR3_t, IR3, IRC);
  ROM #(.addrWidth(10), .dataWidth(32), .Select("high")) rom_1 (.addr(PC[11:2]), .data(IR));
  Register #(.width(2), .trigger("rising"), .Select("low")) register_4 (
    .D(priority_encoder_2_out), .Q(register_4_q), .clk(INT));  // open: en, clr
  Decoder #(.select(2), .tristate("false"), .disabled("Z"), .enable("false")) decoder_1 (
    .out1(decoder_1_out1), .out2(decoder_1_out2), .out3(decoder_1_out3), .sel(register_4_q));  // open: out0
  \单周期硬布线控制器  \u_单周期硬布线控制器_1  (
    .Funct({IR[30], IR[25], IR[14:12]}), .OP(IR[6:2]), .ALU_OP(\单周期硬布线控制器_1_alu_op ), .MemToReg(MemToReg),
    .MemWrite(MemWrite), .ALU_SRC(\单周期硬布线控制器_1_alu_src ), .RegWrite(RegWrite), .ecall(ecall),
    .S_type(S_type), .Jalr(JALR), .Beq(\单周期硬布线控制器_1_beq ), .JAL(JAL), .Bne(\单周期硬布线控制器_1_bne ), .in_3(IR[21]),
    .uret(URET), .BGE(\单周期硬布线控制器_1_bge ), .SB(SB));  // open: rs1, rs2, csrrsi, csrrci
  Multiplexer #(.select(1), .width(5), .disabled("Z"), .enable("false")) multiplexer_5 (
    .in0(IR[19:15]), .in1(5'b10001), .out(multiplexer_5_out), .sel(ecall));
  Multiplexer #(.select(1), .width(5), .disabled("Z"), .enable("false")) multiplexer_6 (
    .in0(IR[24:20]), .in1(5'b01010), .out(multiplexer_6_out), .sel(ecall));
  Multiplexer #(.select(1), .width(12), .disabled("Z"), .enable("false")) multiplexer_7 (
    .in0(IR[31:20]), .in1({IR[31:25], IR[11:7]}), .out(multiplexer_7_out), .sel(S_type));
  and and_6 (IRAreset, decoder_1_out1, URET);
  and and_7 (IRBreset, decoder_1_out2, URET);
  and and_8 (IRCreset, decoder_1_out3, URET);
  assign bit_extender_1_out = {{20{multiplexer_7_out[11]}}, multiplexer_7_out};  // Bit_Extender bit_extender_1
  assign bit_extender_2_out = {{20{IR[31]}}, {IR[31], IR[7], IR[30:25], IR[11:8]}};  // Bit_Extender bit_extender_2
  assign bit_extender_3_out = {{12{IR[31]}}, {IR[31], IR[19:12], IR[20], IR[30:21]}};  // Bit_Extender bit_extender_3
  Regifile regifile_1 (
    .Din(RDin), .Clk(CLK), .R1(R1), .R2(R2out), .WE(RegWrite), .W_num(IR[11:7]), .R1_num(multiplexer_5_out),
    .R2_num(multiplexer_6_out));
  Shifter #(.width(32), .shift("ll")) shifter_1 (.in(bit_extender_2_out), .\dist (5'b00001), .out(B_bias));
  Shifter #(.width(32), .shift("ll")) shifter_2 (.in(bit_extender_3_out), .\dist (5'b00001), .out(J_bias));
  Multiplexer #(.select(1), .width(32), .disabled("Z"), .enable("false")) multiplexer_8 (
    .in0(R2out), .in1(bit_extender_1_out), .out(multiplexer_8_out), .sel(\单周期硬布线控制器_1_alu_src ));
  // Probe on undriven
  ALU alu_1 (
    .X(R1), .Y(multiplexer_8_out), .AluOP(\单周期硬布线控制器_1_alu_op ), .Equal(alu_1_equal), .Result(alu_res),
    .out_4(alu_1_out_4));  // open: Result_2, out_6
  Multiplexer #(.select(1), .width(32), .disabled("Z"), .enable("false")) multiplexer_9 (
    .in0(R2out), .in1(SBin), .out(MDin), .sel(SB));
  D_Flip_Flop #(.trigger("high"), .Pre_Clr_Positions("LEGACY"), .NegatePresetClear("false"), .enable("true"), .NewFFLayout("false")) d_ff_8 (.Q(d_ff_8_q));  // open: clk, D, Qn, preset, en, reset
  // Probe on 13'hbb
  or or_11 (or_11_out, MemWrite, SB);
  Comparator #(.width(13), .mode("twosComplement")) comparator_6 (
    .a(CNT_num), .b(13'hbb), .eq(comparator_6_eq), .lt(comparator_6_lt));  // open: gt
  Clock #(.highDuration(1), .lowDuration(1)) clock_1 (.out(clock_1_out));
  Counter #(.width(13), .max('h1fff), .ongoal("stay"), .trigger("rising"), .behavior("old")) counter_2 (
    .count(comparator_6_lt), .Q(CNT_num), .clk(clock_1_out));  // open: load, D, carry, clr, preset
  and and_9 (and_9_out, \单周期硬布线控制器_1_beq , alu_1_equal);
  and and_10 (and_10_out, \单周期硬布线控制器_1_bne , ~alu_1_equal);  // AND_Gate
  and and_11 (and_11_out, \单周期硬布线控制器_1_bge , alu_1_out_4);
  RAM #(.addrWidth(10), .dataWidth(32), .bus("separate"), .Select("high")) ram_1 (
    .addr(alu_res[11:2]), .din(MDin), .data(MDout), .str(or_11_out), .sel(1'b1), .clk(CLK), .ld(1'b1),
    .clr(RST));
  nand nand_1 (nand_1_out, d_ff_8_q, comparator_6_eq);
  or or_12 (B, and_9_out, and_10_out, and_11_out);
  Multiplexer #(.select(1), .width(16), .disabled("Z"), .enable("false")) multiplexer_10 (
    .in0(MDout[15:0]), .in1(MDout[31:16]), .out(multiplexer_10_out), .sel(alu_res[1]));
  Multiplexer #(.select(2), .width(32), .disabled("Z"), .enable("false")) multiplexer_11 (
    .in0({MDout[31:8], R2out[7:0]}), .in1({MDout[31:16], R2out[7:0], MDout[7:0]}),
    .in2({MDout[31:24], R2out[7:0], MDout[15:0]}), .in3({R2out[7:0], MDout[23:0]}), .out(SBin),
    .sel(alu_res[1:0]));
  assign CLK = nand_1_out ? clock_1_out : 1'bz;  // Controlled_Buffer controlled_buffer_1
  Pull_Resistor #(.pull(1)) pull_resistor_4 (.node(CLK));
  or or_13 (or_13_out, JAL, JALR);
  Priority_Encoder #(.select(2), .disabled("Z")) priority_encoder_3 (
    .in0(1'b1), .in1(MemToReg), .in3(or_13_out), .out(priority_encoder_3_out));  // open: in2, gs, en_out, en_in
  Multiplexer #(.select(2), .width(32), .disabled("Z"), .enable("false")) multiplexer_12 (
    .in0(alu_res), .in1(MDout), .in2(bit_extender_4_out), .in3(PC_1), .out(RDin), .sel(priority_encoder_3_out));
  assign bit_extender_4_out = {{16{1'b0}}, multiplexer_10_out};  // Bit_Extender bit_extender_4

  // Other names for the same wires on the sheet: sel[1:0] = alu_res[1:0]

  // Notes on the sheet:
  //   中断源
  //   中断等待指示
  //   总复位信号应将除ROM以外所有存储组件全部清零
  //   单级中断测试信号模拟器
  //   数码管输出
  //   数码管输出应该用寄存器锁存，否则显示数据只能一闪而过
  //   LED显示模块
  //   指令探针
  //   指令存储器
  //   指令字
  //   contents of rom_1 (hex, n*v repeats v):
  //   7d000113 100413 1f41993 41f9d993 433 c00913 800b13 140413 f47413 800293 100313 499993 89e9b3 1300533
  //   2200893 73 406282b3 fe0294e3 140413 f00f93 1f47433 1c41413 800293 100313 49d993 89e9b3 1300533
  //   2200893 73 406282b3 fe0294e3 1c45413 406b0b33 b0463 f95ff06f 2b3 fff2c293 1029293 fff2e293 500533
  //   2200893 73 f5dff06f 1112023 410113 a12023 410113 812023 410113 1312023 410113 1412023 410113 1512023
  //   410113 1612023 410113 100b13 300a13 100a93 1600433 441413 14469b3 1300533 2200893 73 fe0416e3
  //   415a0a33 fe0a10e3 ffc10113 12b03 ffc10113 12a83 ffc10113 12a03 ffc10113 12983 ffc10113 12403
  //   ffc10113 12503 ffc10113 12883 200073 1112023 410113 a12023 410113 812023 410113 1312023 410113
  //   1412023 410113 1512023 410113 1612023 410113 200b13 300a13 100a93 1600433 441413 14469b3 1300533
  //   2200893 73 fe0416e3 415a0a33 fe0a10e3 ffc10113 12b03 ffc10113 12a83 ffc10113 12a03 ffc10113 12983
  //   ffc10113 12403 ffc10113 12503 ffc10113 12883 200073 1112023 410113 a12023 410113 812023 410113
  //   1312023 410113 1412023 410113 1512023 410113 1612023 410113 300b13 300a13 100a93 1600433 441413
  //   14469b3 1300533 2200893 73 fe0416e3 415a0a33 fe0a10e3 ffc10113 12b03 ffc10113 12a83 ffc10113 12a03
  //   ffc10113 12983 ffc10113 12403 ffc10113 12503 ffc10113 12883 200073
  //   JAL
  //   JALR
  //   URET
  //   SB
  //   B.Inst. Imm
  //   J.Inst. Imm
  //   Beq
  //   Bge
  //   Bne
  //   MemToReg
  //   MemWrite
  //   AluOP
  //   AluSrcB
  //   RegWrite
  //   为方便自动评测，需要输出PC，IR，寄存器堆写如数据RDin
  //   RAM写使能MemWrite、RAM写入数据MDin等信号
  //   控制位
  //   暂停节拍，不能为0
  //   SB指令模块
  //   戳工具置1进入计数暂停模式，ctrl+k时钟自动运行到对应节拍暂停
  //   ctrl+k关闭时钟连续运行，将控制位置零，进入单步调试模式调试
  //   数据存储器
  //   可计数暂停的时钟源
endmodule

module \单周期_多级中断  (
  input  IR1,
  input  IR2,
  input  IR3,
  output RegWrite,
  output MemWrite,
  output [31:0] PC,
  output [31:0] IR,
  output [31:0] RDin,
  output [31:0] MDin,
  output [31:0] LedData
);

  wire alu_1_equal, alu_1_out_4, and_1_out, and_2_out, and_3_out, and_4_out, and_5_out, and_6_out, and_7_out,
       and_8_out, and_12_out, and_13_out, and_14_out, B, CLK, clock_1_out, comparator_1_eq, comparator_2_eq,
       comparator_3_eq, comparator_4_eq, comparator_5_eq, comparator_6_eq, comparator_8_eq, comparator_8_lt,
       csrrci, csrrsi, d_ff_1_q, d_ff_2_q, d_ff_3_q, d_ff_4_q, d_ff_5_q, d_ff_6_q, d_ff_8_q, decoder_1_out1,
       decoder_1_out2, decoder_1_out3, decoder_2_out0, decoder_2_out1, decoder_2_out2, decoder_3_out1,
       decoder_3_out2, decoder_3_out3, ecall, Go, halt, INT, INT_IE, INT_Response, IR1_t, IR2_t, IR3_t, IRA,
       IRAreset, IRB, IRBreset, IRC, IRCreset, JAL, JALR, MemToReg, nand_1_out, not_2_out, not_3_out,
       or_4_out, or_5_out, or_6_out, or_7_out, or_8_out, or_9_out, or_10_out, or_14_out, or_15_out,
       or_17_out, pull_resistor_1_node, pull_resistor_2_node, pull_resistor_3_node, register_2_q, RST,
       S_type, SB, URET, W1, W2, W3, \单周期硬布线控制器_1_alu_src , \单周期硬布线控制器_1_beq , \单周期硬布线控制器_1_bge ,
       \单周期硬布线控制器_1_bne ;
  wire [1:0] counter_2_q, multiplexer_9_out, priority_encoder_1_out, priority_encoder_2_out,
       priority_encoder_3_out, register_4_q, register_5_q, register_6_q, subtractor_1_out;
  wire [3:0] \单周期硬布线控制器_1_alu_op ;
  wire [4:0] multiplexer_6_out, multiplexer_7_out;
  wire [11:0] multiplexer_8_out;
  wire [12:0] CNT_num;
  wire [15:0] multiplexer_12_out, \总周期数 ;
  wire [31:0] adder_2_out, adder_3_out, alu_res, B_bias, bit_extender_1_out, bit_extender_2_out,
       bit_extender_3_out, bit_extender_4_out, INT_PC, J_bias, MDout, multiplexer_2_out, multiplexer_3_out,
       multiplexer_10_out, next_PC, PC_1, R1, R2out, ret_PC, RET_PC_0, RET_PC_1, RET_PC_2, SBin;

  Button \u_继续运行  (.out(Go));
  Button _1 (.out(IRA));
  Button _2 (.out(IRB));
  Button _3 (.out(IRC));
  LED #(.active("true")) led_1 (.in(W1));
  LED #(.active("true")) led_2 (.in(W2));
  LED #(.active("true")) led_3 (.in(W3));
  Hex_Digit_Display hex_digit_display_1 (.value(LedData[31:28]));  // open: dp
  Comparator #(.width(16), .mode("twosComplement")) comparator_1 (
    .a(\总周期数 ), .b(16'h7), .eq(comparator_1_eq));  // open: gt, lt
  Comparator #(.width(16), .mode("twosComplement")) comparator_2 (
    .a(\总周期数 ), .b(16'h241), .eq(comparator_2_eq));  // open: gt, lt
  and and_1 (and_1_out, INT_Response, INT_IE);
  or or_1 (W1, d_ff_1_q, d_ff_4_q);
  or or_2 (W2, d_ff_2_q, d_ff_5_q);
  or or_3 (W3, d_ff_3_q, d_ff_6_q);
  Hex_Digit_Display hex_digit_display_2 (.value(LedData[27:24]));  // open: dp
  Hex_Digit_Display hex_digit_display_3 (.value(LedData[23:20]));  // open: dp
  Comparator #(.width(16), .mode("twosComplement")) comparator_3 (
    .a(16'h258), .b(\总周期数 ), .eq(comparator_3_eq));  // open: gt, lt
  or or_4 (or_4_out, comparator_3_eq, comparator_4_eq);
  Comparator #(.width(16), .mode("twosComplement")) comparator_4 (
    .a(\总周期数 ), .b(16'h1), .eq(comparator_4_eq));  // open: gt, lt
  Comparator #(.width(16), .mode("twosComplement")) comparator_5 (
    .a(\总周期数 ), .b(16'h4), .eq(comparator_5_eq));  // open: gt, lt
  or or_5 (or_5_out, comparator_1_eq, comparator_2_eq);
  Register #(.width(1), .trigger("falling"), .Select("low")) register_1 (
    .D(and_1_out), .Q(INT), .clk(CLK));  // open: en, clr
  Hex_Digit_Display hex_digit_display_4 (.value(LedData[15:12]));  // open: dp
  Hex_Digit_Display hex_digit_display_5 (.value(LedData[19:16]));  // open: dp
  Pull_Resistor #(.pull(0)) pull_resistor_1 (.node(pull_resistor_1_node));
  assign pull_resistor_1_node = or_4_out ? ~CLK : 1'bz;  // Controlled_Inverter controlled_inverter_1
  Pull_Resistor #(.pull(0)) pull_resistor_2 (.node(pull_resistor_2_node));
  assign pull_resistor_2_node = comparator_5_eq ? ~CLK : 1'bz;  // Controlled_Inverter controlled_inverter_2
  Pull_Resistor #(.pull(0)) pull_resistor_3 (.node(pull_resistor_3_node));
  assign pull_resistor_3_node = or_5_out ? ~CLK : 1'bz;  // Controlled_Inverter controlled_inverter_3
  D_Flip_Flop #(.trigger("rising"), .Pre_Clr_Positions("LEGACY"), .NegatePresetClear("false"), .enable("true"), .NewFFLayout("false")) d_ff_1 (
    .clk(IRA), .D(1'b1), .Q(d_ff_1_q), .reset(d_ff_4_q));  // open: Qn, preset, en
  D_Flip_Flop #(.trigger("rising"), .Pre_Clr_Positions("LEGACY"), .NegatePresetClear("false"), .enable("true"), .NewFFLayout("false")) d_ff_2 (
    .clk(IRB), .D(1'b1), .Q(d_ff_2_q), .reset(d_ff_5_q));  // open: Qn, preset, en
  D_Flip_Flop #(.trigger("rising"), .Pre_Clr_Positions("LEGACY"), .NegatePresetClear("false"), .enable("true"), .NewFFLayout("false")) d_ff_3 (
    .clk(IRC), .D(1'b1), .Q(d_ff_3_q), .reset(d_ff_6_q));  // open: Qn, preset, en
  Hex_Digit_Display hex_digit_display_6 (.value(LedData[11:8]));  // open: dp
  Hex_Digit_Display hex_digit_display_7 (.value(LedData[7:4]));  // open: dp
  // Probe on \总周期数 
  or or_6 (or_6_out, INT, csrrci);
  or or_7 (or_7_out, URET, csrrsi);
  or or_8 (or_8_out, d_ff_1_q, d_ff_4_q);
  or or_9 (or_9_out, d_ff_2_q, d_ff_5_q);
  or or_10 (or_10_out, d_ff_3_q, d_ff_6_q);
  Hex_Digit_Display hex_digit_display_8 (.value(LedData[3:0]));  // open: dp
  and and_2 (and_2_out, or_8_out, ~IRAreset);  // AND_Gate
  and and_3 (and_3_out, or_9_out, ~IRBreset);  // AND_Gate
  and and_4 (and_4_out, or_10_out, ~IRCreset);  // AND_Gate
  Adder #(.width(32)) adder_1 (.a(PC), .b(32'h4), .out(PC_1));  // open: cin, cout
  Adder #(.width(32)) adder_2 (.a(PC), .b(B_bias), .out(adder_2_out));  // open: cin, cout
  Multiplexer #(.select(2), .width(32), .disabled("Z"), .enable("false")) multiplexer_1 (
    .in0(PC_1), .in1(adder_2_out), .in2(adder_3_out), .in3(alu_res), .out(next_PC),
    .sel(priority_encoder_2_out));
  Adder #(.width(32)) adder_3 (.a(PC), .b(J_bias), .out(adder_3_out));  // open: cin, cout
  not not_1 (INT_IE, register_2_q);
  Register #(.width(1), .trigger("falling"), .Select("low")) register_2 (
    .D(1'b0), .en(or_7_out), .Q(register_2_q), .clk(CLK), .preset(or_6_out));  // open: clr, cs
  D_Flip_Flop #(.trigger("rising"), .Pre_Clr_Positions("LEGACY"), .NegatePresetClear("false"), .enable("true"), .NewFFLayout("false")) d_ff_4 (
    .clk(CLK), .D(and_2_out), .Q(d_ff_4_q));  // open: Qn, preset, en, reset
  D_Flip_Flop #(.trigger("rising"), .Pre_Clr_Positions("LEGACY"), .NegatePresetClear("false"), .enable("true"), .NewFFLayout("false")) d_ff_5 (
    .clk(CLK), .D(and_3_out), .Q(d_ff_5_q));  // open: Qn, preset, en, reset
  D_Flip_Flop #(.trigger("rising"), .Pre_Clr_Positions("LEGACY"), .NegatePresetClear("false"), .enable("true"), .NewFFLayout("false")) d_ff_6 (
    .clk(CLK), .D(and_4_out), .Q(d_ff_6_q));  // open: Qn, preset, en, reset
  or or_11 (IR1_t, IR1, IRA);
  Priority_Encoder #(.select(2), .disabled("Z")) priority_encoder_1 (
    .in0(1'b1), .in1(d_ff_4_q), .in2(d_ff_5_q), .in3(d_ff_6_q), .out(priority_encoder_1_out));  // open: gs, en_out, en_in
  Decoder #(.select(2), .tristate("false"), .disabled("Z"), .enable("false")) decoder_1 (
    .out1(decoder_1_out1), .out2(decoder_1_out2), .out3(decoder_1_out3), .sel(priority_encoder_1_out));  // open: out0
  or or_12 (IR2_t, IR2, IRB);
  Priority_Encoder #(.select(2), .disabled("Z")) priority_encoder_2 (
    .in0(1'b1), .in1(B), .in2(JAL), .in3(JALR), .out(priority_encoder_2_out));  // open: gs, en_out, en_in
  Multiplexer #(.select(1), .width(32), .disabled("Z"), .enable("false")) multiplexer_2 (
    .in0(next_PC), .in1(INT_PC), .out(multiplexer_2_out), .sel(INT));
  Multiplexer #(.select(1), .width(32), .disabled("Z"), .enable("false")) multiplexer_3 (
    .in0(multiplexer_2_out), .in1(ret_PC), .out(multiplexer_3_out), .sel(URET));
  and and_5 (and_5_out, INT, decoder_1_out1);
  and and_6 (and_6_out, INT, decoder_1_out2);
  and and_7 (and_7_out, INT, decoder_1_out3);
  not not_2 (not_2_out, halt);
  Register #(.width(32), .trigger("rising"), .Select("low")) u_PC (
    .D(multiplexer_3_out), .en(not_3_out), .Q(PC), .clk(CLK), .clr(RST));
  not not_3 (not_3_out, halt);
  Comparator #(.width(32), .mode("unsigned")) comparator_6 (.a(R1), .b(32'ha), .eq(comparator_6_eq));  // open: gt, lt
  Multiplexer #(.select(2), .width(32), .disabled("Z"), .enable("false")) multiplexer_4 (
    .in1(32'h30ac), .in2(32'h3158), .in3(32'h3204), .out(INT_PC), .sel(priority_encoder_1_out));  // open: in0
  Register #(.width(32), .trigger("rising"), .Select("low")) mEPC0 (
    .D(next_PC), .en(and_5_out), .Q(RET_PC_0), .clk(CLK));  // open: clr
  Register #(.width(32), .trigger("rising"), .Select("low")) mEPC1 (
    .D(next_PC), .en(and_6_out), .Q(RET_PC_1), .clk(CLK));  // open: clr
  Register #(.width(32), .trigger("rising"), .Select("low")) mEPC2 (
    .D(next_PC), .en(and_7_out), .Q(RET_PC_2), .clk(CLK));  // open: clr
  or or_13 (IR3_t, IR3, IRC);
  Counter #(.width(16), .max('hffff), .ongoal("wrap"), .trigger("rising"), .behavior("new")) counter_1 (
    .count(not_2_out), .Q(\总周期数 ), .clk(CLK));  // open: load, D, carry, clr, preset, down
  and and_8 (and_8_out, ~comparator_6_eq, ecall);  // AND_Gate
  // RiscV_Probe riscv_probe_1: pin names not known; wires that end beside it: halt, PC[11:2], IR
  ROM #(.addrWidth(10), .dataWidth(32), .Select("high")) rom_1 (.addr(PC[11:2]), .data(IR));
  D_Flip_Flop #(.trigger("rising"), .Pre_Clr_Positions("ABOVE_BELOW"), .NegatePresetClear("false"), .enable("true"), .NewFFLayout("true")) d_ff_7 (
    .clk(comparator_6_eq), .Q(halt), .en(ecall), .reset(Go));  // open: D, Qn, preset
  Register #(.width(32), .trigger("rising"), .Select("low")) register_3 (
    .D(MDin), .en(and_8_out), .Q(LedData), .clk(CLK));  // open: clr
  Multiplexer #(.select(2), .width(32), .disabled("Z"), .enable("false")) multiplexer_5 (
    .in1(RET_PC_0), .in2(RET_PC_1), .in3(RET_PC_2), .out(ret_PC), .sel(priority_encoder_1_out));  // open: in0
  or or_14 (or_14_out, INT, URET);
  \单周期硬布线控制器  \u_单周期硬布线控制器_1  (
    .Funct({IR[30], IR[25], IR[14:12]}), .OP(IR[6:2]), .ALU_OP(\单周期硬布线控制器_1_alu_op ), .MemToReg(MemToReg),
    .MemWrite(MemWrite), .ALU_SRC(\单周期硬布线控制器_1_alu_src ), .RegWrite(RegWrite), .ecall(ecall),
    .S_type(S_type), .Jalr(JALR), .Beq(\单周期硬布线控制器_1_beq ), .JAL(JAL), .Bne(\单周期硬布线控制器_1_bne ), .in_3(IR[21]),
    .uret(URET), .BGE(\单周期硬布线控制器_1_bge ), .SB(SB), .csrrsi(csrrsi), .csrrci(csrrci));  // open: rs1, rs2
  Multiplexer #(.select(1), .width(5), .disabled("Z"), .enable("false")) multiplexer_6 (
    .in0(IR[19:15]), .in1(5'b10001), .out(multiplexer_6_out), .sel(ecall));
  Multiplexer #(.select(1), .width(5), .disabled("Z"), .enable("false")) multiplexer_7 (
    .in0(IR[24:20]), .in1(5'b01010), .out(multiplexer_7_out), .sel(ecall));
  Multiplexer #(.select(1), .width(12), .disabled("Z"), .enable("false")) multiplexer_8 (
    .in0(IR[31:20]), .in1({IR[31:25], IR[11:7]}), .out(multiplexer_8_out), .sel(S_type));
  // Probe on priority_encoder_1_out
  Decoder #(.select(2), .tristate("false"), .disabled("Z"), .enable("false")) decoder_2 (
    .out0(decoder_2_out0), .out1(decoder_2_out1), .out2(decoder_2_out2), .sel(counter_2_q));  // open: out3
  Counter #(.width(2), .max('h3), .ongoal("wrap"), .trigger("rising"), .behavior("new")) counter_2 (
    .count(or_14_out), .Q(counter_2_q), .clk(CLK), .down(URET));  // open: load, D, carry, clr, preset
  assign bit_extender_1_out = {{20{multiplexer_8_out[11]}}, multiplexer_8_out};  // Bit_Extender bit_extender_1
  assign bit_extender_2_out = {{20{IR[31]}}, {IR[31], IR[7], IR[30:25], IR[11:8]}};  // Bit_Extender bit_extender_2
  assign bit_extender_3_out = {{12{IR[31]}}, {IR[31], IR[19:12], IR[20], IR[30:21]}};  // Bit_Extender bit_extender_3
  // Probe on nothing
  Shifter #(.width(32), .shift("ll")) shifter_1 (.in(bit_extender_2_out), .\dist (5'b00001), .out(B_bias));
  Shifter #(.width(32), .shift("ll")) shifter_2 (.in(bit_extender_3_out), .\dist (5'b00001), .out(J_bias));
  Register #(.width(2), .trigger("rising"), .Select("low")) register_4 (
    .D(priority_encoder_1_out), .en(decoder_2_out0), .Q(register_4_q), .clk(CLK));  // open: clr
  Register #(.width(2), .trigger("rising"), .Select("low")) register_5 (
    .D(priority_encoder_1_out), .en(decoder_2_out1), .Q(register_5_q), .clk(CLK));  // open: clr
  Register #(.width(2), .trigger("rising"), .Select("low")) register_6 (
    .D(priority_encoder_1_out), .en(decoder_2_out2), .Q(register_6_q), .clk(CLK));  // open: clr
  Subtractor #(.width(2)) subtractor_1 (.a(counter_2_q), .b(2'b01), .out(subtractor_1_out));  // open: bin, bout
  Regifile regifile_1 (
    .Din(RDin), .Clk(CLK), .R1(R1), .R2(R2out), .WE(RegWrite), .W_num(IR[11:7]), .R1_num(multiplexer_6_out),
    .R2_num(multiplexer_7_out));
  Comparator #(.width(2), .mode("unsigned")) comparator_7 (
    .a(priority_encoder_1_out), .b(multiplexer_9_out), .gt(INT_Response));  // open: eq, lt
  Multiplexer #(.select(2), .width(2), .disabled("Z"), .enable("false")) multiplexer_9 (
    .in0(register_4_q), .in1(register_5_q), .in2(register_6_q), .in3(2'b00), .out(multiplexer_9_out),
    .sel(subtractor_1_out));
  D_Flip_Flop #(.trigger("high"), .Pre_Clr_Positions("LEGACY"), .NegatePresetClear("false"), .enable("true"), .NewFFLayout("false")) d_ff_8 (.Q(d_ff_8_q));  // open: clk, D, Qn, preset, en, reset
  // Probe on 13'hc
  Multiplexer #(.select(1), .width(32), .disabled("Z"), .enable("false")) multiplexer_10 (
    .in0(R2out), .in1(bit_extender_1_out), .out(multiplexer_10_out), .sel(\单周期硬布线控制器_1_alu_src ));
  Multiplexer #(.select(1), .width(32), .disabled("Z"), .enable("false")) multiplexer_11 (
    .in0(R2out), .in1(SBin), .out(MDin), .sel(SB));
  Decoder #(.select(2), .tristate("false"), .disabled("Z"), .enable("false")) decoder_3 (
    .out1(decoder_3_out1), .out2(decoder_3_out2), .out3(decoder_3_out3), .sel(multiplexer_9_out));  // open: out0
  and and_9 (IRAreset, decoder_3_out1, URET);
  Comparator #(.width(13), .mode("twosComplement")) comparator_8 (
    .a(CNT_num), .b(13'hc), .eq(comparator_8_eq), .lt(comparator_8_lt));  // open: gt
  Clock #(.highDuration(1), .lowDuration(1)) clock_1 (.out(clock_1_out));
  ALU alu_1 (
    .X(R1), .Y(multiplexer_10_out), .AluOP(\单周期硬布线控制器_1_alu_op ), .Equal(alu_1_equal), .Result(alu_res),
    .out_4(alu_1_out_4));  // open: Result_2, out_6
  and and_10 (IRBreset, decoder_3_out2, URET);
  and and_11 (IRCreset, decoder_3_out3, URET);
  Counter #(.width(13), .max('h1fff), .ongoal("stay"), .trigger("rising"), .behavior("old")) counter_3 (
    .count(comparator_8_lt), .Q(CNT_num), .clk(clock_1_out));  // open: load, D, carry, clr, preset
  or or_15 (or_15_out, MemWrite, SB);
  nand nand_1 (nand_1_out, d_ff_8_q, comparator_8_eq);
  and and_12 (and_12_out, \单周期硬布线控制器_1_beq , alu_1_equal);
  and and_13 (and_13_out, \单周期硬布线控制器_1_bne , ~alu_1_equal);  // AND_Gate
  and and_14 (and_14_out, \单周期硬布线控制器_1_bge , alu_1_out_4);
  RAM #(.addrWidth(10), .dataWidth(32), .bus("separate"), .Select("high")) ram_1 (
    .addr(alu_res[11:2]), .din(MDin), .data(MDout), .str(or_15_out), .sel(1'b1), .clk(CLK), .ld(1'b1),
    .clr(RST));
  assign CLK = nand_1_out ? clock_1_out : 1'bz;  // Controlled_Buffer controlled_buffer_1
  Pull_Resistor #(.pull(1)) pull_resistor_4 (.node(CLK));
  or or_16 (B, and_12_out, and_13_out, and_14_out);
  Multiplexer #(.select(1), .width(16), .disabled("Z"), .enable("false")) multiplexer_12 (
    .in0(MDout[15:0]), .in1(MDout[31:16]), .out(multiplexer_12_out), .sel(alu_res[1]));
  Multiplexer #(.select(2), .width(32), .disabled("Z"), .enable("false")) multiplexer_13 (
    .in0({MDout[31:8], R2out[7:0]}), .in1({MDout[31:16], R2out[7:0], MDout[7:0]}),
    .in2({MDout[31:24], R2out[7:0], MDout[15:0]}), .in3({R2out[7:0], MDout[23:0]}), .out(SBin),
    .sel(alu_res[1:0]));
  assign bit_extender_4_out = {{16{1'b0}}, multiplexer_12_out};  // Bit_Extender bit_extender_4
  or or_17 (or_17_out, JAL, JALR);
  Priority_Encoder #(.select(2), .disabled("Z")) priority_encoder_3 (
    .in0(1'b1), .in1(MemToReg), .in3(or_17_out), .out(priority_encoder_3_out));  // open: in2, gs, en_out, en_in
  Multiplexer #(.select(2), .width(32), .disabled("Z"), .enable("false")) multiplexer_14 (
    .in0(alu_res), .in1(MDout), .in2(bit_extender_4_out), .in3(PC_1), .out(RDin), .sel(priority_encoder_3_out));

  // Other names for the same wires on the sheet: sel[1:0] = alu_res[1:0]

  // Notes on the sheet:
  //   中断源
  //   中断等待指示
  //   总复位信号应将除ROM以外所有存储组件全部清零
  //   多级中断测试信号模拟器
  //   数码管输出
  //   数码管输出应该用寄存器锁存，否则显示数据只能一闪而过
  //   LED显示模块
  //   指令探针
  //   指令存储器
  //   contents of rom_1 (hex, n*v repeats v):
  //   7d000113 100413 1f41993 41f9d993 433 c00913 800b13 140413 f47413 800293 100313 499993 89e9b3 1300533
  //   2200893 73 406282b3 fe0294e3 140413 f00f93 1f47433 1c41413 800293 100313 49d993 89e9b3 1300533
  //   2200893 73 406282b3 fe0294e3 1c45413 406b0b33 b0463 f95ff06f 2b3 fff2c293 1029293 fff2e293 500533
  //   2200893 73 f5dff06f 1112023 410113 a12023 410113 812023 410113 1312023 410113 1412023 410113 1512023
  //   410113 1612023 410113 40e073 100b13 300a13 100a93 1600433 441413 14469b3 1300533 2200893 73 fe0416e3
  //   415a0a33 fe0a10e3 40f073 ffc10113 12b03 ffc10113 12a83 ffc10113 12a03 ffc10113 12983 ffc10113 12403
  //   ffc10113 12503 ffc10113 12883 200073 1112023 410113 a12023 410113 812023 410113 1312023 410113
  //   1412023 410113 1512023 410113 1612023 410113 40e073 200b13 300a13 100a93 1600433 441413 14469b3
  //   1300533 2200893 73 fe0416e3 415a0a33 fe0a10e3 40f073 ffc10113 12b03 ffc10113 12a83 ffc10113 12a03
  //   ffc10113 12983 ffc10113 12403 ffc10113 12503 ffc10113 12883 200073 1112023 410113 a12023 410113
  //   812023 410113 1312023 410113 1412023 410113 1512023 410113 1612023 410113 40e073 300b13 300a13
  //   100a93 1600433 441413 14469b3 1300533 2200893 73 fe0416e3 415a0a33 fe0a10e3 40f073 ffc10113 12b03
  //   ffc10113 12a83 ffc10113 12a03 ffc10113 12983 ffc10113 12403 ffc10113 12503 ffc10113 12883 200073
  //   指令字
  //   为方便自动评测，需要输出PC，IR，寄存器堆写如数据RDin
  //   JAL
  //   JALR
  //   URET
  //   SB
  //   B.Inst. Imm
  //   J.Inst. Imm
  //   RAM写使能MemWrite、RAM写入数据MDin等信号
  //   Beq
  //   Bge
  //   Bne
  //   MemToReg
  //   MemWrite
  //   AluOP
  //   AluSrcB
  //   RegWrite
  //   控制位
  //   暂停节拍，不能为0
  //   戳工具置1进入计数暂停模式，ctrl+k时钟自动运行到对应节拍暂停
  //   ctrl+k关闭时钟连续运行，将控制位置零，进入单步调试模式调试
  //   SB指令模块
  //   数据存储器
  //   可计数暂停的时钟源
endmodule

module \封装正确性测试  (
);

  wire IR1, IR2, IR3, MemW, RegW;
  wire [31:0] EX_PC, ID_PC, IF_PC, IR, LED, MDin, MDinr, MEM_PC, PC, RDin, RDinr, WB_PC;

  \单周期RISC_V  \u_单周期risc_v_1  (
    .IR1(IR1), .IR2(IR2), .IR3(IR3), .RegWrite(RegW), .MemWrite(MemW), .PC(PC), .IR(IR), .RDin(RDin),
    .MDin(MDin), .LedData(LED));
  \气泡流水线  \u_气泡流水线_1  (
    .RegWrite(RegW), .MemWrite(MemW), .IF_PC(IF_PC), .ID_PC(ID_PC), .EX_PC(EX_PC), .M_PC(MEM_PC),
    .WB_PC(WB_PC), .RDin(RDinr), .MDin(MDinr), .LedData(LED));
  \单周期_单级中断  \u_单周期_单级中断_1  (
    .IR1(IR1), .IR2(IR2), .IR3(IR3), .RegWrite(RegW), .MemWrite(MemW), .PC(PC), .IR(IR), .RDin(RDin),
    .MDin(MDin), .LedData(LED));
  \理想流水线  \u_理想流水线_1  (
    .RegWrite(RegW), .MemWrite(MemW), .IF_PC(IF_PC), .ID_PC(ID_PC), .EX_PC(EX_PC), .M_PC(MEM_PC),
    .WB_PC(WB_PC), .RDin(RDinr), .MDin(MDinr), .LedData(LED));
  \重定向流水线  \u_重定向流水线_1  (
    .RegWrite(RegW), .MemWrite(MemW), .IF_PC(IF_PC), .ID_PC(ID_PC), .EX_PC(EX_PC), .M_PC(MEM_PC),
    .WB_PC(WB_PC), .RDin(RDinr), .MDin(MDinr), .LedData(LED));
  \单周期_多级中断  \u_单周期_多级中断_1  (
    .IR1(IR1), .IR2(IR2), .IR3(IR3), .RegWrite(RegW), .MemWrite(MemW), .PC(PC), .IR(IR), .RDin(RDin),
    .MDin(MDin), .LedData(LED));

  // Notes on the sheet:
  //   单周期封装测试
  //   气泡流水封装测试
  //   单周期+单级中断封装测试
  //   请检查上面封装有无位宽不匹配，引脚标签是否和连接的标签相对应，否则无法在educoder平台上正确测试
  //   理想流水封装测试
  //   重定向流水封装测试
  //   单周期+多级中断封装测试
endmodule

module IF_ID (
  input  [31:0] IR,
  input  [31:0] PC,
  input  [31:0] PC_4,
  input  PredictJump,
  input  Reset,
  input  BranchTaken,
  input  En,
  input  CLK,
  output [31:0] IR_2,
  output [31:0] PC_2,
  output [31:0] PC_4_2,
  output PredictJump_2
);

  wire multiplexer_4_out, or_1_out;
  wire [31:0] multiplexer_1_out, multiplexer_2_out, multiplexer_3_out;

  Multiplexer #(.select(1), .width(32), .disabled("Z"), .enable("false")) multiplexer_1 (
    .in0(IR), .in1({32{1'b0}}), .out(multiplexer_1_out), .sel(or_1_out));
  Multiplexer #(.select(1), .width(32), .disabled("Z"), .enable("false")) multiplexer_2 (
    .in0(PC), .in1({32{1'b0}}), .out(multiplexer_2_out), .sel(or_1_out));
  Multiplexer #(.select(1), .width(32), .disabled("Z"), .enable("false")) multiplexer_3 (
    .in0(PC_4), .in1({32{1'b0}}), .out(multiplexer_3_out), .sel(or_1_out));
  Multiplexer #(.select(1), .width(1), .disabled("Z"), .enable("false")) multiplexer_4 (
    .in0(PredictJump), .in1(1'b0), .out(multiplexer_4_out), .sel(or_1_out));
  or or_1 (or_1_out, Reset, BranchTaken);
  Register #(.width(32), .trigger("rising"), .Select("low")) register_1 (
    .D(multiplexer_1_out), .en(En), .Q(IR_2), .clk(CLK));  // open: clr
  Register #(.width(32), .trigger("rising"), .Select("low")) register_2 (
    .D(multiplexer_2_out), .en(En), .Q(PC_2), .clk(CLK));  // open: clr
  Register #(.width(32), .trigger("rising"), .Select("low")) register_3 (
    .D(multiplexer_3_out), .en(En), .Q(PC_4_2), .clk(CLK));  // open: clr
  Register #(.width(1), .trigger("rising"), .Select("low")) register_4 (
    .D(multiplexer_4_out), .en(En), .Q(PredictJump_2), .clk(CLK));  // open: clr
endmodule

module ID_EX (
  input  [31:0] R1,
  input  [31:0] R2,
  input  Beq,
  input  Bne,
  input  [31:0] imm1,
  input  Bge,
  input  MemToReg,
  input  [31:0] imm2,
  input  MemWrite,
  input  AluSrcB,
  input  [31:0] PC,
  input  RegWrite,
  input  PredictJump,
  input  [31:0] PC_4,
  input  Ecall,
  input  [31:0] IR,
  input  Jal,
  input  Jalr,
  input  [1:0] rs1forward,
  input  SB,
  input  [3:0] AluOp,
  input  [1:0] rs2forward,
  input  [4:0] rd,
  input  branch,
  input  Reset,
  input  flush,
  input  En,
  input  CLK,
  output [31:0] R1_2,
  output [31:0] R2_2,
  output Beq_2,
  output Bne_2,
  output [31:0] imm1_2,
  output Bge_2,
  output MemToReg_2,
  output [31:0] imm2_2,
  output MemWrite_2,
  output AluSrcB_2,
  output [31:0] PC_2,
  output RegWrite_2,
  output PredictJump_2,
  output [31:0] PC_4_2,
  output Ecall_2,
  output [31:0] IR_2,
  output Jal_2,
  output Jalr_2,
  output [1:0] rs1forward_2,
  output SB_2,
  output [3:0] AluOp_2,
  output [1:0] rs2forward_2,
  output [4:0] rd_2,
  output branch_2
);

  wire multiplexer_1_out, multiplexer_2_out, multiplexer_3_out, multiplexer_4_out, multiplexer_5_out,
       multiplexer_6_out, multiplexer_7_out, multiplexer_8_out, multiplexer_9_out, multiplexer_10_out,
       multiplexer_11_out, multiplexer_12_out, multiplexer_24_out, or_1_out;
  wire [1:0] multiplexer_22_out, multiplexer_23_out;
  wire [3:0] multiplexer_13_out;
  wire [4:0] multiplexer_14_out;
  wire [31:0] multiplexer_15_out, multiplexer_16_out, multiplexer_17_out, multiplexer_18_out,
       multiplexer_19_out, multiplexer_20_out, multiplexer_21_out;

  Multiplexer #(.select(1), .width(1), .disabled("Z"), .enable("false")) multiplexer_1 (
    .in0(Beq), .in1(1'b0), .out(multiplexer_1_out), .sel(or_1_out));
  Multiplexer #(.select(1), .width(1), .disabled("Z"), .enable("false")) multiplexer_2 (
    .in0(Bne), .in1(1'b0), .out(multiplexer_2_out), .sel(or_1_out));
  Multiplexer #(.select(1), .width(1), .disabled("Z"), .enable("false")) multiplexer_3 (
    .in0(Bge), .in1(1'b0), .out(multiplexer_3_out), .sel(or_1_out));
  Multiplexer #(.select(1), .width(1), .disabled("Z"), .enable("false")) multiplexer_4 (
    .in0(MemToReg), .in1(1'b0), .out(multiplexer_4_out), .sel(or_1_out));
  Multiplexer #(.select(1), .width(1), .disabled("Z"), .enable("false")) multiplexer_5 (
    .in0(MemWrite), .in1(1'b0), .out(multiplexer_5_out), .sel(or_1_out));
  Multiplexer #(.select(1), .width(1), .disabled("Z"), .enable("false")) multiplexer_6 (
    .in0(AluSrcB), .in1(1'b0), .out(multiplexer_6_out), .sel(or_1_out));
  Multiplexer #(.select(1), .width(1), .disabled("Z"), .enable("false")) multiplexer_7 (
    .in0(RegWrite), .in1(1'b0), .out(multiplexer_7_out), .sel(or_1_out));
  Multiplexer #(.select(1), .width(1), .disabled("Z"), .enable("false")) multiplexer_8 (
    .in0(PredictJump), .in1(1'b0), .out(multiplexer_8_out), .sel(or_1_out));
  Multiplexer #(.select(1), .width(1), .disabled("Z"), .enable("false")) multiplexer_9 (
    .in0(Ecall), .in1(1'b0), .out(multiplexer_9_out), .sel(or_1_out));
  Multiplexer #(.select(1), .width(1), .disabled("Z"), .enable("false")) multiplexer_10 (
    .in0(Jal), .in1(1'b0), .out(multiplexer_10_out), .sel(or_1_out));
  Multiplexer #(.select(1), .width(1), .disabled("Z"), .enable("false")) multiplexer_11 (
    .in0(Jalr), .in1(1'b0), .out(multiplexer_11_out), .sel(or_1_out));
  Multiplexer #(.select(1), .width(1), .disabled("Z"), .enable("false")) multiplexer_12 (
    .in0(SB), .in1(1'b0), .out(multiplexer_12_out), .sel(or_1_out));
  Multiplexer #(.select(1), .width(4), .disabled("Z"), .enable("false")) multiplexer_13 (
    .in0(AluOp), .in1(4'b0000), .out(multiplexer_13_out), .sel(or_1_out));
  Multiplexer #(.select(1), .width(5), .disabled("Z"), .enable("false")) multiplexer_14 (
    .in0(rd), .in1({5{1'b0}}), .out(multiplexer_14_out), .sel(or_1_out));
  or or_1 (or_1_out, Reset, flush);
  Register #(.width(1), .trigger("rising"), .Select("low")) register_1 (
    .D(multiplexer_1_out), .en(En), .Q(Beq_2), .clk(CLK));  // open: clr
  Register #(.width(1), .trigger("rising"), .Select("low")) register_2 (
    .D(multiplexer_2_out), .en(En), .Q(Bne_2), .clk(CLK));  // open: clr
  Register #(.width(1), .trigger("rising"), .Select("low")) register_3 (
    .D(multiplexer_3_out), .en(En), .Q(Bge_2), .clk(CLK));  // open: clr
  Register #(.width(1), .trigger("rising"), .Select("low")) register_4 (
    .D(multiplexer_4_out), .en(En), .Q(MemToReg_2), .clk(CLK));  // open: clr
  Register #(.width(1), .trigger("rising"), .Select("low")) register_5 (
    .D(multiplexer_5_out), .en(En), .Q(MemWrite_2), .clk(CLK));  // open: clr
  Register #(.width(1), .trigger("rising"), .Select("low")) register_6 (
    .D(multiplexer_6_out), .en(En), .Q(AluSrcB_2), .clk(CLK));  // open: clr
  Register #(.width(1), .trigger("rising"), .Select("low")) register_7 (
    .D(multiplexer_7_out), .en(En), .Q(RegWrite_2), .clk(CLK));  // open: clr
  Register #(.width(1), .trigger("rising"), .Select("low")) register_8 (
    .D(multiplexer_8_out), .en(En), .Q(PredictJump_2), .clk(CLK));  // open: clr
  Register #(.width(1), .trigger("rising"), .Select("low")) register_9 (
    .D(multiplexer_9_out), .en(En), .Q(Ecall_2), .clk(CLK));  // open: clr
  Register #(.width(1), .trigger("rising"), .Select("low")) register_10 (
    .D(multiplexer_10_out), .en(En), .Q(Jal_2), .clk(CLK));  // open: clr
  Register #(.width(1), .trigger("rising"), .Select("low")) register_11 (
    .D(multiplexer_11_out), .en(En), .Q(Jalr_2), .clk(CLK));  // open: clr
  Register #(.width(1), .trigger("rising"), .Select("low")) register_12 (
    .D(multiplexer_12_out), .en(En), .Q(SB_2), .clk(CLK));  // open: clr
  Register #(.width(4), .trigger("rising"), .Select("low")) register_13 (
    .D(multiplexer_13_out), .en(En), .Q(AluOp_2), .clk(CLK));  // open: clr
  Register #(.width(5), .trigger("rising"), .Select("low")) register_14 (
    .D(multiplexer_14_out), .en(En), .Q(rd_2), .clk(CLK));  // open: clr
  Multiplexer #(.select(1), .width(32), .disabled("Z"), .enable("false")) multiplexer_15 (
    .in0(R1), .in1({32{1'b0}}), .out(multiplexer_15_out), .sel(or_1_out));
  Multiplexer #(.select(1), .width(32), .disabled("Z"), .enable("false")) multiplexer_16 (
    .in0(R2), .in1({32{1'b0}}), .out(multiplexer_16_out), .sel(or_1_out));
  Multiplexer #(.select(1), .width(32), .disabled("Z"), .enable("false")) multiplexer_17 (
    .in0(imm1), .in1({32{1'b0}}), .out(multiplexer_17_out), .sel(or_1_out));
  Multiplexer #(.select(1), .width(32), .disabled("Z"), .enable("false")) multiplexer_18 (
    .in0(imm2), .in1({32{1'b0}}), .out(multiplexer_18_out), .sel(or_1_out));
  Multiplexer #(.select(1), .width(32), .disabled("Z"), .enable("false")) multiplexer_19 (
    .in0(PC), .in1({32{1'b0}}), .out(multiplexer_19_out), .sel(or_1_out));
  Multiplexer #(.select(1), .width(32), .disabled("Z"), .enable("false")) multiplexer_20 (
    .in0(PC_4), .in1({32{1'b0}}), .out(multiplexer_20_out), .sel(or_1_out));
  Multiplexer #(.select(1), .width(32), .disabled("Z"), .enable("false")) multiplexer_21 (
    .in0(IR), .in1({32{1'b0}}), .out(multiplexer_21_out), .sel(or_1_out));
  Multiplexer #(.select(1), .width(2), .disabled("Z"), .enable("false")) multiplexer_22 (
    .in0(rs1forward), .in1(2'b00), .out(multiplexer_22_out), .sel(or_1_out));
  Multiplexer #(.select(1), .width(2), .disabled("Z"), .enable("false")) multiplexer_23 (
    .in0(rs2forward), .in1(2'b00), .out(multiplexer_23_out), .sel(or_1_out));
  Multiplexer #(.select(1), .width(1), .disabled("Z"), .enable("false")) multiplexer_24 (
    .in0(branch), .in1(1'b0), .out(multiplexer_24_out), .sel(or_1_out));
  Register #(.width(32), .trigger("rising"), .Select("low")) register_15 (
    .D(multiplexer_15_out), .en(En), .Q(R1_2), .clk(CLK));  // open: clr
  Register #(.width(32), .trigger("rising"), .Select("low")) register_16 (
    .D(multiplexer_16_out), .en(En), .Q(R2_2), .clk(CLK));  // open: clr
  Register #(.width(32), .trigger("rising"), .Select("low")) register_17 (
    .D(multiplexer_17_out), .en(En), .Q(imm1_2), .clk(CLK));  // open: clr
  Register #(.width(32), .trigger("rising"), .Select("low")) register_18 (
    .D(multiplexer_18_out), .en(En), .Q(imm2_2), .clk(CLK));  // open: clr
  Register #(.width(32), .trigger("rising"), .Select("low")) register_19 (
    .D(multiplexer_19_out), .en(En), .Q(PC_2), .clk(CLK));  // open: clr
  Register #(.width(32), .trigger("rising"), .Select("low")) register_20 (
    .D(multiplexer_20_out), .en(En), .Q(PC_4_2), .clk(CLK));  // open: clr
  Register #(.width(32), .trigger("rising"), .Select("low")) register_21 (
    .D(multiplexer_21_out), .en(En), .Q(IR_2), .clk(CLK));  // open: clr
  Register #(.width(2), .trigger("rising"), .Select("low")) register_22 (
    .D(multiplexer_22_out), .en(En), .Q(rs1forward_2), .clk(CLK));  // open: clr
  Register #(.width(2), .trigger("rising"), .Select("low")) register_23 (
    .D(multiplexer_23_out), .en(En), .Q(rs2forward_2), .clk(CLK));  // open: clr
  Register #(.width(1), .trigger("rising"), .Select("low")) register_24 (
    .D(multiplexer_24_out), .en(En), .Q(branch_2), .clk(CLK));  // open: clr
endmodule

module EX_MEM (
  input  [31:0] result,
  input  halt,
  input  MemToReg,
  input  [31:0] WriteData,
  input  MemWrite,
  input  [31:0] PC,
  input  RegWrite,
  input  Jal,
  input  [31:0] PC_4,
  input  Jalr,
  input  SB,
  input  [31:0] IR,
  input  [4:0] rd,
  input  Reset,
  input  En,
  input  CLK,
  output [31:0] result_2,
  output halt_2,
  output MemToReg_2,
  output [31:0] WriteData_2,
  output MemWrite_2,
  output [31:0] PC_2,
  output RegWrite_2,
  output Jal_2,
  output [31:0] PC_4_2,
  output Jalr_2,
  output SB_2,
  output [31:0] IR_2,
  output [4:0] rd_2
);

  wire multiplexer_1_out, multiplexer_2_out, multiplexer_3_out, multiplexer_4_out, multiplexer_5_out,
       multiplexer_6_out, multiplexer_7_out;
  wire [4:0] multiplexer_8_out;
  wire [31:0] multiplexer_9_out, multiplexer_10_out, multiplexer_11_out, multiplexer_12_out,
       multiplexer_13_out;

  Multiplexer #(.select(1), .width(1), .disabled("Z"), .enable("false")) multiplexer_1 (
    .in0(halt), .in1(1'b0), .out(multiplexer_1_out), .sel(Reset));
  Multiplexer #(.select(1), .width(1), .disabled("Z"), .enable("false")) multiplexer_2 (
    .in0(MemToReg), .in1(1'b0), .out(multiplexer_2_out), .sel(Reset));
  Multiplexer #(.select(1), .width(1), .disabled("Z"), .enable("false")) multiplexer_3 (
    .in0(MemWrite), .in1(1'b0), .out(multiplexer_3_out), .sel(Reset));
  Multiplexer #(.select(1), .width(1), .disabled("Z"), .enable("false")) multiplexer_4 (
    .in0(RegWrite), .in1(1'b0), .out(multiplexer_4_out), .sel(Reset));
  Multiplexer #(.select(1), .width(1), .disabled("Z"), .enable("false")) multiplexer_5 (
    .in0(Jal), .in1(1'b0), .out(multiplexer_5_out), .sel(Reset));
  Multiplexer #(.select(1), .width(1), .disabled("Z"), .enable("false")) multiplexer_6 (
    .in0(Jalr), .in1(1'b0), .out(multiplexer_6_out), .sel(Reset));
  Multiplexer #(.select(1), .width(1), .disabled("Z"), .enable("false")) multiplexer_7 (
    .in0(SB), .in1(1'b0), .out(multiplexer_7_out), .sel(Reset));
  Multiplexer #(.select(1), .width(5), .disabled("Z"), .enable("false")) multiplexer_8 (
    .in0(rd), .in1({5{1'b0}}), .out(multiplexer_8_out), .sel(Reset));
  Register #(.width(1), .trigger("rising"), .Select("low")) register_1 (
    .D(multiplexer_1_out), .en(En), .Q(halt_2), .clk(CLK));  // open: clr
  Register #(.width(1), .trigger("rising"), .Select("low")) register_2 (
    .D(multiplexer_2_out), .en(En), .Q(MemToReg_2), .clk(CLK));  // open: clr
  Register #(.width(1), .trigger("rising"), .Select("low")) register_3 (
    .D(multiplexer_3_out), .en(En), .Q(MemWrite_2), .clk(CLK));  // open: clr
  Register #(.width(1), .trigger("rising"), .Select("low")) register_4 (
    .D(multiplexer_4_out), .en(En), .Q(RegWrite_2), .clk(CLK));  // open: clr
  Register #(.width(1), .trigger("rising"), .Select("low")) register_5 (
    .D(multiplexer_5_out), .en(En), .Q(Jal_2), .clk(CLK));  // open: clr
  Register #(.width(1), .trigger("rising"), .Select("low")) register_6 (
    .D(multiplexer_6_out), .en(En), .Q(Jalr_2), .clk(CLK));  // open: clr
  Register #(.width(1), .trigger("rising"), .Select("low")) register_7 (
    .D(multiplexer_7_out), .en(En), .Q(SB_2), .clk(CLK));  // open: clr
  Register #(.width(5), .trigger("rising"), .Select("low")) register_8 (
    .D(multiplexer_8_out), .en(En), .Q(rd_2), .clk(CLK));  // open: clr
  Multiplexer #(.select(1), .width(32), .disabled("Z"), .enable("false")) multiplexer_9 (
    .in0(result), .in1({32{1'b0}}), .out(multiplexer_9_out), .sel(Reset));
  Multiplexer #(.select(1), .width(32), .disabled("Z"), .enable("false")) multiplexer_10 (
    .in0(WriteData), .in1({32{1'b0}}), .out(multiplexer_10_out), .sel(Reset));
  Multiplexer #(.select(1), .width(32), .disabled("Z"), .enable("false")) multiplexer_11 (
    .in0(PC), .in1({32{1'b0}}), .out(multiplexer_11_out), .sel(Reset));
  Multiplexer #(.select(1), .width(32), .disabled("Z"), .enable("false")) multiplexer_12 (
    .in0(PC_4), .in1({32{1'b0}}), .out(multiplexer_12_out), .sel(Reset));
  Multiplexer #(.select(1), .width(32), .disabled("Z"), .enable("false")) multiplexer_13 (
    .in0(IR), .in1({32{1'b0}}), .out(multiplexer_13_out), .sel(Reset));
  Register #(.width(32), .trigger("rising"), .Select("low")) register_9 (
    .D(multiplexer_9_out), .en(En), .Q(result_2), .clk(CLK));  // open: clr
  Register #(.width(32), .trigger("rising"), .Select("low")) register_10 (
    .D(multiplexer_10_out), .en(En), .Q(WriteData_2), .clk(CLK));  // open: clr
  Register #(.width(32), .trigger("rising"), .Select("low")) register_11 (
    .D(multiplexer_11_out), .en(En), .Q(PC_2), .clk(CLK));  // open: clr
  Register #(.width(32), .trigger("rising"), .Select("low")) register_12 (
    .D(multiplexer_12_out), .en(En), .Q(PC_4_2), .clk(CLK));  // open: clr
  Register #(.width(32), .trigger("rising"), .Select("low")) register_13 (
    .D(multiplexer_13_out), .en(En), .Q(IR_2), .clk(CLK));  // open: clr
endmodule

module MEM_WB (
  input  [31:0] result,
  input  [31:0] ReadData,
  input  halt,
  input  MemToReg,
  input  [31:0] PC,
  input  RegWrite,
  input  Jal,
  input  [31:0] PC_4,
  input  Jalr,
  input  [31:0] IR,
  input  [4:0] rd,
  input  Reset,
  input  En,
  input  CLK,
  output [31:0] result_2,
  output [31:0] ReadData_2,
  output halt_2,
  output MemToReg_2,
  output [31:0] PC_2,
  output RegWrite_2,
  output Jal_2,
  output [31:0] PC_4_2,
  output Jalr_2,
  output [31:0] IR_2,
  output [4:0] rd_2
);

  wire multiplexer_1_out, multiplexer_2_out, multiplexer_3_out, multiplexer_4_out, multiplexer_5_out;
  wire [4:0] multiplexer_6_out;
  wire [31:0] multiplexer_7_out, multiplexer_8_out, multiplexer_9_out, multiplexer_10_out, multiplexer_11_out;

  Multiplexer #(.select(1), .width(1), .disabled("Z"), .enable("false")) multiplexer_1 (
    .in0(halt), .in1(1'b0), .out(multiplexer_1_out), .sel(Reset));
  Multiplexer #(.select(1), .width(1), .disabled("Z"), .enable("false")) multiplexer_2 (
    .in0(MemToReg), .in1(1'b0), .out(multiplexer_2_out), .sel(Reset));
  Multiplexer #(.select(1), .width(1), .disabled("Z"), .enable("false")) multiplexer_3 (
    .in0(RegWrite), .in1(1'b0), .out(multiplexer_3_out), .sel(Reset));
  Multiplexer #(.select(1), .width(1), .disabled("Z"), .enable("false")) multiplexer_4 (
    .in0(Jal), .in1(1'b0), .out(multiplexer_4_out), .sel(Reset));
  Multiplexer #(.select(1), .width(1), .disabled("Z"), .enable("false")) multiplexer_5 (
    .in0(Jalr), .in1(1'b0), .out(multiplexer_5_out), .sel(Reset));
  Multiplexer #(.select(1), .width(5), .disabled("Z"), .enable("false")) multiplexer_6 (
    .in0(rd), .in1({5{1'b0}}), .out(multiplexer_6_out), .sel(Reset));
  Register #(.width(1), .trigger("rising"), .Select("low")) register_1 (
    .D(multiplexer_1_out), .en(En), .Q(halt_2), .clk(CLK));  // open: clr
  Register #(.width(1), .trigger("rising"), .Select("low")) register_2 (
    .D(multiplexer_2_out), .en(En), .Q(MemToReg_2), .clk(CLK));  // open: clr
  Register #(.width(1), .trigger("rising"), .Select("low")) register_3 (
    .D(multiplexer_3_out), .en(En), .Q(RegWrite_2), .clk(CLK));  // open: clr
  Register #(.width(1), .trigger("rising"), .Select("low")) register_4 (
    .D(multiplexer_4_out), .en(En), .Q(Jal_2), .clk(CLK));  // open: clr
  Register #(.width(1), .trigger("rising"), .Select("low")) register_5 (
    .D(multiplexer_5_out), .en(En), .Q(Jalr_2), .clk(CLK));  // open: clr
  Register #(.width(5), .trigger("rising"), .Select("low")) register_6 (
    .D(multiplexer_6_out), .en(En), .Q(rd_2), .clk(CLK));  // open: clr
  Multiplexer #(.select(1), .width(32), .disabled("Z"), .enable("false")) multiplexer_7 (
    .in0(result), .in1({32{1'b0}}), .out(multiplexer_7_out), .sel(Reset));
  Multiplexer #(.select(1), .width(32), .disabled("Z"), .enable("false")) multiplexer_8 (
    .in0(ReadData), .in1({32{1'b0}}), .out(multiplexer_8_out), .sel(Reset));
  Multiplexer #(.select(1), .width(32), .disabled("Z"), .enable("false")) multiplexer_9 (
    .in0(PC), .in1({32{1'b0}}), .out(multiplexer_9_out), .sel(Reset));
  Multiplexer #(.select(1), .width(32), .disabled("Z"), .enable("false")) multiplexer_10 (
    .in0(PC_4), .in1({32{1'b0}}), .out(multiplexer_10_out), .sel(Reset));
  Multiplexer #(.select(1), .width(32), .disabled("Z"), .enable("false")) multiplexer_11 (
    .in0(IR), .in1({32{1'b0}}), .out(multiplexer_11_out), .sel(Reset));
  Register #(.width(32), .trigger("rising"), .Select("low")) register_7 (
    .D(multiplexer_7_out), .en(En), .Q(result_2), .clk(CLK));  // open: clr
  Register #(.width(32), .trigger("rising"), .Select("low")) register_8 (
    .D(multiplexer_8_out), .en(En), .Q(ReadData_2), .clk(CLK));  // open: clr
  Register #(.width(32), .trigger("rising"), .Select("low")) register_9 (
    .D(multiplexer_9_out), .en(En), .Q(PC_2), .clk(CLK));  // open: clr
  Register #(.width(32), .trigger("rising"), .Select("low")) register_10 (
    .D(multiplexer_10_out), .en(En), .Q(PC_4_2), .clk(CLK));  // open: clr
  Register #(.width(32), .trigger("rising"), .Select("low")) register_11 (
    .D(multiplexer_11_out), .en(En), .Q(IR_2), .clk(CLK));  // open: clr
endmodule

module \气泡流水线逻辑  (
  input  BranchTaken,
  input  [31:0] IR,
  input  ecall,
  input  rs1,
  input  EX_RegWrite,
  input  [4:0] EX_rd,
  input  rs2,
  input  MEM_RegWrite,
  input  [4:0] MEM_rd,
  output stall,
  output flush
);

  wire and_1_out, and_2_out, and_3_out, and_4_out, and_5_out, and_6_out, comparator_1_eq, comparator_2_eq,
       comparator_3_eq, comparator_4_eq, comparator_5_eq, comparator_6_eq, comparator_7_eq, comparator_8_eq,
       comparator_9_eq, comparator_10_eq, comparator_11_eq, comparator_12_eq, or_1_out, or_2_out, or_3_out,
       or_4_out;

  Comparator #(.width(5), .mode("unsigned")) comparator_1 (
    .a({5{1'b0}}), .b(IR[19:15]), .eq(comparator_1_eq));  // open: gt, lt
  Comparator #(.width(5), .mode("unsigned")) comparator_2 (
    .a(EX_rd), .b(IR[19:15]), .eq(comparator_2_eq));  // open: gt, lt
  Comparator #(.width(5), .mode("unsigned")) comparator_3 (
    .a(IR[19:15]), .b(MEM_rd), .eq(comparator_3_eq));  // open: gt, lt
  Comparator #(.width(5), .mode("unsigned")) comparator_4 (
    .a(IR[19:15]), .b({5{1'b0}}), .eq(comparator_4_eq));  // open: gt, lt
  Comparator #(.width(5), .mode("unsigned")) comparator_5 (
    .a({5{1'b0}}), .b(IR[24:20]), .eq(comparator_5_eq));  // open: gt, lt
  Comparator #(.width(5), .mode("unsigned")) comparator_6 (
    .a(EX_rd), .b(IR[24:20]), .eq(comparator_6_eq));  // open: gt, lt
  Comparator #(.width(5), .mode("unsigned")) comparator_7 (
    .a(IR[24:20]), .b(MEM_rd), .eq(comparator_7_eq));  // open: gt, lt
  Comparator #(.width(5), .mode("unsigned")) comparator_8 (
    .a(IR[24:20]), .b({5{1'b0}}), .eq(comparator_8_eq));  // open: gt, lt
  Comparator #(.width(5), .mode("unsigned")) comparator_9 (
    .a(5'b01010), .b(EX_rd), .eq(comparator_9_eq));  // open: gt, lt
  Comparator #(.width(5), .mode("unsigned")) comparator_10 (
    .a(EX_rd), .b(5'b10001), .eq(comparator_10_eq));  // open: gt, lt
  Comparator #(.width(5), .mode("unsigned")) comparator_11 (
    .a(5'b01010), .b(MEM_rd), .eq(comparator_11_eq));  // open: gt, lt
  Comparator #(.width(5), .mode("unsigned")) comparator_12 (
    .a(MEM_rd), .b(5'b10001), .eq(comparator_12_eq));  // open: gt, lt
  and and_1 (and_1_out, ~comparator_1_eq, rs1, EX_RegWrite, comparator_2_eq);  // AND_Gate
  and and_2 (and_2_out, rs1, comparator_3_eq, MEM_RegWrite, ~comparator_4_eq);  // AND_Gate
  and and_3 (and_3_out, ~comparator_5_eq, rs2, EX_RegWrite, comparator_6_eq);  // AND_Gate
  and and_4 (and_4_out, comparator_7_eq, rs2, MEM_RegWrite, ~comparator_8_eq);  // AND_Gate
  or or_1 (or_1_out, comparator_9_eq, comparator_10_eq);
  or or_2 (or_2_out, comparator_11_eq, comparator_12_eq);
  and and_5 (and_5_out, or_1_out, EX_RegWrite, ecall);
  and and_6 (and_6_out, ecall, MEM_RegWrite, or_2_out);
  or or_3 (or_3_out, and_1_out, and_2_out, and_3_out, and_4_out);
  or or_4 (or_4_out, and_5_out, and_6_out);
  or or_5 (stall, or_3_out, or_4_out);
  or or_6 (flush, stall, BranchTaken);

  // Other names for the same wires on the sheet: DataHazzard = stall; rs1_t[4:0] = IR[19:15]; rs2_t[4:0] = IR[24:20];
  //   rs1_used = rs1; rs2_used = rs2
endmodule

module \重定向处理逻辑  (
  input  BranchTaken,
  input  [31:0] IR,
  input  ecall,
  input  EX_MemToReg,
  input  rs_av,
  input  EX_RegWrite,
  input  [4:0] EX_rd,
  input  rt_av,
  input  MEM_RegWrite,
  input  [4:0] MEM_rd,
  output stall,
  output flush,
  output [1:0] rs1Forward,
  output [1:0] rs2Forward
);

  wire _1, _2, _3, _4, and_5_out, and_6_out, and_7_out, and_8_out, and_9_out, and_10_out, and_11_out,
       and_12_out, and_15_out, and_16_out, comparator_1_eq, comparator_2_eq, comparator_3_eq,
       comparator_4_eq, comparator_5_eq, comparator_6_eq, comparator_7_eq, comparator_8_eq, comparator_9_eq,
       comparator_10_eq, comparator_11_eq, comparator_12_eq, comparator_13_eq, comparator_14_eq,
       comparator_15_eq, comparator_16_eq, or_2_out, or_4_out;

  Comparator #(.width(5), .mode("unsigned")) comparator_1 (
    .a(EX_rd), .b(5'b10001), .eq(comparator_1_eq));  // open: gt, lt
  Comparator #(.width(5), .mode("unsigned")) comparator_2 (
    .a(EX_rd), .b(5'b01010), .eq(comparator_2_eq));  // open: gt, lt
  Comparator #(.width(5), .mode("unsigned")) comparator_3 (
    .a(5'b10001), .b(MEM_rd), .eq(comparator_3_eq));  // open: gt, lt
  Comparator #(.width(5), .mode("unsigned")) comparator_4 (
    .a(5'b01010), .b(MEM_rd), .eq(comparator_4_eq));  // open: gt, lt
  Comparator #(.width(5), .mode("unsigned")) comparator_5 (
    .a({5{1'b0}}), .b(IR[19:15]), .eq(comparator_5_eq));  // open: gt, lt
  Comparator #(.width(5), .mode("unsigned")) comparator_6 (
    .a({5{1'b0}}), .b(IR[19:15]), .eq(comparator_6_eq));  // open: gt, lt
  Comparator #(.width(5), .mode("unsigned")) comparator_7 (
    .a({5{1'b0}}), .b(IR[24:20]), .eq(comparator_7_eq));  // open: gt, lt
  Comparator #(.width(5), .mode("unsigned")) comparator_8 (
    .a({5{1'b0}}), .b(IR[24:20]), .eq(comparator_8_eq));  // open: gt, lt
  and and_1 (_1, ecall, comparator_1_eq, EX_RegWrite);
  and and_2 (_3, ecall, comparator_2_eq, EX_RegWrite);
  and and_3 (_2, ecall, comparator_3_eq, MEM_RegWrite);
  and and_4 (_4, ecall, comparator_4_eq, MEM_RegWrite);
  and and_5 (and_5_out, rs_av, ~comparator_5_eq);  // AND_Gate
  Comparator #(.width(5), .mode("unsigned")) comparator_9 (
    .a(EX_rd), .b(IR[19:15]), .eq(comparator_9_eq));  // open: gt, lt
  and and_6 (and_6_out, rs_av, ~comparator_6_eq);  // AND_Gate
  Comparator #(.width(5), .mode("unsigned")) comparator_10 (
    .a(MEM_rd), .b(IR[19:15]), .eq(comparator_10_eq));  // open: gt, lt
  and and_7 (and_7_out, rt_av, ~comparator_7_eq);  // AND_Gate
  Comparator #(.width(5), .mode("unsigned")) comparator_11 (
    .a(EX_rd), .b(IR[24:20]), .eq(comparator_11_eq));  // open: gt, lt
  and and_8 (and_8_out, rt_av, ~comparator_8_eq);  // AND_Gate
  Comparator #(.width(5), .mode("unsigned")) comparator_12 (
    .a(MEM_rd), .b(IR[24:20]), .eq(comparator_12_eq));  // open: gt, lt
  and and_9 (and_9_out, and_5_out, EX_RegWrite, comparator_9_eq);
  and and_10 (and_10_out, and_6_out, MEM_RegWrite, comparator_10_eq);
  and and_11 (and_11_out, and_7_out, EX_RegWrite, comparator_11_eq);
  and and_12 (and_12_out, and_8_out, MEM_RegWrite, comparator_12_eq);
  Comparator #(.width(5), .mode("unsigned")) comparator_13 (
    .a(EX_rd), .b(IR[19:15]), .eq(comparator_13_eq));  // open: gt, lt
  Comparator #(.width(5), .mode("unsigned")) comparator_14 (
    .a(IR[19:15]), .b({5{1'b0}}), .eq(comparator_14_eq));  // open: gt, lt
  Comparator #(.width(5), .mode("unsigned")) comparator_15 (
    .a({5{1'b0}}), .b(IR[24:20]), .eq(comparator_15_eq));  // open: gt, lt
  Comparator #(.width(5), .mode("unsigned")) comparator_16 (
    .a(IR[24:20]), .b(EX_rd), .eq(comparator_16_eq));  // open: gt, lt
  or or_1 (rs1Forward[1], and_9_out, _1);
  or or_2 (or_2_out, and_10_out, _2);
  or or_3 (rs2Forward[1], and_11_out, _3);
  or or_4 (or_4_out, and_12_out, _4);
  and and_13 (rs1Forward[0], ~rs1Forward[1], or_2_out);  // AND_Gate
  and and_14 (rs2Forward[0], ~rs2Forward[1], or_4_out);  // AND_Gate
  or or_5 (flush, stall, BranchTaken);
  and and_15 (and_15_out, rs_av, comparator_13_eq, ~comparator_14_eq, EX_MemToReg);  // AND_Gate
  and and_16 (and_16_out, EX_MemToReg, ~comparator_15_eq, comparator_16_eq, rt_av);  // AND_Gate
  or or_6 (stall, and_15_out, and_16_out);

  // Other names for the same wires on the sheet: rs1[4:0] = IR[19:15]; rs2[4:0] = IR[24:20]; LoadUse = stall;
  //   rs1_used = rs_av; rs2_used = rt_av
endmodule

module \流水线中断  (
  output RegWrite,
  output MemWrite,
  output [31:0] IF_PC,
  output [31:0] ID_PC,
  output [31:0] EX_PC,
  output [31:0] M_PC,
  output [31:0] WB_PC,
  output [31:0] RDin,
  output [31:0] MDin,
  output [31:0] LedData
);

  wire alu_1_equal, alu_1_out_4, and_1_out, and_2_out, and_3_out, and_4_out, and_5_out, and_9_out,
       and_10_out, and_11_out, and_12_out, and_14_out, and_15_out, and_16_out, beq, bge, bne, Branch_BT,
       BranchTaken, CLK, clock_1_out, comparator_1_eq, comparator_1_lt, comparator_2_eq, d_ff_1_q, d_ff_2_q,
       d_ff_3_q, d_ff_4_q, d_ff_5_q, d_ff_6_q, d_ff_7_q, decoder_1_out1, decoder_1_out2, decoder_1_out3,
       ecall, EX_ecall, EX_halt, EX_J, EX_Jal, EX_Jalr, EX_MEM_halt_2, EX_MEM_jal_2, EX_MEM_jalr_2,
       EX_MEM_memtoreg_2, EX_RegWrite, EX_SB, flush, Go, halt, ID_EX_alusrcb_2, ID_EX_memtoreg_2,
       ID_EX_memwrite_2, IF_URET, INT, INT_IE, INT_IR, IR1, IR2, IR3, IRAreset, IRBreset, IRCreset, JAL,
       MEM_RegWrite, MEM_SB, MEM_str, MEM_WB_halt_2, MEM_WB_jal_2, MEM_WB_jalr_2, nand_1_out, not_2_out,
       not_3_out, not_4_out, or_5_out, or_6_out, or_7_out, or_12_out, register_2_q, riscv_probe_4_p2, RST, S,
       S_type, SB, stall, undriven, W1, W2, W3, \单周期硬布线控制器_1_alu_src , \单周期硬布线控制器_1_beq , \单周期硬布线控制器_1_bge ,
       \单周期硬布线控制器_1_bne , \单周期硬布线控制器_1_jalr , \单周期硬布线控制器_1_memtoreg , \单周期硬布线控制器_1_memwrite ,
       \单周期硬布线控制器_1_regwrite , \单周期硬布线控制器_1_rs1 , \单周期硬布线控制器_1_rs2 ;
  wire [1:0] MEM_WB_memtoreg_2, priority_encoder_1_out, register_3_q, SB_sel;
  wire [3:0] ID_EX_aluop_2, \单周期硬布线控制器_1_alu_op ;
  wire [4:0] EX_MEM_rd_2, ID_EX_rd_2, multiplexer_4_out, multiplexer_5_out, WB_rd;
  wire [11:0] multiplexer_6_out;
  wire [12:0] CNT_num;
  wire [15:0] \LoadUse次数 , \总周期数 , \插入气泡数 , \无条件分支数 , \条件分支成功数 ;
  wire [31:0] ALU_addr, bit_extender_1_out, bit_extender_2_out, bit_extender_3_out, Branch_addr, EX_IR,
       EX_MEM_pc_4_2, EX_PC_4, ID_EX_imm1_2, ID_EX_imm2_2, ID_EX_r1_2, ID_EX_r2_2, ID_IR, ID_PC_4, IF_IR,
       IF_PC_4, IF_PCin, IF_PCsel, INT_PC, MDout, MEM_Din, MEM_IR, MEM_WB_pc_4_2, MEM_WB_readdata_2,
       MEM_WB_result_2, multiplexer_1_out, multiplexer_7_out, multiplexer_9_out, regifile_1_r1,
       regifile_1_r2, ret_PC, SBin, shifter_1_out, WB_IR;
  wire [31:2] EX_MEM_result_2;

  Button \u_总复位  (.out(RST));
  Button _1 (.out(IR1));
  Button _2 (.out(IR2));
  Button _3 (.out(IR3));
  // Probe on \总周期数 
  // Probe on \总周期数 
  // Probe on IF_PCin
  and and_1 (and_1_out, ~stall, ~halt);  // AND_Gate
  or or_1 (W1, d_ff_1_q, d_ff_4_q);
  or or_2 (W2, d_ff_2_q, d_ff_5_q);
  or or_3 (W3, d_ff_3_q, d_ff_6_q);
  Button \u_继续运行  (.out(Go));
  LED #(.active("true")) led_1 (.in(W1));
  LED #(.active("true")) led_2 (.in(W2));
  LED #(.active("true")) led_3 (.in(W3));
  // Probe on IF_PC[19:0]
  // RiscV_Probe riscv_probe_1: pin names not known; wires that end beside it: IF_IR
  Multiplexer #(.select(1), .width(32), .disabled("Z"), .enable("false")) multiplexer_1 (
    .in0(IF_PCsel), .in1(INT_PC), .out(multiplexer_1_out), .sel(INT));
  Multiplexer #(.select(1), .width(32), .disabled("Z"), .enable("false")) multiplexer_2 (
    .in0(multiplexer_1_out), .in1(ret_PC), .out(IF_PCin), .sel(IF_URET));
  Multiplexer #(.select(2), .width(32), .disabled("Z"), .enable("false")) multiplexer_3 (
    .in0(IF_PC_4), .in1(ALU_addr), .in2(Branch_addr), .out(IF_PCsel), .sel({S, EX_Jalr}));  // open: in3
  Register #(.width(32), .trigger("rising"), .Select("low")) PC (
    .D(IF_PCin), .en(and_1_out), .Q(IF_PC), .clk(CLK), .clr(RST));
  and and_2 (and_2_out, INT_IR, INT_IE);
  Hex_Digit_Display hex_digit_display_1 (.value(LedData[27:24]));  // open: dp
  Hex_Digit_Display hex_digit_display_2 (.value(LedData[31:28]));  // open: dp
  Register #(.width(1), .trigger("falling"), .Select("low")) register_1 (
    .D(and_2_out), .Q(INT), .clk(CLK));  // open: en, clr
  D_Flip_Flop #(.trigger("rising"), .Pre_Clr_Positions("LEGACY"), .NegatePresetClear("false"), .enable("true"), .NewFFLayout("false")) d_ff_1 (
    .clk(IR1), .D(1'b1), .Q(d_ff_1_q), .reset(d_ff_4_q));  // open: Qn, preset, en
  D_Flip_Flop #(.trigger("rising"), .Pre_Clr_Positions("LEGACY"), .NegatePresetClear("false"), .enable("true"), .NewFFLayout("false")) d_ff_2 (
    .clk(IR2), .D(1'b1), .Q(d_ff_2_q), .reset(d_ff_5_q));  // open: Qn, preset, en
  D_Flip_Flop #(.trigger("rising"), .Pre_Clr_Positions("LEGACY"), .NegatePresetClear("false"), .enable("true"), .NewFFLayout("false")) d_ff_3 (
    .clk(IR3), .D(1'b1), .Q(d_ff_3_q), .reset(d_ff_6_q));  // open: Qn, preset, en
  Hex_Digit_Display hex_digit_display_3 (.value(LedData[19:16]));  // open: dp
  Hex_Digit_Display hex_digit_display_4 (.value(LedData[23:20]));  // open: dp
  // Probe on ID_PC[19:0]
  // RiscV_Probe riscv_probe_2: pin names not known; wires that end beside it: ID_IR
  or or_4 (EX_J, EX_Jal, EX_Jalr);
  Adder #(.width(32)) adder_1 (.a(IF_PC), .b(32'h4), .out(IF_PC_4));  // open: cin, cout
  or or_5 (or_5_out, d_ff_1_q, d_ff_4_q);
  or or_6 (or_6_out, d_ff_2_q, d_ff_5_q);
  or or_7 (or_7_out, d_ff_3_q, d_ff_6_q);
  Hex_Digit_Display hex_digit_display_5 (.value(LedData[15:12]));  // open: dp
  Hex_Digit_Display hex_digit_display_6 (.value(LedData[11:8]));  // open: dp
  ROM #(.addrWidth(10), .dataWidth(32), .Select("high")) \u_指令存储器  (.addr(IF_PC[11:2]), .data(IF_IR));
  Register #(.width(32), .trigger("rising"), .Select("low")) mEPC (
    .D(IF_PCsel), .en(INT), .Q(ret_PC), .clk(CLK));  // open: clr
  and and_3 (and_3_out, or_5_out, ~IRAreset);  // AND_Gate
  and and_4 (and_4_out, or_6_out, ~IRBreset);  // AND_Gate
  and and_5 (and_5_out, or_7_out, ~IRCreset);  // AND_Gate
  Hex_Digit_Display hex_digit_display_7 (.value(LedData[3:0]));  // open: dp
  Hex_Digit_Display hex_digit_display_8 (.value(LedData[7:4]));  // open: dp
  // Probe on EX_PC[19:0]
  // RiscV_Probe riscv_probe_3: pin names not known; wires that end beside it: EX_IR
  or or_8 (BranchTaken, S, EX_Jalr);
  IF_ID IF_ID (
    .IR(IF_IR), .PC(IF_PC), .PC_4(IF_PC_4), .IR_2(ID_IR), .PC_2(ID_PC), .PC_4_2(ID_PC_4), .Reset(RST),
    .BranchTaken(BranchTaken), .En(and_1_out), .CLK(CLK));  // open: PredictJump, PredictJump_2
  D_Flip_Flop #(.trigger("rising"), .Pre_Clr_Positions("LEGACY"), .NegatePresetClear("false"), .enable("true"), .NewFFLayout("false")) d_ff_4 (
    .clk(CLK), .D(and_3_out), .Q(d_ff_4_q));  // open: Qn, preset, en, reset
  D_Flip_Flop #(.trigger("rising"), .Pre_Clr_Positions("LEGACY"), .NegatePresetClear("false"), .enable("true"), .NewFFLayout("false")) d_ff_5 (
    .clk(CLK), .D(and_4_out), .Q(d_ff_5_q));  // open: Qn, preset, en, reset
  D_Flip_Flop #(.trigger("rising"), .Pre_Clr_Positions("LEGACY"), .NegatePresetClear("false"), .enable("true"), .NewFFLayout("false")) d_ff_6 (
    .clk(CLK), .D(and_5_out), .Q(d_ff_6_q));  // open: Qn, preset, en, reset
  // RiscV_Probe riscv_probe_4: pin names not known; wires that end beside it: MEM_IR, riscv_probe_4_p2
  not not_1 (INT_IE, register_2_q);
  Register #(.width(1), .trigger("falling"), .Select("low")) register_2 (
    .D(1'b0), .en(IF_URET), .Q(register_2_q), .clk(CLK), .preset(INT));  // open: clr, cs
  // Probe on \总周期数 
  // Probe on M_PC[19:0]
  \单周期硬布线控制器  \u_单周期硬布线控制器_1  (
    .Funct({ID_IR[30], ID_IR[25], ID_IR[14:12]}), .OP(ID_IR[6:2]), .ALU_OP(\单周期硬布线控制器_1_alu_op ),
    .MemToReg(\单周期硬布线控制器_1_memtoreg ), .MemWrite(\单周期硬布线控制器_1_memwrite ), .ALU_SRC(\单周期硬布线控制器_1_alu_src ),
    .RegWrite(\单周期硬布线控制器_1_regwrite ), .ecall(ecall), .S_type(S_type), .Jalr(\单周期硬布线控制器_1_jalr ),
    .Beq(\单周期硬布线控制器_1_beq ), .JAL(JAL), .Bne(\单周期硬布线控制器_1_bne ), .in_3(ID_IR[21]), .uret(riscv_probe_4_p2),
    .BGE(\单周期硬布线控制器_1_bge ), .SB(SB), .rs1(\单周期硬布线控制器_1_rs1 ), .rs2(\单周期硬布线控制器_1_rs2 ));  // open: csrrsi, csrrci
  Multiplexer #(.select(1), .width(5), .disabled("Z"), .enable("false")) multiplexer_4 (
    .in0(ID_IR[19:15]), .in1(5'b10001), .out(multiplexer_4_out), .sel(ecall));
  Multiplexer #(.select(1), .width(5), .disabled("Z"), .enable("false")) multiplexer_5 (
    .in0(ID_IR[24:20]), .in1(5'b01010), .out(multiplexer_5_out), .sel(ecall));
  Multiplexer #(.select(1), .width(12), .disabled("Z"), .enable("false")) multiplexer_6 (
    .in0(ID_IR[31:20]), .in1({ID_IR[31:25], ID_IR[11:7]}), .out(multiplexer_6_out), .sel(S_type));
  Priority_Encoder #(.select(2), .disabled("Z")) priority_encoder_1 (
    .in0(1'b0), .in1(d_ff_4_q), .in2(d_ff_5_q), .in3(d_ff_6_q), .out(priority_encoder_1_out), .gs(INT_IR));  // open: en_out, en_in
  // Probe on \总周期数 
  // Probe on \无条件分支数 
  // Probe on \条件分支成功数 
  // Probe on \插入气泡数 
  // Probe on \LoadUse次数 
  // Probe on WB_PC[19:0]
  // RiscV_Probe riscv_probe_5: pin names not known; wires that end beside it: WB_IR
  assign bit_extender_1_out = {{20{multiplexer_6_out[11]}}, multiplexer_6_out};  // Bit_Extender bit_extender_1
  assign bit_extender_2_out = {{20{ID_IR[31]}}, {ID_IR[31], ID_IR[7], ID_IR[30:25], ID_IR[11:8]}};  // Bit_Extender bit_extender_2
  assign bit_extender_3_out = {{12{ID_IR[31]}}, {ID_IR[31], ID_IR[19:12], ID_IR[20], ID_IR[30:21]}};  // Bit_Extender bit_extender_3
  // Probe on undriven
  // Probe on ID_PC[11:0]
  // Probe on IF_PC[11:0]
  not not_2 (not_2_out, CLK);
  Multiplexer #(.select(1), .width(32), .disabled("Z"), .enable("false")) multiplexer_7 (
    .in0(bit_extender_2_out), .in1(bit_extender_3_out), .out(multiplexer_7_out), .sel(JAL));
  Register #(.width(2), .trigger("rising"), .Select("low")) register_3 (
    .D(priority_encoder_1_out), .Q(register_3_q), .clk(INT));  // open: en, clr
  Multiplexer #(.select(2), .width(32), .disabled("Z"), .enable("false")) multiplexer_8 (
    .in1(32'h30ac), .in2(32'h3150), .in3(32'h31f4), .out(INT_PC), .sel(priority_encoder_1_out));  // open: in0
  // Probe on EX_PC[11:0]
  D_Flip_Flop #(.trigger("high"), .Pre_Clr_Positions("LEGACY"), .NegatePresetClear("false"), .enable("true"), .NewFFLayout("false")) d_ff_7 (.Q(d_ff_7_q));  // open: clk, D, Qn, preset, en, reset
  Regifile regifile_1 (
    .Din(RDin), .Clk(not_2_out), .R1(regifile_1_r1), .R2(regifile_1_r2), .WE(RegWrite), .W_num(WB_rd),
    .R1_num(multiplexer_4_out), .R2_num(multiplexer_5_out));
  not not_3 (not_3_out, halt);
  Decoder #(.select(2), .tristate("false"), .disabled("Z"), .enable("false")) decoder_1 (
    .out1(decoder_1_out1), .out2(decoder_1_out2), .out3(decoder_1_out3), .sel(register_3_q));  // open: out0
  // Probe on M_PC[11:0]
  // Probe on WB_PC[11:0]
  // Probe on 13'h1552
  and and_6 (IRAreset, decoder_1_out1, IF_URET);
  and and_7 (IRBreset, decoder_1_out2, IF_URET);
  and and_8 (IRCreset, decoder_1_out3, IF_URET);
  Comparator #(.width(13), .mode("twosComplement")) comparator_1 (
    .a(CNT_num), .b(13'h1552), .eq(comparator_1_eq), .lt(comparator_1_lt));  // open: gt
  Clock #(.highDuration(1), .lowDuration(1)) clock_1 (.out(clock_1_out));
  ID_EX ID_EX (
    .Beq(\单周期硬布线控制器_1_beq ), .Beq_2(beq), .Bne(\单周期硬布线控制器_1_bne ), .Bne_2(bne), .Bge(\单周期硬布线控制器_1_bge ),
    .Bge_2(bge), .MemToReg(\单周期硬布线控制器_1_memtoreg ), .MemToReg_2(ID_EX_memtoreg_2),
    .MemWrite(\单周期硬布线控制器_1_memwrite ), .MemWrite_2(ID_EX_memwrite_2), .AluSrcB(\单周期硬布线控制器_1_alu_src ),
    .AluSrcB_2(ID_EX_alusrcb_2), .RegWrite_2(EX_RegWrite), .RegWrite(\单周期硬布线控制器_1_regwrite ), .Ecall(ecall),
    .Ecall_2(EX_ecall), .Jal_2(EX_Jal), .Jal(JAL), .Jalr(\单周期硬布线控制器_1_jalr ), .Jalr_2(EX_Jalr), .SB(SB),
    .SB_2(EX_SB), .Reset(RST), .flush(flush), .En(not_3_out), .CLK(CLK), .AluOp(\单周期硬布线控制器_1_alu_op ),
    .AluOp_2(ID_EX_aluop_2), .rd(ID_IR[11:7]), .rd_2(ID_EX_rd_2), .R1(regifile_1_r1), .R1_2(ID_EX_r1_2),
    .R2(regifile_1_r2), .R2_2(ID_EX_r2_2), .imm1(bit_extender_1_out), .imm1_2(ID_EX_imm1_2),
    .imm2(multiplexer_7_out), .imm2_2(ID_EX_imm2_2), .PC(ID_PC), .PC_2(EX_PC), .PC_4(ID_PC_4),
    .PC_4_2(EX_PC_4), .IR(ID_IR), .IR_2(EX_IR));  // open: PredictJump, PredictJump_2, rs1forward, rs1forward_2, rs2forward, rs2forward_2, branch, branch_2
  // Probe on ID_EX_r2_2
  nand nand_1 (nand_1_out, d_ff_7_q, comparator_1_eq);
  Counter #(.width(13), .max('h1fff), .ongoal("stay"), .trigger("rising"), .behavior("old")) counter_1 (
    .count(comparator_1_lt), .Q(CNT_num), .clk(clock_1_out));  // open: load, D, carry, clr, preset
  Multiplexer #(.select(1), .width(32), .disabled("Z"), .enable("false")) multiplexer_9 (
    .in0(ID_EX_r2_2), .in1(ID_EX_imm1_2), .out(multiplexer_9_out), .sel(ID_EX_alusrcb_2));
  Shifter #(.width(32), .shift("ll")) shifter_1 (.in(ID_EX_imm2_2), .\dist (5'b00001), .out(shifter_1_out));
  assign CLK = nand_1_out ? clock_1_out : 1'bz;  // Controlled_Buffer controlled_buffer_1
  Pull_Resistor #(.pull(1)) pull_resistor_1 (.node(CLK));
  Comparator #(.width(32), .mode("unsigned")) comparator_2 (
    .a(ID_EX_r1_2), .b(32'ha), .eq(comparator_2_eq));  // open: gt, lt
  and and_9 (and_9_out, EX_ecall, ~comparator_2_eq);  // AND_Gate
  and and_10 (and_10_out, alu_1_equal, beq);
  and and_11 (and_11_out, ~alu_1_equal, bne);  // AND_Gate
  and and_12 (and_12_out, alu_1_out_4, bge);
  ALU alu_1 (
    .X(ID_EX_r1_2), .Y(multiplexer_9_out), .AluOP(ID_EX_aluop_2), .Equal(alu_1_equal), .Result(ALU_addr),
    .out_4(alu_1_out_4));  // open: Result_2, out_6
  Adder #(.width(32)) adder_2 (.a(shifter_1_out), .b(EX_PC), .out(Branch_addr));  // open: cin, cout
  and and_13 (EX_halt, EX_ecall, comparator_2_eq);
  Register #(.width(32), .trigger("rising"), .Select("low")) register_4 (
    .D(ID_EX_r2_2), .en(and_9_out), .Q(LedData), .clk(CLK));  // open: clr
  not not_4 (not_4_out, halt);
  or or_9 (Branch_BT, and_12_out, and_11_out, and_10_out);
  or or_10 (S, Branch_BT, EX_Jal);
  Counter #(.width(16), .max('hffff), .ongoal("wrap"), .trigger("rising"), .behavior("old")) counter_2 (
    .count(not_4_out), .Q(\总周期数 ), .clk(CLK));  // open: load, D, carry, clr, preset
  Comparator #(.width(32), .mode("unsigned")) comparator_3 (.a(IF_IR), .b(32'h200073), .eq(IF_URET));  // open: gt, lt
  and and_14 (and_14_out, not_4_out, EX_J);
  EX_MEM EX_MEM (
    .MemToReg(ID_EX_memtoreg_2), .MemToReg_2(EX_MEM_memtoreg_2), .MemWrite(ID_EX_memwrite_2),
    .MemWrite_2(MemWrite), .RegWrite(EX_RegWrite), .RegWrite_2(MEM_RegWrite), .Jal(EX_Jal),
    .Jal_2(EX_MEM_jal_2), .Jalr(EX_Jalr), .Jalr_2(EX_MEM_jalr_2), .SB(EX_SB), .SB_2(MEM_SB), .rd(ID_EX_rd_2),
    .rd_2(EX_MEM_rd_2), .Reset(RST), .En(not_3_out), .CLK(CLK), .PC(EX_PC), .PC_2(M_PC), .PC_4(EX_PC_4),
    .PC_4_2(EX_MEM_pc_4_2), .IR(EX_IR), .IR_2(MEM_IR), .WriteData(ID_EX_r2_2), .WriteData_2(MDin),
    .result(ALU_addr), .result_2({EX_MEM_result_2, SB_sel}), .halt(EX_halt), .halt_2(EX_MEM_halt_2));
  Multiplexer #(.select(1), .width(32), .disabled("Z"), .enable("false")) multiplexer_10 (
    .in0(MDin), .in1(SBin), .out(MEM_Din), .sel(MEM_SB));
  Counter #(.width(16), .max('hffff), .ongoal("wrap"), .trigger("rising"), .behavior("old")) counter_3 (
    .count(and_14_out), .Q(\无条件分支数 ), .clk(CLK));  // open: load, D, carry, clr, preset
  or or_11 (MEM_str, MemWrite, MEM_SB);
  Counter #(.width(16), .max('hffff), .ongoal("wrap"), .trigger("rising"), .behavior("old")) counter_4 (
    .count(and_15_out), .Q(\条件分支成功数 ), .clk(CLK));  // open: load, D, carry, clr, preset
  and and_15 (and_15_out, not_4_out, Branch_BT);
  RAM #(.addrWidth(10), .dataWidth(32), .bus("separate"), .Select("high")) ram_1 (
    .addr(EX_MEM_result_2[11:2]), .din(MEM_Din), .data(MDout), .str(MEM_str), .sel(1'b1), .clk(CLK),
    .ld(1'b1), .clr(RST));
  \气泡流水线逻辑  \u_气泡流水线逻辑  (
    .BranchTaken(BranchTaken), .IR(ID_IR), .ecall(ecall), .rs1(\单周期硬布线控制器_1_rs1 ), .EX_RegWrite(EX_RegWrite),
    .EX_rd(ID_EX_rd_2), .rs2(\单周期硬布线控制器_1_rs2 ), .MEM_RegWrite(MEM_RegWrite), .MEM_rd(EX_MEM_rd_2),
    .stall(stall), .flush(flush));
  Counter #(.width(16), .max('hffff), .ongoal("wrap"), .trigger("rising"), .behavior("old")) counter_5 (
    .count(and_16_out), .Q(\插入气泡数 ), .clk(CLK));  // open: load, D, carry, clr, preset
  and and_16 (and_16_out, not_4_out, or_12_out);
  or or_12 (or_12_out, stall, BranchTaken);
  MEM_WB MEM_WB (
    .result({EX_MEM_result_2, SB_sel}), .result_2(MEM_WB_result_2), .MemToReg(EX_MEM_memtoreg_2),
    .ReadData(MDout), .MemToReg_2(MEM_WB_memtoreg_2[0]), .ReadData_2(MEM_WB_readdata_2), .PC(M_PC),
    .RegWrite(MEM_RegWrite), .PC_2(WB_PC), .RegWrite_2(RegWrite), .Jal(EX_MEM_jal_2), .Jal_2(MEM_WB_jal_2),
    .PC_4(EX_MEM_pc_4_2), .Jalr(EX_MEM_jalr_2), .PC_4_2(MEM_WB_pc_4_2), .Jalr_2(MEM_WB_jalr_2), .IR(MEM_IR),
    .IR_2(WB_IR), .rd(EX_MEM_rd_2), .rd_2(WB_rd), .Reset(RST), .En(not_3_out), .CLK(CLK),
    .halt(EX_MEM_halt_2), .halt_2(MEM_WB_halt_2));
  Multiplexer #(.select(2), .width(32), .disabled("Z"), .enable("false")) multiplexer_11 (
    .in0({MDout[31:8], MDin[7:0]}), .in1({MDout[31:16], MDin[7:0], MDout[7:0]}),
    .in2({MDout[31:24], MDin[7:0], MDout[15:0]}), .in3({MDin[7:0], MDout[23:0]}), .out(SBin), .sel(SB_sel));
  or or_13 (MEM_WB_memtoreg_2[1], MEM_WB_jal_2, MEM_WB_jalr_2);
  Multiplexer #(.select(2), .width(32), .disabled("Z"), .enable("false")) multiplexer_12 (
    .in0(MEM_WB_result_2), .in1(MEM_WB_readdata_2), .in2(MEM_WB_pc_4_2), .out(RDin), .sel(MEM_WB_memtoreg_2));  // open: in3
  D_Flip_Flop #(.trigger("rising"), .Pre_Clr_Positions("ABOVE_BELOW"), .NegatePresetClear("false"), .enable("true"), .NewFFLayout("true")) d_ff_8 (
    .clk(MEM_WB_halt_2), .D(1'b1), .Q(halt), .en(1'b1), .reset(Go));  // open: Qn, preset

  // Other names for the same wires on the sheet: MEM_PC[31:0] = M_PC; next_PC[31:0] = IF_PCsel;
  //   WB_RegWrite = RegWrite

  // Notes on the sheet:
  //   中断源
  //   时空图监测，可删除
  //   中断等待指示
  //   数码管输出
  //   contents of 指令存储器 (hex, n*v repeats v):
  //   7d000113 100413 1f41993 41f9d993 433 c00913 800b13 140413 f47413 800293 100313 499993 89e9b3 1300533
  //   2200893 73 406282b3 fe0294e3 140413 f00f93 1f47433 1c41413 800293 100313 49d993 89e9b3 1300533
  //   2200893 73 406282b3 fe0294e3 1c45413 406b0b33 b0463 f95ff06f 2b3 fff2c293 1029293 fff2e293 500533
  //   2200893 73 f5dff06f 1112023 410113 a12023 410113 812023 410113 1312023 410113 1412023 410113 1512023
  //   410113 1612023 410113 100b13 300a13 100a93 1600433 441413 14469b3 1300533 2200893 73 fe0416e3
  //   415a0a33 fe0a10e3 ffc10113 12b03 ffc10113 12a83 ffc10113 12a03 ffc10113 12983 ffc10113 12403
  //   ffc10113 12503 ffc10113 12883 200073 1112023 410113 a12023 410113 812023 410113 1312023 410113
  //   1412023 410113 1512023 410113 1612023 410113 200b13 300a13 100a93 1600433 441413 14469b3 1300533
  //   2200893 73 fe0416e3 415a0a33 fe0a10e3 ffc10113 12b03 ffc10113 12a83 ffc10113 12a03 ffc10113 12983
  //   ffc10113 12403 ffc10113 12503 ffc10113 12883 200073 1112023 410113 a12023 410113 812023 410113
  //   1312023 410113 1412023 410113 1512023 410113 1612023 410113 300b13 300a13 100a93 1600433 441413
  //   14469b3 1300533 2200893 73 fe0416e3 415a0a33 fe0a10e3 ffc10113 12b03 ffc10113 12a83 ffc10113 12a03
  //   ffc10113 12983 ffc10113 12403 ffc10113 12503 ffc10113 12883 200073
  //   JAL
  //   JALR
  //   SB
  //   指令字
  //   B.Inst. Imm
  //   rd
  //   Beq
  //   Bge
  //   Bne
  //   URET
  //   J.Inst. Imm
  //   MemToReg
  //   MemWrite
  //   AluOP
  //   AluSrcB
  //   RegWrite
  //   控制位
  //   暂停节拍，不能为0
  //   流水调试日志用
  //   戳工具置1进入计数暂停模式，ctrl+k时钟自动运行到对应节拍暂停
  //   ctrl+k关闭时钟连续运行，将控制位置零，进入单步调试模式调试
  //   可计数暂停的时钟源
  //   为方便自动评测，需要输出流水线各段保存的PC值，注意是PC不是PC+4，另外ID段寄存器写入信息，Mem段内存写入信息也要输出
  //   SB指令模块
endmodule
module \重定向流水线中断  (
  output RegWrite,
  output MemWrite,
  output [31:0] IF_PC,
  output [31:0] ID_PC,
  output [31:0] EX_PC,
  output [31:0] M_PC,
  output [31:0] WB_PC,
  output [31:0] RDin,
  output [31:0] MDin,
  output [31:0] LedData
);

  wire alu_1_equal, alu_1_out_4, and_1_out, and_2_out, and_3_out, and_4_out, and_5_out, and_10_out,
       and_11_out, and_12_out, and_13_out, and_14_out, and_15_out, and_16_out, and_17_out, beq, bge, bne,
       Branch_BT, BranchTaken, CLK, clock_1_out, comparator_1_eq, comparator_1_lt, comparator_2_eq, d_ff_1_q,
       d_ff_2_q, d_ff_3_q, d_ff_4_q, d_ff_5_q, d_ff_6_q, d_ff_7_q, decoder_1_out1, decoder_1_out2,
       decoder_1_out3, ecall, EX_ecall, EX_halt, EX_J, EX_Jal, EX_Jalr, EX_MEM_halt_2, EX_MEM_jal_2,
       EX_MEM_jalr_2, EX_MEM_memtoreg_2, EX_RegWrite, EX_SB, flush, Go, halt, ID_EX_alusrcb_2,
       ID_EX_memtoreg_2, ID_EX_memwrite_2, IF_URET, INT, INT_IE, INT_IR, IR1, IR2, IR3, IRAreset, IRBreset,
       IRCreset, JAL, MEM_RegWrite, MEM_SB, MEM_str, MEM_WB_halt_2, MEM_WB_jal_2, MEM_WB_jalr_2, nand_1_out,
       not_2_out, not_3_out, not_4_out, or_5_out, or_6_out, or_7_out, register_2_q, RST, S, S_type, SB,
       stall, undriven, W1, W2, W3, \单周期硬布线控制器_1_alu_src , \单周期硬布线控制器_1_beq , \单周期硬布线控制器_1_bge ,
       \单周期硬布线控制器_1_bne , \单周期硬布线控制器_1_jalr , \单周期硬布线控制器_1_memtoreg , \单周期硬布线控制器_1_memwrite ,
       \单周期硬布线控制器_1_regwrite , \单周期硬布线控制器_1_rs1 , \单周期硬布线控制器_1_rs2 ;
  wire [1:0] MEM_WB_memtoreg_2, priority_encoder_1_out, register_3_q, rs_F, rs_next, rt_F, rt_next;
  wire [3:0] ID_EX_aluop_2, \单周期硬布线控制器_1_alu_op ;
  wire [4:0] EX_MEM_rd_2, ID_EX_rd_2, multiplexer_4_out, multiplexer_5_out, WB_rd;
  wire [11:0] multiplexer_6_out;
  wire [12:0] CNT_num;
  wire [15:0] \LoadUse次数 , \总周期数 , \插入气泡数 , \无条件分支数 , \条件分支成功数 ;
  wire [31:0] ALU_addr, bit_extender_1_out, bit_extender_2_out, bit_extender_3_out, Branch_addr, EX_IR,
       EX_MEM_pc_4_2, EX_PC_4, ID_EX_imm1_2, ID_EX_imm2_2, ID_EX_r1_2, ID_EX_r2_2, ID_IR, ID_PC_4, IF_IR,
       IF_PC_4, IF_PCin, IF_PCsel, INT_PC, MDout, MEM_ALUresult, MEM_Din, MEM_IR, MEM_WB_pc_4_2,
       MEM_WB_readdata_2, MEM_WB_result_2, multiplexer_2_out, multiplexer_7_out, multiplexer_9_out,
       multiplexer_10_out, multiplexer_11_out, regifile_1_r1, regifile_1_r2, ret_PC, SBin, shifter_1_out,
       WB_IR;

  Button \u_总复位  (.out(RST));
  Button _1 (.out(IR1));
  Button _2 (.out(IR2));
  Button _3 (.out(IR3));
  // Probe on \总周期数 
  // Probe on \总周期数 
  Button \u_继续运行  (.out(Go));
  LED #(.active("true")) led_1 (.in(W1));
  LED #(.active("true")) led_2 (.in(W2));
  LED #(.active("true")) led_3 (.in(W3));
  Multiplexer #(.select(2), .width(32), .disabled("Z"), .enable("false")) multiplexer_1 (
    .in0(IF_PC_4), .in1(ALU_addr), .in2(Branch_addr), .out(IF_PCsel), .sel({S, EX_Jalr}));  // open: in3
  and and_1 (and_1_out, ~stall, ~halt);  // AND_Gate
  or or_1 (W1, d_ff_1_q, d_ff_4_q);
  or or_2 (W2, d_ff_2_q, d_ff_5_q);
  or or_3 (W3, d_ff_3_q, d_ff_6_q);
  Hex_Digit_Display hex_digit_display_1 (.value(LedData[31:28]));  // open: dp
  // Probe on IF_PC[19:0]
  // RiscV_Probe riscv_probe_1: pin names not known; wires that end beside it: IF_IR
  Multiplexer #(.select(1), .width(32), .disabled("Z"), .enable("false")) multiplexer_2 (
    .in0(IF_PCsel), .in1(INT_PC), .out(multiplexer_2_out), .sel(INT));
  Register #(.width(32), .trigger("rising"), .Select("low")) PC (
    .D(IF_PCin), .en(and_1_out), .Q(IF_PC), .clk(CLK), .clr(RST));
  Hex_Digit_Display hex_digit_display_2 (.value(LedData[27:24]));  // open: dp
  Hex_Digit_Display hex_digit_display_3 (.value(LedData[23:20]));  // open: dp
  Multiplexer #(.select(1), .width(32), .disabled("Z"), .enable("false")) multiplexer_3 (
    .in0(multiplexer_2_out), .in1(ret_PC), .out(IF_PCin), .sel(IF_URET));
  Adder #(.width(32)) adder_1 (.a(IF_PC), .b(32'h4), .out(IF_PC_4));  // open: cin, cout
  Register #(.width(1), .trigger("falling"), .Select("low")) register_1 (
    .D(and_2_out), .Q(INT), .clk(CLK));  // open: en, clr
  and and_2 (and_2_out, INT_IR, INT_IE);
  Hex_Digit_Display hex_digit_display_4 (.value(LedData[15:12]));  // open: dp
  Hex_Digit_Display hex_digit_display_5 (.value(LedData[19:16]));  // open: dp
  // Probe on ID_PC[19:0]
  // RiscV_Probe riscv_probe_2: pin names not known; wires that end beside it: ID_IR
  \重定向处理逻辑  \u_重定向处理逻辑_1  (
    .BranchTaken(BranchTaken), .IR(ID_IR), .ecall(ecall), .rs_av(\单周期硬布线控制器_1_rs1 ),
    .EX_RegWrite(EX_RegWrite), .EX_rd(ID_EX_rd_2), .rt_av(\单周期硬布线控制器_1_rs2 ), .MEM_RegWrite(MEM_RegWrite),
    .MEM_rd(EX_MEM_rd_2), .stall(stall), .flush(flush), .EX_MemToReg(ID_EX_memtoreg_2), .rs1Forward(rs_next),
    .rs2Forward(rt_next));
  or or_4 (EX_J, EX_Jal, EX_Jalr);
  D_Flip_Flop #(.trigger("rising"), .Pre_Clr_Positions("LEGACY"), .NegatePresetClear("false"), .enable("true"), .NewFFLayout("false")) d_ff_1 (
    .clk(IR1), .D(1'b1), .Q(d_ff_1_q), .reset(d_ff_4_q));  // open: Qn, preset, en
  or or_5 (or_5_out, d_ff_1_q, d_ff_4_q);
  D_Flip_Flop #(.trigger("rising"), .Pre_Clr_Positions("LEGACY"), .NegatePresetClear("false"), .enable("true"), .NewFFLayout("false")) d_ff_2 (
    .clk(IR2), .D(1'b1), .Q(d_ff_2_q), .reset(d_ff_5_q));  // open: Qn, preset, en
  or or_6 (or_6_out, d_ff_2_q, d_ff_5_q);
  D_Flip_Flop #(.trigger("rising"), .Pre_Clr_Positions("LEGACY"), .NegatePresetClear("false"), .enable("true"), .NewFFLayout("false")) d_ff_3 (
    .clk(IR3), .D(1'b1), .Q(d_ff_3_q), .reset(d_ff_6_q));  // open: Qn, preset, en
  or or_7 (or_7_out, d_ff_3_q, d_ff_6_q);
  Hex_Digit_Display hex_digit_display_6 (.value(LedData[11:8]));  // open: dp
  Hex_Digit_Display hex_digit_display_7 (.value(LedData[7:4]));  // open: dp
  // Probe on EX_PC[19:0]
  // RiscV_Probe riscv_probe_3: pin names not known; wires that end beside it: EX_IR
  ROM #(.addrWidth(10), .dataWidth(32), .Select("high")) \u_指令存储器  (.addr(IF_PC[11:2]), .data(IF_IR));
  Register #(.width(32), .trigger("rising"), .Select("low")) mEPC (
    .D(IF_PCsel), .en(INT), .Q(ret_PC), .clk(CLK));  // open: clr
  and and_3 (and_3_out, or_5_out, ~IRAreset);  // AND_Gate
  and and_4 (and_4_out, or_6_out, ~IRBreset);  // AND_Gate
  and and_5 (and_5_out, or_7_out, ~IRCreset);  // AND_Gate
  Hex_Digit_Display hex_digit_display_8 (.value(LedData[3:0]));  // open: dp
  or or_8 (BranchTaken, S, EX_Jalr);
  IF_ID IF_ID (
    .IR(IF_IR), .PC(IF_PC), .PC_4(IF_PC_4), .IR_2(ID_IR), .PC_2(ID_PC), .PC_4_2(ID_PC_4), .Reset(RST),
    .BranchTaken(BranchTaken), .En(and_1_out), .CLK(CLK));  // open: PredictJump, PredictJump_2
  D_Flip_Flop #(.trigger("rising"), .Pre_Clr_Positions("LEGACY"), .NegatePresetClear("false"), .enable("true"), .NewFFLayout("false")) d_ff_4 (
    .clk(CLK), .D(and_3_out), .Q(d_ff_4_q));  // open: Qn, preset, en, reset
  D_Flip_Flop #(.trigger("rising"), .Pre_Clr_Positions("LEGACY"), .NegatePresetClear("false"), .enable("true"), .NewFFLayout("false")) d_ff_5 (
    .clk(CLK), .D(and_4_out), .Q(d_ff_5_q));  // open: Qn, preset, en, reset
  D_Flip_Flop #(.trigger("rising"), .Pre_Clr_Positions("LEGACY"), .NegatePresetClear("false"), .enable("true"), .NewFFLayout("false")) d_ff_6 (
    .clk(CLK), .D(and_5_out), .Q(d_ff_6_q));  // open: Qn, preset, en, reset
  // Probe on M_PC[19:0]
  // RiscV_Probe riscv_probe_4: pin names not known; wires that end beside it: MEM_IR
  Register #(.width(1), .trigger("falling"), .Select("low")) register_2 (
    .D(1'b0), .en(IF_URET), .Q(register_2_q), .clk(CLK), .preset(INT));  // open: clr, cs
  // Probe on \总周期数 
  // Probe on \总周期数 
  // Probe on \无条件分支数 
  // Probe on \条件分支成功数 
  // Probe on \插入气泡数 
  // Probe on \LoadUse次数 
  \单周期硬布线控制器  \u_单周期硬布线控制器_1  (
    .Funct({ID_IR[30], ID_IR[25], ID_IR[14:12]}), .OP(ID_IR[6:2]), .ALU_OP(\单周期硬布线控制器_1_alu_op ),
    .MemToReg(\单周期硬布线控制器_1_memtoreg ), .MemWrite(\单周期硬布线控制器_1_memwrite ), .ALU_SRC(\单周期硬布线控制器_1_alu_src ),
    .RegWrite(\单周期硬布线控制器_1_regwrite ), .ecall(ecall), .S_type(S_type), .Jalr(\单周期硬布线控制器_1_jalr ),
    .Beq(\单周期硬布线控制器_1_beq ), .JAL(JAL), .Bne(\单周期硬布线控制器_1_bne ), .in_3(ID_IR[21]), .BGE(\单周期硬布线控制器_1_bge ),
    .SB(SB), .rs1(\单周期硬布线控制器_1_rs1 ), .rs2(\单周期硬布线控制器_1_rs2 ));  // open: uret, csrrsi, csrrci
  Multiplexer #(.select(1), .width(5), .disabled("Z"), .enable("false")) multiplexer_4 (
    .in0(ID_IR[19:15]), .in1(5'b10001), .out(multiplexer_4_out), .sel(ecall));
  Multiplexer #(.select(1), .width(5), .disabled("Z"), .enable("false")) multiplexer_5 (
    .in0(ID_IR[24:20]), .in1(5'b01010), .out(multiplexer_5_out), .sel(ecall));
  Multiplexer #(.select(1), .width(12), .disabled("Z"), .enable("false")) multiplexer_6 (
    .in0(ID_IR[31:20]), .in1({ID_IR[31:25], ID_IR[11:7]}), .out(multiplexer_6_out), .sel(S_type));
  not not_1 (INT_IE, register_2_q);
  Priority_Encoder #(.select(2), .disabled("Z")) priority_encoder_1 (
    .in0(1'b0), .in1(d_ff_4_q), .in2(d_ff_5_q), .in3(d_ff_6_q), .out(priority_encoder_1_out), .gs(INT_IR));  // open: en_out, en_in
  // Probe on IF_PC[11:0]
  // Probe on WB_PC[19:0]
  // RiscV_Probe riscv_probe_5: pin names not known; wires that end beside it: WB_IR
  assign bit_extender_1_out = {{20{multiplexer_6_out[11]}}, multiplexer_6_out};  // Bit_Extender bit_extender_1
  assign bit_extender_2_out = {{20{ID_IR[31]}}, {ID_IR[31], ID_IR[7], ID_IR[30:25], ID_IR[11:8]}};  // Bit_Extender bit_extender_2
  Multiplexer #(.select(1), .width(32), .disabled("Z"), .enable("false")) multiplexer_7 (
    .in0(bit_extender_2_out), .in1(bit_extender_3_out), .out(multiplexer_7_out), .sel(JAL));
  assign bit_extender_3_out = {{12{ID_IR[31]}}, {ID_IR[31], ID_IR[19:12], ID_IR[20], ID_IR[30:21]}};  // Bit_Extender bit_extender_3
  // Probe on undriven
  // Probe on ID_PC[11:0]
  not not_2 (not_2_out, CLK);
  Regifile regifile_1 (
    .Din(RDin), .Clk(not_2_out), .R1(regifile_1_r1), .R2(regifile_1_r2), .WE(RegWrite), .W_num(WB_rd),
    .R1_num(multiplexer_4_out), .R2_num(multiplexer_5_out));
  not not_3 (not_3_out, halt);
  Multiplexer #(.select(2), .width(32), .disabled("Z"), .enable("false")) multiplexer_8 (
    .in1(32'h30ac), .in2(32'h3150), .in3(32'h31f4), .out(INT_PC), .sel(priority_encoder_1_out));  // open: in0
  // Probe on M_PC[11:0]
  // Probe on EX_PC[11:0]
  D_Flip_Flop #(.trigger("high"), .Pre_Clr_Positions("LEGACY"), .NegatePresetClear("false"), .enable("true"), .NewFFLayout("false")) d_ff_7 (.Q(d_ff_7_q));  // open: clk, D, Qn, preset, en, reset
  // Probe on 13'hc
  Register #(.width(2), .trigger("rising"), .Select("low")) register_3 (
    .D(priority_encoder_1_out), .Q(register_3_q), .clk(INT));  // open: en, clr
  Decoder #(.select(2), .tristate("false"), .disabled("Z"), .enable("false")) decoder_1 (
    .out1(decoder_1_out1), .out2(decoder_1_out2), .out3(decoder_1_out3), .sel(register_3_q));  // open: out0
  // Probe on WB_PC[11:0]
  Comparator #(.width(13), .mode("twosComplement")) comparator_1 (
    .a(CNT_num), .b(13'hc), .eq(comparator_1_eq), .lt(comparator_1_lt));  // open: gt
  Clock #(.highDuration(1), .lowDuration(1)) clock_1 (.out(clock_1_out));
  Counter #(.width(13), .max('h1fff), .ongoal("stay"), .trigger("rising"), .behavior("old")) counter_1 (
    .count(comparator_1_lt), .Q(CNT_num), .clk(clock_1_out));  // open: load, D, carry, clr, preset
  ID_EX ID_EX (
    .Beq(\单周期硬布线控制器_1_beq ), .Beq_2(beq), .Bne(\单周期硬布线控制器_1_bne ), .Bne_2(bne), .Bge(\单周期硬布线控制器_1_bge ),
    .Bge_2(bge), .MemToReg(\单周期硬布线控制器_1_memtoreg ), .MemToReg_2(ID_EX_memtoreg_2),
    .MemWrite(\单周期硬布线控制器_1_memwrite ), .MemWrite_2(ID_EX_memwrite_2), .AluSrcB(\单周期硬布线控制器_1_alu_src ),
    .AluSrcB_2(ID_EX_alusrcb_2), .RegWrite_2(EX_RegWrite), .RegWrite(\单周期硬布线控制器_1_regwrite ), .Ecall(ecall),
    .Ecall_2(EX_ecall), .Jal_2(EX_Jal), .Jal(JAL), .Jalr(\单周期硬布线控制器_1_jalr ), .Jalr_2(EX_Jalr), .SB(SB),
    .SB_2(EX_SB), .Reset(RST), .flush(flush), .En(not_3_out), .CLK(CLK), .AluOp(\单周期硬布线控制器_1_alu_op ),
    .AluOp_2(ID_EX_aluop_2), .rd(ID_IR[11:7]), .rd_2(ID_EX_rd_2), .R1(regifile_1_r1), .R1_2(ID_EX_r1_2),
    .R2(regifile_1_r2), .R2_2(ID_EX_r2_2), .imm1(bit_extender_1_out), .imm1_2(ID_EX_imm1_2),
    .imm2(multiplexer_7_out), .imm2_2(ID_EX_imm2_2), .PC(ID_PC), .PC_2(EX_PC), .PC_4(ID_PC_4),
    .PC_4_2(EX_PC_4), .IR(ID_IR), .IR_2(EX_IR), .rs1forward(rs_next), .rs1forward_2(rs_F),
    .rs2forward(rt_next), .rs2forward_2(rt_F));  // open: PredictJump, PredictJump_2, branch, branch_2
  and and_6 (IRAreset, decoder_1_out1, IF_URET);
  and and_7 (IRBreset, decoder_1_out2, IF_URET);
  and and_8 (IRCreset, decoder_1_out3, IF_URET);
  nand nand_1 (nand_1_out, d_ff_7_q, comparator_1_eq);
  Multiplexer #(.select(2), .width(32), .disabled("Z"), .enable("false")) multiplexer_9 (
    .in0(ID_EX_r1_2), .in1(RDin), .in2(MEM_ALUresult), .out(multiplexer_9_out), .sel(rs_F));  // open: in3
  Multiplexer #(.select(2), .width(32), .disabled("Z"), .enable("false")) multiplexer_10 (
    .in0(ID_EX_r2_2), .in1(RDin), .in2(MEM_ALUresult), .out(multiplexer_10_out), .sel(rt_F));  // open: in3
  assign CLK = nand_1_out ? clock_1_out : 1'bz;  // Controlled_Buffer controlled_buffer_1
  Pull_Resistor #(.pull(1)) pull_resistor_1 (.node(CLK));
  Multiplexer #(.select(1), .width(32), .disabled("Z"), .enable("false")) multiplexer_11 (
    .in0(multiplexer_10_out), .in1(ID_EX_imm1_2), .out(multiplexer_11_out), .sel(ID_EX_alusrcb_2));
  Shifter #(.width(32), .shift("ll")) shifter_1 (.in(ID_EX_imm2_2), .\dist (5'b00001), .out(shifter_1_out));
  Comparator #(.width(32), .mode("unsigned")) comparator_2 (
    .a(multiplexer_9_out), .b(32'ha), .eq(comparator_2_eq));  // open: gt, lt
  and and_9 (EX_halt, EX_ecall, comparator_2_eq);
  Register #(.width(32), .trigger("rising"), .Select("low")) register_4 (
    .D(multiplexer_10_out), .en(and_10_out), .Q(LedData), .clk(CLK));  // open: clr
  and and_10 (and_10_out, EX_ecall, ~comparator_2_eq);  // AND_Gate
  Counter #(.width(16), .max('hffff), .ongoal("wrap"), .trigger("rising"), .behavior("old")) counter_2 (
    .count(not_4_out), .Q(\总周期数 ), .clk(CLK));  // open: load, D, carry, clr, preset
  not not_4 (not_4_out, halt);
  and and_11 (and_11_out, alu_1_equal, beq);
  and and_12 (and_12_out, ~alu_1_equal, bne);  // AND_Gate
  and and_13 (and_13_out, alu_1_out_4, bge);
  or or_9 (Branch_BT, and_13_out, and_12_out, and_11_out);
  ALU alu_1 (
    .X(multiplexer_9_out), .Y(multiplexer_11_out), .AluOP(ID_EX_aluop_2), .Equal(alu_1_equal),
    .Result(ALU_addr), .out_4(alu_1_out_4));  // open: Result_2, out_6
  Adder #(.width(32)) adder_2 (.a(shifter_1_out), .b(EX_PC), .out(Branch_addr));  // open: cin, cout
  Comparator #(.width(32), .mode("unsigned")) comparator_3 (.a(IF_IR), .b(32'h200073), .eq(IF_URET));  // open: gt, lt
  or or_10 (S, Branch_BT, EX_Jal);
  Counter #(.width(16), .max('hffff), .ongoal("wrap"), .trigger("rising"), .behavior("old")) counter_3 (
    .count(and_14_out), .Q(\无条件分支数 ), .clk(CLK));  // open: load, D, carry, clr, preset
  and and_14 (and_14_out, not_4_out, EX_J);
  EX_MEM EX_MEM (
    .MemToReg(ID_EX_memtoreg_2), .MemToReg_2(EX_MEM_memtoreg_2), .MemWrite(ID_EX_memwrite_2),
    .MemWrite_2(MemWrite), .RegWrite(EX_RegWrite), .RegWrite_2(MEM_RegWrite), .Jal(EX_Jal),
    .Jal_2(EX_MEM_jal_2), .Jalr(EX_Jalr), .Jalr_2(EX_MEM_jalr_2), .SB(EX_SB), .SB_2(MEM_SB), .rd(ID_EX_rd_2),
    .rd_2(EX_MEM_rd_2), .Reset(RST), .En(not_3_out), .CLK(CLK), .PC(EX_PC), .PC_2(M_PC), .PC_4(EX_PC_4),
    .PC_4_2(EX_MEM_pc_4_2), .IR(EX_IR), .IR_2(MEM_IR), .WriteData(multiplexer_10_out), .WriteData_2(MDin),
    .result(ALU_addr), .result_2(MEM_ALUresult), .halt(EX_halt), .halt_2(EX_MEM_halt_2));
  Multiplexer #(.select(1), .width(32), .disabled("Z"), .enable("false")) multiplexer_12 (
    .in0(MDin), .in1(SBin), .out(MEM_Din), .sel(MEM_SB));
  and and_15 (and_15_out, not_4_out, Branch_BT);
  or or_11 (MEM_str, MemWrite, MEM_SB);
  Counter #(.width(16), .max('hffff), .ongoal("wrap"), .trigger("rising"), .behavior("old")) counter_4 (
    .count(and_15_out), .Q(\条件分支成功数 ), .clk(CLK));  // open: load, D, carry, clr, preset
  and and_16 (and_16_out, not_4_out, BranchTaken);
  RAM #(.addrWidth(10), .dataWidth(32), .bus("separate"), .Select("high")) ram_1 (
    .addr(MEM_ALUresult[11:2]), .din(MEM_Din), .data(MDout), .str(MEM_str), .sel(1'b1), .clk(CLK), .ld(1'b1),
    .clr(RST));
  Counter #(.width(16), .max('hffff), .ongoal("wrap"), .trigger("rising"), .behavior("old")) counter_5 (
    .count(and_16_out), .Q(\插入气泡数 ), .clk(CLK));  // open: load, D, carry, clr, preset
  and and_17 (and_17_out, not_4_out, stall);
  Multiplexer #(.select(2), .width(32), .disabled("Z"), .enable("false")) multiplexer_13 (
    .in0({MDout[31:8], MDin[7:0]}), .in1({MDout[31:16], MDin[7:0], MDout[7:0]}),
    .in2({MDout[31:24], MDin[7:0], MDout[15:0]}), .in3({MDin[7:0], MDout[23:0]}), .out(SBin),
    .sel(MEM_ALUresult[1:0]));
  Counter #(.width(16), .max('hffff), .ongoal("wrap"), .trigger("rising"), .behavior("old")) counter_6 (
    .count(and_17_out), .Q(\LoadUse次数 ), .clk(CLK));  // open: load, D, carry, clr, preset
  MEM_WB MEM_WB (
    .result(MEM_ALUresult), .result_2(MEM_WB_result_2), .MemToReg(EX_MEM_memtoreg_2), .ReadData(MDout),
    .MemToReg_2(MEM_WB_memtoreg_2[0]), .ReadData_2(MEM_WB_readdata_2), .PC(M_PC), .RegWrite(MEM_RegWrite),
    .PC_2(WB_PC), .RegWrite_2(RegWrite), .Jal(EX_MEM_jal_2), .Jal_2(MEM_WB_jal_2), .PC_4(EX_MEM_pc_4_2),
    .Jalr(EX_MEM_jalr_2), .PC_4_2(MEM_WB_pc_4_2), .Jalr_2(MEM_WB_jalr_2), .IR(MEM_IR), .IR_2(WB_IR),
    .rd(EX_MEM_rd_2), .rd_2(WB_rd), .Reset(RST), .En(not_3_out), .CLK(CLK), .halt(EX_MEM_halt_2),
    .halt_2(MEM_WB_halt_2));
  or or_12 (MEM_WB_memtoreg_2[1], MEM_WB_jal_2, MEM_WB_jalr_2);
  Multiplexer #(.select(2), .width(32), .disabled("Z"), .enable("false")) multiplexer_14 (
    .in0(MEM_WB_result_2), .in1(MEM_WB_readdata_2), .in2(MEM_WB_pc_4_2), .out(RDin), .sel(MEM_WB_memtoreg_2));  // open: in3
  D_Flip_Flop #(.trigger("rising"), .Pre_Clr_Positions("ABOVE_BELOW"), .NegatePresetClear("false"), .enable("true"), .NewFFLayout("true")) d_ff_8 (
    .clk(MEM_WB_halt_2), .D(1'b1), .Q(halt), .en(1'b1), .reset(Go));  // open: Qn, preset

  // Other names for the same wires on the sheet: SB_sel[1:0] = MEM_ALUresult[1:0]; MEM_PC[31:0] = M_PC;
  //   next_PC[31:0] = IF_PCsel; WB_RegWrite = RegWrite

  // Notes on the sheet:
  //   中断源
  //   中断等待指示
  //   时空图监测，可删除
  //   数码管输出
  //   contents of 指令存储器 (hex, n*v repeats v):
  //   7d000113 100413 1f41993 41f9d993 433 c00913 800b13 140413 f47413 800293 100313 499993 89e9b3 1300533
  //   2200893 73 406282b3 fe0294e3 140413 f00f93 1f47433 1c41413 800293 100313 49d993 89e9b3 1300533
  //   2200893 73 406282b3 fe0294e3 1c45413 406b0b33 b0463 f95ff06f 2b3 fff2c293 1029293 fff2e293 500533
  //   2200893 73 f5dff06f 1112023 410113 a12023 410113 812023 410113 1312023 410113 1412023 410113 1512023
  //   410113 1612023 410113 100b13 300a13 100a93 1600433 441413 14469b3 1300533 2200893 73 fe0416e3
  //   415a0a33 fe0a10e3 ffc10113 12b03 ffc10113 12a83 ffc10113 12a03 ffc10113 12983 ffc10113 12403
  //   ffc10113 12503 ffc10113 12883 200073 1112023 410113 a12023 410113 812023 410113 1312023 410113
  //   1412023 410113 1512023 410113 1612023 410113 200b13 300a13 100a93 1600433 441413 14469b3 1300533
  //   2200893 73 fe0416e3 415a0a33 fe0a10e3 ffc10113 12b03 ffc10113 12a83 ffc10113 12a03 ffc10113 12983
  //   ffc10113 12403 ffc10113 12503 ffc10113 12883 200073 1112023 410113 a12023 410113 812023 410113
  //   1312023 410113 1412023 410113 1512023 410113 1612023 410113 300b13 300a13 100a93 1600433 441413
  //   14469b3 1300533 2200893 73 fe0416e3 415a0a33 fe0a10e3 ffc10113 12b03 ffc10113 12a83 ffc10113 12a03
  //   ffc10113 12983 ffc10113 12403 ffc10113 12503 ffc10113 12883 200073
  //   指令字
  //   JAL
  //   JALR
  //   URET
  //   SB
  //   B.Inst. Imm
  //   J.Inst. Imm
  //   rd
  //   Beq
  //   Bge
  //   Bne
  //   MemToReg
  //   MemWrite
  //   AluOP
  //   AluSrcB
  //   RegWrite
  //   控制位
  //   暂停节拍，不能为0
  //   流水调试日志用
  //   戳工具置1进入计数暂停模式，ctrl+k时钟自动运行到对应节拍暂停
  //   ctrl+k关闭时钟连续运行，将控制位置零，进入单步调试模式调试
  //   可计数暂停的时钟源
  //   为方便自动评测，需要输出流水线各段保存的PC值，注意是PC不是PC+4，另外ID段寄存器写入信息，Mem段内存写入信息也要输出
  //   SB指令模块
endmodule

module \分支历史表BPB  (
  input  [31:0] PC,
  input  [31:0] EX_PC,
  input  EX_Branch,
  input  EX_BranchTaken,
  input  [31:0] EX_BranchAddr,
  input  CLK,
  output PredictJump,
  output [31:0] JumpAddr
);

  wire and_17_out, and_18_out, and_19_out, and_20_out, and_21_out, and_22_out, and_23_out, and_24_out,
       and_25_out, comparator_1_eq, comparator_2_eq, comparator_3_eq, comparator_4_eq, comparator_5_eq,
       comparator_6_eq, comparator_7_eq, comparator_8_eq, comparator_9_eq, comparator_10_eq,
       comparator_11_eq, comparator_12_eq, comparator_13_eq, comparator_14_eq, comparator_15_eq,
       comparator_16_eq, Full, L0, L1, L2, L3, L4, L5, L6, L7, Miss, not_2_out, not_3_out, not_4_out,
       not_5_out, not_6_out, not_7_out, not_8_out, not_9_out, not_10_out, or_1_out, or_2_out, or_3_out,
       or_4_out, or_5_out, or_6_out, or_7_out, or_8_out, or_9_out, V0, V1, V2, V3, V4, V5, V6, V7, write0,
       write1, write2, write3, write4, write5, write6, write7, \行0 , \行1 , \行2 , \行3 , \行4 , \行5 , \行6 , \行7 ;
  wire [0:0] multiplexer_2_out;
  wire [1:0] multiplexer_1_out, multiplexer_6_out, multiplexer_7_out, multiplexer_8_out, multiplexer_9_out,
       multiplexer_10_out, multiplexer_11_out, multiplexer_12_out, multiplexer_13_out, multiplexer_14_out,
       Next, Predict0, Predict1, Predict2, Predict3, Predict4, Predict5, Predict6, Predict7;
  wire [2:0] \max归并比较_1_max_num , \max归并比较_2_max_num , \max归并比较_3_max_num , \max归并比较_4_max_num ,
       \max归并比较_5_max_num , \max归并比较_6_max_num , multiplexer_3_out, out, priority_encoder_1_out,
       priority_encoder_2_out, priority_encoder_3_out;
  wire [15:0] C0, C1, C2, C3, C4, C5, C6, C7, \max归并比较_1_max , \max归并比较_2_max , \max归并比较_3_max ,
       \max归并比较_4_max , \max归并比较_5_max , \max归并比较_6_max ;
  wire [31:0] adder_1_out, Addr0, Addr1, Addr2, Addr3, Addr4, Addr5, Addr6, Addr7, multiplexer_4_out, tag0,
       tag1, tag2, tag3, tag4, tag5, tag6, tag7;

  Comparator #(.width(32), .mode("unsigned")) comparator_1 (.a(tag0), .b(PC), .eq(comparator_1_eq));  // open: gt, lt
  Comparator #(.width(32), .mode("unsigned")) comparator_2 (.a(tag1), .b(PC), .eq(comparator_2_eq));  // open: gt, lt
  Comparator #(.width(32), .mode("unsigned")) comparator_3 (.a(tag2), .b(PC), .eq(comparator_3_eq));  // open: gt, lt
  Comparator #(.width(32), .mode("unsigned")) comparator_4 (.a(tag3), .b(PC), .eq(comparator_4_eq));  // open: gt, lt
  Comparator #(.width(32), .mode("unsigned")) comparator_5 (.a(tag4), .b(PC), .eq(comparator_5_eq));  // open: gt, lt
  Comparator #(.width(32), .mode("unsigned")) comparator_6 (.a(tag5), .b(PC), .eq(comparator_6_eq));  // open: gt, lt
  Comparator #(.width(32), .mode("unsigned")) comparator_7 (.a(tag6), .b(PC), .eq(comparator_7_eq));  // open: gt, lt
  Comparator #(.width(32), .mode("unsigned")) comparator_8 (.a(tag7), .b(PC), .eq(comparator_8_eq));  // open: gt, lt
  Comparator #(.width(32), .mode("unsigned")) comparator_9 (.a(tag0), .b(EX_PC), .eq(comparator_9_eq));  // open: gt, lt
  Comparator #(.width(32), .mode("unsigned")) comparator_10 (
    .a(tag1), .b(EX_PC), .eq(comparator_10_eq));  // open: gt, lt
  Comparator #(.width(32), .mode("unsigned")) comparator_11 (
    .a(tag2), .b(EX_PC), .eq(comparator_11_eq));  // open: gt, lt
  Comparator #(.width(32), .mode("unsigned")) comparator_12 (
    .a(tag3), .b(EX_PC), .eq(comparator_12_eq));  // open: gt, lt
  Comparator #(.width(32), .mode("unsigned")) comparator_13 (
    .a(tag4), .b(EX_PC), .eq(comparator_13_eq));  // open: gt, lt
  Comparator #(.width(32), .mode("unsigned")) comparator_14 (
    .a(tag5), .b(EX_PC), .eq(comparator_14_eq));  // open: gt, lt
  Comparator #(.width(32), .mode("unsigned")) comparator_15 (
    .a(tag6), .b(EX_PC), .eq(comparator_15_eq));  // open: gt, lt
  Comparator #(.width(32), .mode("unsigned")) comparator_16 (
    .a(tag7), .b(EX_PC), .eq(comparator_16_eq));  // open: gt, lt
  and and_1 (L0, comparator_1_eq, V0);
  and and_2 (L1, comparator_2_eq, V1);
  and and_3 (L2, comparator_3_eq, V2);
  and and_4 (L3, comparator_4_eq, V3);
  and and_5 (L4, comparator_5_eq, V4);
  and and_6 (L5, comparator_6_eq, V5);
  and and_7 (L6, comparator_7_eq, V6);
  and and_8 (L7, comparator_8_eq, V7);
  and and_9 (\行0 , comparator_9_eq, V0);
  and and_10 (\行1 , comparator_10_eq, V1);
  and and_11 (\行2 , comparator_11_eq, V2);
  and and_12 (\行3 , comparator_12_eq, V3);
  and and_13 (\行4 , comparator_13_eq, V4);
  and and_14 (\行5 , comparator_14_eq, V5);
  and and_15 (\行6 , comparator_15_eq, V6);
  and and_16 (\行7 , comparator_16_eq, V7);
  Priority_Encoder #(.select(3), .disabled("Z")) priority_encoder_1 (
    .in0(\行0 ), .in1(\行1 ), .in2(\行2 ), .in3(\行3 ), .in4(\行4 ), .in5(\行5 ), .in6(\行6 ), .in7(\行7 ),
    .out(priority_encoder_1_out), .en_in(1'b1));  // open: gs, en_out
  Pull_Resistor #(.pull(0)) pull_resistor_1 (.node(priority_encoder_1_out));
  Multiplexer #(.select(3), .width(2), .disabled("Z"), .enable("false")) multiplexer_1 (
    .in0(Predict0), .in1(Predict1), .in2(Predict2), .in3(Predict3), .in4(Predict4), .in5(Predict5),
    .in6(Predict6), .in7(Predict7), .out(multiplexer_1_out), .sel(priority_encoder_1_out));
  Priority_Encoder #(.select(3), .disabled("Z")) priority_encoder_2 (
    .in0(L0), .in1(L1), .in2(L2), .in3(L3), .in4(L4), .in5(L5), .in6(L6), .in7(L7),
    .out(priority_encoder_2_out), .en_in(1'b1));  // open: gs, en_out
  or or_1 (or_1_out, \行0 , \行1 , \行2 , \行3 , \行4 , \行5 , \行6 , \行7 );
  not not_1 (Miss, or_1_out);
  not not_2 (not_2_out, V0);
  not not_3 (not_3_out, V1);
  not not_4 (not_4_out, V2);
  Priority_Encoder #(.select(3), .disabled("Z")) priority_encoder_3 (
    .in0(not_2_out), .in1(not_3_out), .in2(not_4_out), .in3(not_5_out), .in4(not_6_out), .in5(not_7_out),
    .in6(not_8_out), .in7(not_9_out), .out(priority_encoder_3_out), .en_out(Full), .en_in(1'b1));  // open: gs
  not not_5 (not_5_out, V3);
  not not_6 (not_6_out, V4);
  not not_7 (not_7_out, V5);
  not not_8 (not_8_out, V6);
  not not_9 (not_9_out, V7);
  Multiplexer #(.select(3), .width(2), .disabled("Z"), .enable("false")) multiplexer_2 (
    .in0(Predict0), .in1(Predict1), .in2(Predict2), .in3(Predict3), .in4(Predict4), .in5(Predict5),
    .in6(Predict6), .in7(Predict7), .out({PredictJump, multiplexer_2_out[0]}), .sel(priority_encoder_2_out));
  Pull_Resistor #(.pull(0)) pull_resistor_2 (.node(PredictJump));
  FSM fsm_1 (.x(multiplexer_1_out[1]), .x2(Next[1]), .y(multiplexer_1_out[0]), .J(EX_BranchTaken), .y2(Next[0]));
  not not_10 (not_10_out, PredictJump);
  Demultiplexer #(.select(3), .width(1), .tristate("false"), .disabled("Z"), .enable("false")) demultiplexer_1 (
    .out0(write0), .out1(write1), .out2(write2), .out3(write3), .out4(write4), .out5(write5), .out6(write6),
    .out7(write7), .in(and_17_out), .sel(multiplexer_3_out));
  and and_17 (and_17_out, Miss, EX_Branch);
  Multiplexer #(.select(1), .width(3), .disabled("Z"), .enable("false")) multiplexer_3 (
    .in0(priority_encoder_3_out), .in1(out), .out(multiplexer_3_out), .sel(Full));
  Multiplexer #(.select(3), .width(32), .disabled("Z"), .enable("false")) multiplexer_4 (
    .in0(Addr0), .in1(Addr1), .in2(Addr2), .in3(Addr3), .in4(Addr4), .in5(Addr5), .in6(Addr6), .in7(Addr7),
    .out(multiplexer_4_out), .sel(priority_encoder_2_out));
  Multiplexer #(.select(1), .width(32), .disabled("Z"), .enable("false")) multiplexer_5 (
    .in0(multiplexer_4_out), .in1(adder_1_out), .out(JumpAddr), .sel(not_10_out));
  Adder #(.width(32)) adder_1 (.a(PC), .b(32'h4), .out(adder_1_out));  // open: cin, cout
  or or_2 (or_2_out, write0, L0);
  or or_3 (or_3_out, write1, L1);
  or or_4 (or_4_out, write2, L2);
  or or_5 (or_5_out, write3, L3);
  or or_6 (or_6_out, write4, L4);
  or or_7 (or_7_out, write5, L5);
  or or_8 (or_8_out, write6, L6);
  or or_9 (or_9_out, write7, L7);
  Register #(.width(1), .trigger("rising"), .Select("low")) register_1 (
    .D(1'b1), .en(write0), .Q(V0), .clk(CLK));  // open: clr
  Register #(.width(1), .trigger("rising"), .Select("low")) register_2 (
    .D(1'b1), .en(write1), .Q(V1), .clk(CLK));  // open: clr
  Register #(.width(1), .trigger("rising"), .Select("low")) register_3 (
    .D(1'b1), .en(write2), .Q(V2), .clk(CLK));  // open: clr
  Register #(.width(1), .trigger("rising"), .Select("low")) register_4 (
    .D(1'b1), .en(write3), .Q(V3), .clk(CLK));  // open: clr
  Register #(.width(1), .trigger("rising"), .Select("low")) register_5 (
    .D(1'b1), .en(write4), .Q(V4), .clk(CLK));  // open: clr
  Register #(.width(1), .trigger("rising"), .Select("low")) register_6 (
    .D(1'b1), .en(write5), .Q(V5), .clk(CLK));  // open: clr
  Register #(.width(1), .trigger("rising"), .Select("low")) register_7 (
    .D(1'b1), .en(write6), .Q(V6), .clk(CLK));  // open: clr
  Register #(.width(1), .trigger("rising"), .Select("low")) register_8 (
    .D(1'b1), .en(write7), .Q(V7), .clk(CLK));  // open: clr
  Counter #(.width(16), .max('hffff), .ongoal("wrap"), .trigger("rising"), .behavior("new")) counter_1 (
    .load(or_2_out), .D({16{1'b0}}), .Q(C0), .clk(CLK));  // open: count, carry, clr, preset, down
  Counter #(.width(16), .max('hffff), .ongoal("wrap"), .trigger("rising"), .behavior("new")) counter_2 (
    .load(or_3_out), .D({16{1'b0}}), .Q(C1), .clk(CLK));  // open: count, carry, clr, preset, down
  Counter #(.width(16), .max('hffff), .ongoal("wrap"), .trigger("rising"), .behavior("new")) counter_3 (
    .load(or_4_out), .D({16{1'b0}}), .Q(C2), .clk(CLK));  // open: count, carry, clr, preset, down
  Counter #(.width(16), .max('hffff), .ongoal("wrap"), .trigger("rising"), .behavior("new")) counter_4 (
    .load(or_5_out), .D({16{1'b0}}), .Q(C3), .clk(CLK));  // open: count, carry, clr, preset, down
  Counter #(.width(16), .max('hffff), .ongoal("wrap"), .trigger("rising"), .behavior("new")) counter_5 (
    .load(or_6_out), .D({16{1'b0}}), .Q(C4), .clk(CLK));  // open: count, carry, clr, preset, down
  Counter #(.width(16), .max('hffff), .ongoal("wrap"), .trigger("rising"), .behavior("new")) counter_6 (
    .load(or_7_out), .D({16{1'b0}}), .Q(C5), .clk(CLK));  // open: count, carry, clr, preset, down
  Counter #(.width(16), .max('hffff), .ongoal("wrap"), .trigger("rising"), .behavior("new")) counter_7 (
    .load(or_8_out), .D({16{1'b0}}), .Q(C6), .clk(CLK));  // open: count, carry, clr, preset, down
  Counter #(.width(16), .max('hffff), .ongoal("wrap"), .trigger("rising"), .behavior("new")) counter_8 (
    .load(or_9_out), .D({16{1'b0}}), .Q(C7), .clk(CLK));  // open: count, carry, clr, preset, down
  Register #(.width(32), .trigger("rising"), .Select("low")) register_9 (
    .D(EX_PC), .en(write0), .Q(tag0), .clk(CLK));  // open: clr
  Register #(.width(32), .trigger("rising"), .Select("low")) register_10 (
    .D(EX_PC), .en(write1), .Q(tag1), .clk(CLK));  // open: clr
  Register #(.width(32), .trigger("rising"), .Select("low")) register_11 (
    .D(EX_PC), .en(write2), .Q(tag2), .clk(CLK));  // open: clr
  Register #(.width(32), .trigger("rising"), .Select("low")) register_12 (
    .D(EX_PC), .en(write3), .Q(tag3), .clk(CLK));  // open: clr
  Register #(.width(32), .trigger("rising"), .Select("low")) register_13 (
    .D(EX_PC), .en(write4), .Q(tag4), .clk(CLK));  // open: clr
  Register #(.width(32), .trigger("rising"), .Select("low")) register_14 (
    .D(EX_PC), .en(write5), .Q(tag5), .clk(CLK));  // open: clr
  Register #(.width(32), .trigger("rising"), .Select("low")) register_15 (
    .D(EX_PC), .en(write6), .Q(tag6), .clk(CLK));  // open: clr
  Register #(.width(32), .trigger("rising"), .Select("low")) register_16 (
    .D(EX_PC), .en(write7), .Q(tag7), .clk(CLK));  // open: clr
  Register #(.width(32), .trigger("rising"), .Select("low")) register_17 (
    .D(EX_BranchAddr), .en(CLK), .Q(Addr0), .clk(CLK));  // open: clr
  Register #(.width(32), .trigger("rising"), .Select("low")) register_18 (
    .D(EX_BranchAddr), .en(CLK), .Q(Addr1), .clk(CLK));  // open: clr
  Register #(.width(32), .trigger("rising"), .Select("low")) register_19 (
    .D(EX_BranchAddr), .en(CLK), .Q(Addr2), .clk(CLK));  // open: clr
  Register #(.width(32), .trigger("rising"), .Select("low")) register_20 (
    .D(EX_BranchAddr), .en(CLK), .Q(Addr3), .clk(CLK));  // open: clr
  Register #(.width(32), .trigger("rising"), .Select("low")) register_21 (
    .D(EX_BranchAddr), .en(CLK), .Q(Addr4), .clk(CLK));  // open: clr
  Register #(.width(32), .trigger("rising"), .Select("low")) register_22 (
    .D(EX_BranchAddr), .en(CLK), .Q(Addr5), .clk(CLK));  // open: clr
  Register #(.width(32), .trigger("rising"), .Select("low")) register_23 (
    .D(EX_BranchAddr), .en(CLK), .Q(Addr6), .clk(CLK));  // open: clr
  Register #(.width(32), .trigger("rising"), .Select("low")) register_24 (
    .D(EX_BranchAddr), .en(write7), .Q(Addr7), .clk(CLK));  // open: clr
  Multiplexer #(.select(1), .width(2), .disabled("Z"), .enable("false")) multiplexer_6 (
    .in0(2'b01), .in1(2'b10), .out(multiplexer_6_out), .sel(EX_BranchTaken));
  Multiplexer #(.select(1), .width(2), .disabled("Z"), .enable("false")) multiplexer_7 (
    .in0(Next), .in1(multiplexer_6_out), .out(multiplexer_7_out), .sel(CLK));
  Multiplexer #(.select(1), .width(2), .disabled("Z"), .enable("false")) multiplexer_8 (
    .in0(Next), .in1(multiplexer_6_out), .out(multiplexer_8_out), .sel(CLK));
  Multiplexer #(.select(1), .width(2), .disabled("Z"), .enable("false")) multiplexer_9 (
    .in0(Next), .in1(multiplexer_6_out), .out(multiplexer_9_out), .sel(CLK));
  Multiplexer #(.select(1), .width(2), .disabled("Z"), .enable("false")) multiplexer_10 (
    .in0(Next), .in1(multiplexer_6_out), .out(multiplexer_10_out), .sel(CLK));
  Multiplexer #(.select(1), .width(2), .disabled("Z"), .enable("false")) multiplexer_11 (
    .in0(Next), .in1(multiplexer_6_out), .out(multiplexer_11_out), .sel(CLK));
  Multiplexer #(.select(1), .width(2), .disabled("Z"), .enable("false")) multiplexer_12 (
    .in0(Next), .in1(multiplexer_6_out), .out(multiplexer_12_out), .sel(CLK));
  Multiplexer #(.select(1), .width(2), .disabled("Z"), .enable("false")) multiplexer_13 (
    .in0(Next), .in1(multiplexer_6_out), .out(multiplexer_13_out), .sel(CLK));
  Multiplexer #(.select(1), .width(2), .disabled("Z"), .enable("false")) multiplexer_14 (
    .in0(Next), .in1(multiplexer_6_out), .out(multiplexer_14_out), .sel(write7));
  and and_18 (and_18_out, EX_Branch, \行0 );
  and and_19 (and_19_out, EX_Branch, \行1 );
  and and_20 (and_20_out, EX_Branch, \行2 );
  and and_21 (and_21_out, EX_Branch, \行3 );
  and and_22 (and_22_out, EX_Branch, \行4 );
  and and_23 (and_23_out, EX_Branch, \行5 );
  and and_24 (and_24_out, EX_Branch, \行6 );
  and and_25 (and_25_out, EX_Branch, \行7 );
  \Max归并比较  \max归并比较_1  (
    .Y(C1), .X(C0), .Y_num(3'b001), .X_num(3'b000), .MAX(\max归并比较_1_max ), .Max_num(\max归并比较_1_max_num ));
  \Max归并比较  \max归并比较_2  (
    .Y(C3), .X(C2), .Y_num(3'b011), .X_num(3'b010), .MAX(\max归并比较_2_max ), .Max_num(\max归并比较_2_max_num ));
  \Max归并比较  \max归并比较_3  (
    .Y(C5), .X(C4), .Y_num(3'b101), .X_num(3'b100), .MAX(\max归并比较_3_max ), .Max_num(\max归并比较_3_max_num ));
  \Max归并比较  \max归并比较_4  (
    .Y(C7), .X(C6), .Y_num(3'b111), .X_num(3'b110), .MAX(\max归并比较_4_max ), .Max_num(\max归并比较_4_max_num ));
  Register #(.width(2), .trigger("rising"), .Select("low")) register_25 (
    .D(multiplexer_7_out), .en(and_18_out), .Q(Predict0), .clk(CLK));  // open: clr
  Register #(.width(2), .trigger("rising"), .Select("low")) register_26 (
    .D(multiplexer_8_out), .en(and_19_out), .Q(Predict1), .clk(CLK));  // open: clr
  Register #(.width(2), .trigger("rising"), .Select("low")) register_27 (
    .D(multiplexer_9_out), .en(and_20_out), .Q(Predict2), .clk(CLK));  // open: clr
  Register #(.width(2), .trigger("rising"), .Select("low")) register_28 (
    .D(multiplexer_10_out), .en(and_21_out), .Q(Predict3), .clk(CLK));  // open: clr
  Register #(.width(2), .trigger("rising"), .Select("low")) register_29 (
    .D(multiplexer_11_out), .en(and_22_out), .Q(Predict4), .clk(CLK));  // open: clr
  Register #(.width(2), .trigger("rising"), .Select("low")) register_30 (
    .D(multiplexer_12_out), .en(and_23_out), .Q(Predict5), .clk(CLK));  // open: clr
  Register #(.width(2), .trigger("rising"), .Select("low")) register_31 (
    .D(multiplexer_13_out), .en(and_24_out), .Q(Predict6), .clk(CLK));  // open: clr
  Register #(.width(2), .trigger("rising"), .Select("low")) register_32 (
    .D(multiplexer_14_out), .en(and_25_out), .Q(Predict7), .clk(CLK));  // open: clr
  \Max归并比较  \max归并比较_5  (
    .Y(\max归并比较_2_max ), .X(\max归并比较_1_max ), .Y_num(\max归并比较_2_max_num ), .X_num(\max归并比较_1_max_num ),
    .MAX(\max归并比较_5_max ), .Max_num(\max归并比较_5_max_num ));
  \Max归并比较  \max归并比较_6  (
    .Y(\max归并比较_4_max ), .X(\max归并比较_3_max ), .Y_num(\max归并比较_4_max_num ), .X_num(\max归并比较_3_max_num ),
    .MAX(\max归并比较_6_max ), .Max_num(\max归并比较_6_max_num ));
  \Max归并比较  \max归并比较_7  (
    .Y(\max归并比较_6_max ), .X(\max归并比较_5_max ), .Y_num(\max归并比较_6_max_num ), .X_num(\max归并比较_5_max_num ),
    .Max_num(out));  // open: MAX

  // Notes on the sheet:
  //   valid值
endmodule

// Max
module \Max归并比较  (
  input  [15:0] Y,
  input  [15:0] X,
  input  [2:0] Y_num,
  input  [2:0] X_num,
  output [15:0] MAX,
  output [2:0] Max_num
);

  wire comparator_1_eq, comparator_1_gt, or_1_out;

  Multiplexer #(.select(1), .width(16), .disabled("Z"), .enable("false")) multiplexer_1 (
    .in0(Y), .in1(X), .out(MAX), .sel(or_1_out));
  Comparator #(.width(16), .mode("unsigned")) comparator_1 (
    .a(X), .b(Y), .gt(comparator_1_gt), .eq(comparator_1_eq));  // open: lt
  or or_1 (or_1_out, comparator_1_gt, comparator_1_eq);
  Multiplexer #(.select(1), .width(3), .disabled("Z"), .enable("false")) multiplexer_2 (
    .in0(Y_num), .in1(X_num), .out(Max_num), .sel(or_1_out));

  // Notes on the sheet:
  //   输出两个输入中的较大值，并输出较大值的3位编号
endmodule

module FSM (
  input  x,
  input  y,
  input  J,
  output x2,
  output y2
);

  wire and_1_out, and_2_out, and_3_out, and_4_out, not_1_out, not_2_out, not_3_out, not_4_out, not_5_out;

  not not_1 (not_1_out, y);
  not not_2 (not_2_out, x);
  not not_3 (not_3_out, y);
  not not_4 (not_4_out, y);
  not not_5 (not_5_out, J);
  and and_1 (and_1_out, y, J);
  and and_2 (and_2_out, x, not_1_out);
  and and_3 (and_3_out, not_2_out, not_3_out, J);
  and and_4 (and_4_out, x, not_4_out, not_5_out);
  or or_1 (x2, and_1_out, and_2_out);
  or or_2 (y2, and_3_out, and_4_out);
endmodule

module \重定向流水线_动态分支预测  (
  output RegWrite,
  output MemWrite,
  output [31:0] IF_PC,
  output [31:0] ID_PC,
  output [31:0] EX_PC,
  output [31:0] M_PC,
  output [31:0] WB_PC,
  output [31:0] RDin,
  output [31:0] MDin,
  output [31:0] LedData
);

  wire alu_1_equal, alu_1_out_4, and_1_out, and_2_out, and_3_out, and_4_out, and_5_out, and_7_out, and_8_out,
       and_9_out, and_10_out, beq, bge, bne, Branch_BT, BranchTaken, CLK, clock_1_out, comparator_1_eq,
       comparator_1_lt, comparator_2_eq, d_ff_1_q, ecall, EX_Branch, EX_BranchTaken, EX_ecall, EX_halt, EX_J,
       EX_Jal, EX_Jalr, EX_MEM_halt_2, EX_MEM_jal_2, EX_MEM_jalr_2, EX_MEM_memtoreg_2, EX_predJmp,
       EX_RegWrite, EX_SB, flush, Go, halt, ID_Branch, ID_EX_alusrcb_2, ID_EX_memtoreg_2, ID_EX_memwrite_2,
       ID_predJmp, IF_predictJmp, IR1, IR2, IR3, JAL, MEM_RegWrite, MEM_SB, MEM_str, MEM_WB_halt_2,
       MEM_WB_jal_2, MEM_WB_jalr_2, nand_1_out, not_1_out, not_2_out, or_2_out, or_5_out, predError, RST, S,
       S_type, SB, stall, W1, W2, W3, \单周期硬布线控制器_1_alu_src , \单周期硬布线控制器_1_beq , \单周期硬布线控制器_1_bge ,
       \单周期硬布线控制器_1_bne , \单周期硬布线控制器_1_jalr , \单周期硬布线控制器_1_memtoreg , \单周期硬布线控制器_1_memwrite ,
       \单周期硬布线控制器_1_regwrite , \单周期硬布线控制器_1_rs1 , \单周期硬布线控制器_1_rs2 ;
  wire [1:0] MEM_WB_memtoreg_2, rs_F, rs_next, rt_F, rt_next;
  wire [3:0] ID_EX_aluop_2, \单周期硬布线控制器_1_alu_op ;
  wire [4:0] EX_MEM_rd_2, ID_EX_rd_2, multiplexer_5_out, multiplexer_6_out, WB_rd;
  wire [11:0] multiplexer_7_out;
  wire [12:0] CNT_num;
  wire [15:0] \LoadUse次数 , \总周期数 , \插入气泡数 , \无条件分支数 , \条件分支成功数 ;
  wire [31:0] ALU_addr, bit_extender_1_out, bit_extender_2_out, bit_extender_3_out, Branch_addr, EX_IR,
       EX_MEM_pc_4_2, EX_PC_4, ID_EX_imm1_2, ID_EX_imm2_2, ID_EX_r1_2, ID_EX_r2_2, ID_IR, ID_PC_4, IF_IR,
       IF_PC_4, JmpAddr, MDout, MEM_ALUresult, MEM_Din, MEM_IR, MEM_WB_pc_4_2, MEM_WB_readdata_2,
       MEM_WB_result_2, multiplexer_1_out, multiplexer_2_out, multiplexer_8_out, multiplexer_9_out,
       multiplexer_10_out, multiplexer_11_out, Next_PC, predictAddr, regifile_1_r1, regifile_1_r2, SBin,
       shifter_1_out, WB_IR;

  Button \u_总复位  (.out(RST));
  Button _1 (.out(IR1));
  Button _2 (.out(IR2));
  Button _3 (.out(IR3));
  // Probe on \总周期数 
  // Probe on \总周期数 
  or or_1 (EX_BranchTaken, S, EX_Jalr);
  and and_1 (and_1_out, ~stall, or_2_out);  // AND_Gate
  Button \u_继续运行  (.out(Go));
  LED #(.active("true")) led_1 (.in(W1));
  LED #(.active("true")) led_2 (.in(W2));
  LED #(.active("true")) led_3 (.in(W3));
  // Probe on IF_PC[19:0]
  // RiscV_Probe riscv_probe_1: pin names not known; wires that end beside it: IF_IR
  Register #(.width(32), .trigger("rising"), .Select("low")) PC (
    .D(Next_PC), .en(and_1_out), .Q(IF_PC), .clk(CLK), .clr(RST));
  or or_2 (or_2_out, ~halt, Go);  // OR_Gate
  Hex_Digit_Display hex_digit_display_1 (.value(LedData[27:24]));  // open: dp
  Hex_Digit_Display hex_digit_display_2 (.value(LedData[31:28]));  // open: dp
  Hex_Digit_Display hex_digit_display_3 (.value(LedData[23:20]));  // open: dp
  Hex_Digit_Display hex_digit_display_4 (.value(LedData[19:16]));  // open: dp
  // Probe on ID_PC[19:0]
  // RiscV_Probe riscv_probe_2: pin names not known; wires that end beside it: ID_IR
  \重定向处理逻辑  \u_重定向处理逻辑_1  (
    .BranchTaken(predError), .IR(ID_IR), .ecall(ecall), .rs_av(\单周期硬布线控制器_1_rs1 ), .EX_RegWrite(EX_RegWrite),
    .EX_rd(ID_EX_rd_2), .rt_av(\单周期硬布线控制器_1_rs2 ), .MEM_RegWrite(MEM_RegWrite), .MEM_rd(EX_MEM_rd_2),
    .stall(stall), .flush(flush), .EX_MemToReg(ID_EX_memtoreg_2), .rs1Forward(rs_next), .rs2Forward(rt_next));
  or or_3 (EX_J, EX_Jal, EX_Jalr);
  Adder #(.width(32)) adder_1 (.a(IF_PC), .b(32'h4), .out(IF_PC_4));  // open: cin, cout
  Multiplexer #(.select(1), .width(32), .disabled("Z"), .enable("false")) multiplexer_1 (
    .in0(IF_PC_4), .in1(predictAddr), .out(multiplexer_1_out), .sel(IF_predictJmp));
  Multiplexer #(.select(1), .width(32), .disabled("Z"), .enable("false")) multiplexer_2 (
    .in0(EX_PC_4), .in1(JmpAddr), .out(multiplexer_2_out), .sel(EX_BranchTaken));
  Hex_Digit_Display hex_digit_display_5 (.value(LedData[11:8]));  // open: dp
  Hex_Digit_Display hex_digit_display_6 (.value(LedData[15:12]));  // open: dp
  ROM #(.addrWidth(10), .dataWidth(32), .Select("high")) \u_指令存储器  (.addr(IF_PC[11:2]), .data(IF_IR));
  Multiplexer #(.select(1), .width(32), .disabled("Z"), .enable("false")) multiplexer_3 (
    .in0(multiplexer_1_out), .in1(multiplexer_2_out), .out(Next_PC), .sel(predError));
  Hex_Digit_Display hex_digit_display_7 (.value(LedData[7:4]));  // open: dp
  Hex_Digit_Display hex_digit_display_8 (.value(LedData[3:0]));  // open: dp
  // Probe on EX_PC[19:0]
  // RiscV_Probe riscv_probe_3: pin names not known; wires that end beside it: EX_IR
  IF_ID IF_ID (
    .IR(IF_IR), .PC(IF_PC), .PC_4(IF_PC_4), .PredictJump(IF_predictJmp), .IR_2(ID_IR), .PC_2(ID_PC),
    .PC_4_2(ID_PC_4), .PredictJump_2(ID_predJmp), .Reset(RST), .BranchTaken(predError), .En(and_1_out),
    .CLK(CLK));
  Multiplexer #(.select(1), .width(32), .disabled("Z"), .enable("false")) multiplexer_4 (
    .in0(Branch_addr), .in1(ALU_addr), .out(JmpAddr), .sel(EX_Jalr));
  // RiscV_Probe riscv_probe_4: pin names not known; wires that end beside it: MEM_IR
  // Probe on \总周期数 
  // Probe on M_PC[19:0]
  \单周期硬布线控制器  \u_单周期硬布线控制器_1  (
    .Funct({ID_IR[30], ID_IR[25], ID_IR[14:12]}), .OP(ID_IR[6:2]), .ALU_OP(\单周期硬布线控制器_1_alu_op ),
    .MemToReg(\单周期硬布线控制器_1_memtoreg ), .MemWrite(\单周期硬布线控制器_1_memwrite ), .ALU_SRC(\单周期硬布线控制器_1_alu_src ),
    .RegWrite(\单周期硬布线控制器_1_regwrite ), .ecall(ecall), .S_type(S_type), .Jalr(\单周期硬布线控制器_1_jalr ),
    .Beq(\单周期硬布线控制器_1_beq ), .JAL(JAL), .Bne(\单周期硬布线控制器_1_bne ), .in_3(ID_IR[21]), .BGE(\单周期硬布线控制器_1_bge ),
    .SB(SB), .rs1(\单周期硬布线控制器_1_rs1 ), .rs2(\单周期硬布线控制器_1_rs2 ));  // open: uret, csrrsi, csrrci
  Multiplexer #(.select(1), .width(5), .disabled("Z"), .enable("false")) multiplexer_5 (
    .in0(ID_IR[19:15]), .in1(5'b10001), .out(multiplexer_5_out), .sel(ecall));
  Multiplexer #(.select(1), .width(5), .disabled("Z"), .enable("false")) multiplexer_6 (
    .in0(ID_IR[24:20]), .in1(5'b01010), .out(multiplexer_6_out), .sel(ecall));
  Multiplexer #(.select(1), .width(12), .disabled("Z"), .enable("false")) multiplexer_7 (
    .in0(ID_IR[31:20]), .in1({ID_IR[31:25], ID_IR[11:7]}), .out(multiplexer_7_out), .sel(S_type));
  \分支历史表BPB  \u_分支历史表bpb_1  (
    .PC(IF_PC), .EX_PC(EX_PC), .EX_Branch(EX_Branch), .EX_BranchTaken(EX_BranchTaken),
    .EX_BranchAddr(JmpAddr), .CLK(CLK), .PredictJump(IF_predictJmp), .JumpAddr(predictAddr));
  // Probe on \总周期数 
  // Probe on \无条件分支数 
  // Probe on \条件分支成功数 
  // Probe on \插入气泡数 
  // Probe on \LoadUse次数 
  // Probe on WB_PC[19:0]
  // RiscV_Probe riscv_probe_5: pin names not known; wires that end beside it: WB_IR
  or or_4 (ID_Branch, \单周期硬布线控制器_1_beq , \单周期硬布线控制器_1_bge , \单周期硬布线控制器_1_jalr , \单周期硬布线控制器_1_bne , JAL);
  assign bit_extender_1_out = {{20{multiplexer_7_out[11]}}, multiplexer_7_out};  // Bit_Extender bit_extender_1
  assign bit_extender_2_out = {{20{ID_IR[31]}}, {ID_IR[31], ID_IR[7], ID_IR[30:25], ID_IR[11:8]}};  // Bit_Extender bit_extender_2
  assign bit_extender_3_out = {{12{ID_IR[31]}}, {ID_IR[31], ID_IR[19:12], ID_IR[20], ID_IR[30:21]}};  // Bit_Extender bit_extender_3
  // Probe on IF_PC[11:0]
  // Probe on ID_PC[11:0]
  not not_1 (not_1_out, CLK);
  Multiplexer #(.select(1), .width(32), .disabled("Z"), .enable("false")) multiplexer_8 (
    .in0(bit_extender_2_out), .in1(bit_extender_3_out), .out(multiplexer_8_out), .sel(JAL));
  or or_5 (or_5_out, ~halt, Go);  // OR_Gate
  // Probe on EX_PC[11:0]
  D_Flip_Flop #(.trigger("high"), .Pre_Clr_Positions("LEGACY"), .NegatePresetClear("false"), .enable("true"), .NewFFLayout("false")) d_ff_1 (.Q(d_ff_1_q));  // open: clk, D, Qn, preset, en, reset
  Regifile regifile_1 (
    .Din(RDin), .Clk(not_1_out), .R1(regifile_1_r1), .R2(regifile_1_r2), .WE(RegWrite), .W_num(WB_rd),
    .R1_num(multiplexer_5_out), .R2_num(multiplexer_6_out));
  // Probe on WB_PC[11:0]
  // Probe on M_PC[11:0]
  // Probe on 13'hc
  Comparator #(.width(13), .mode("twosComplement")) comparator_1 (
    .a(CNT_num), .b(13'hc), .eq(comparator_1_eq), .lt(comparator_1_lt));  // open: gt
  Clock #(.highDuration(1), .lowDuration(1)) clock_1 (.out(clock_1_out));
  ID_EX ID_EX (
    .Beq(\单周期硬布线控制器_1_beq ), .Beq_2(beq), .Bne(\单周期硬布线控制器_1_bne ), .Bne_2(bne), .Bge(\单周期硬布线控制器_1_bge ),
    .Bge_2(bge), .MemToReg(\单周期硬布线控制器_1_memtoreg ), .MemToReg_2(ID_EX_memtoreg_2),
    .MemWrite(\单周期硬布线控制器_1_memwrite ), .MemWrite_2(ID_EX_memwrite_2), .AluSrcB(\单周期硬布线控制器_1_alu_src ),
    .AluSrcB_2(ID_EX_alusrcb_2), .RegWrite_2(EX_RegWrite), .RegWrite(\单周期硬布线控制器_1_regwrite ),
    .PredictJump(ID_predJmp), .PredictJump_2(EX_predJmp), .Ecall(ecall), .Ecall_2(EX_ecall), .Jal_2(EX_Jal),
    .Jal(JAL), .Jalr(\单周期硬布线控制器_1_jalr ), .Jalr_2(EX_Jalr), .SB(SB), .SB_2(EX_SB), .Reset(RST),
    .flush(flush), .En(or_5_out), .CLK(CLK), .AluOp(\单周期硬布线控制器_1_alu_op ), .AluOp_2(ID_EX_aluop_2),
    .rd(ID_IR[11:7]), .rd_2(ID_EX_rd_2), .R1(regifile_1_r1), .R1_2(ID_EX_r1_2), .R2(regifile_1_r2),
    .R2_2(ID_EX_r2_2), .imm1(bit_extender_1_out), .imm1_2(ID_EX_imm1_2), .imm2(multiplexer_8_out),
    .imm2_2(ID_EX_imm2_2), .PC(ID_PC), .PC_2(EX_PC), .PC_4(ID_PC_4), .PC_4_2(EX_PC_4), .IR(ID_IR),
    .IR_2(EX_IR), .rs1forward(rs_next), .rs1forward_2(rs_F), .rs2forward(rt_next), .rs2forward_2(rt_F),
    .branch(ID_Branch), .branch_2(EX_Branch));
  nand nand_1 (nand_1_out, d_ff_1_q, comparator_1_eq);
  Counter #(.width(13), .max('h1fff), .ongoal("stay"), .trigger("rising"), .behavior("old")) counter_1 (
    .count(comparator_1_lt), .Q(CNT_num), .clk(clock_1_out));  // open: load, D, carry, clr, preset
  Multiplexer #(.select(2), .width(32), .disabled("Z"), .enable("false")) multiplexer_9 (
    .in0(ID_EX_r2_2), .in1(RDin), .in2(MEM_ALUresult), .out(multiplexer_9_out), .sel(rt_F));  // open: in3
  xor xor_1 (predError, EX_BranchTaken, EX_predJmp);
  assign CLK = nand_1_out ? clock_1_out : 1'bz;  // Controlled_Buffer controlled_buffer_1
  Pull_Resistor #(.pull(1)) pull_resistor_1 (.node(CLK));
  Multiplexer #(.select(2), .width(32), .disabled("Z"), .enable("false")) multiplexer_10 (
    .in0(ID_EX_r1_2), .in1(RDin), .in2(MEM_ALUresult), .out(multiplexer_10_out), .sel(rs_F));  // open: in3
  Shifter #(.width(32), .shift("ll")) shifter_1 (.in(ID_EX_imm2_2), .\dist (5'b00001), .out(shifter_1_out));
  Multiplexer #(.select(1), .width(32), .disabled("Z"), .enable("false")) multiplexer_11 (
    .in0(multiplexer_9_out), .in1(ID_EX_imm1_2), .out(multiplexer_11_out), .sel(ID_EX_alusrcb_2));
  Comparator #(.width(32), .mode("unsigned")) comparator_2 (
    .a(multiplexer_10_out), .b(32'ha), .eq(comparator_2_eq));  // open: gt, lt
  and and_2 (and_2_out, EX_ecall, ~comparator_2_eq);  // AND_Gate
  not not_2 (not_2_out, halt);
  and and_3 (and_3_out, alu_1_equal, beq);
  and and_4 (and_4_out, ~alu_1_equal, bne);  // AND_Gate
  and and_5 (and_5_out, alu_1_out_4, bge);
  ALU alu_1 (
    .X(multiplexer_10_out), .Y(multiplexer_11_out), .AluOP(ID_EX_aluop_2), .Equal(alu_1_equal),
    .Result(ALU_addr), .out_4(alu_1_out_4));  // open: Result_2, out_6
  Adder #(.width(32)) adder_2 (.a(shifter_1_out), .b(EX_PC), .out(Branch_addr));  // open: cin, cout
  and and_6 (EX_halt, EX_ecall, comparator_2_eq);
  Register #(.width(32), .trigger("rising"), .Select("low")) register_1 (
    .D(multiplexer_9_out), .en(and_2_out), .Q(LedData), .clk(CLK));  // open: clr
  Counter #(.width(16), .max('hffff), .ongoal("wrap"), .trigger("rising"), .behavior("old")) counter_2 (
    .count(not_2_out), .Q(\总周期数 ), .clk(CLK));  // open: load, D, carry, clr, preset
  or or_6 (Branch_BT, and_5_out, and_4_out, and_3_out);
  or or_7 (S, Branch_BT, EX_Jal);
  and and_7 (and_7_out, not_2_out, EX_J);
  Multiplexer #(.select(1), .width(32), .disabled("Z"), .enable("false")) multiplexer_12 (
    .in0(MDin), .in1(SBin), .out(MEM_Din), .sel(MEM_SB));
  Counter #(.width(16), .max('hffff), .ongoal("wrap"), .trigger("rising"), .behavior("old")) counter_3 (
    .count(and_7_out), .Q(\无条件分支数 ), .clk(CLK));  // open: load, D, carry, clr, preset
  EX_MEM EX_MEM (
    .MemToReg(ID_EX_memtoreg_2), .MemToReg_2(EX_MEM_memtoreg_2), .MemWrite(ID_EX_memwrite_2),
    .MemWrite_2(MemWrite), .RegWrite(EX_RegWrite), .RegWrite_2(MEM_RegWrite), .Jal(EX_Jal),
    .Jal_2(EX_MEM_jal_2), .Jalr(EX_Jalr), .Jalr_2(EX_MEM_jalr_2), .SB(EX_SB), .SB_2(MEM_SB), .rd(ID_EX_rd_2),
    .rd_2(EX_MEM_rd_2), .Reset(RST), .En(or_5_out), .CLK(CLK), .PC(EX_PC), .PC_2(M_PC), .PC_4(EX_PC_4),
    .PC_4_2(EX_MEM_pc_4_2), .IR(EX_IR), .IR_2(MEM_IR), .WriteData(multiplexer_9_out), .WriteData_2(MDin),
    .result(ALU_addr), .result_2(MEM_ALUresult), .halt(EX_halt), .halt_2(EX_MEM_halt_2));
  or or_8 (MEM_str, MemWrite, MEM_SB);
  Counter #(.width(16), .max('hffff), .ongoal("wrap"), .trigger("rising"), .behavior("old")) counter_4 (
    .count(and_8_out), .Q(\条件分支成功数 ), .clk(CLK));  // open: load, D, carry, clr, preset
  and and_8 (and_8_out, not_2_out, Branch_BT);
  RAM #(.addrWidth(10), .dataWidth(32), .bus("separate"), .Select("high")) ram_1 (
    .addr(MEM_ALUresult[11:2]), .din(MEM_Din), .data(MDout), .str(MEM_str), .sel(1'b1), .clk(CLK), .ld(1'b1),
    .clr(RST));
  Counter #(.width(16), .max('hffff), .ongoal("wrap"), .trigger("rising"), .behavior("old")) counter_5 (
    .count(and_9_out), .Q(\插入气泡数 ), .clk(CLK));  // open: load, D, carry, clr, preset
  and and_9 (and_9_out, not_2_out, BranchTaken);
  and and_10 (and_10_out, not_2_out, stall);
  Multiplexer #(.select(2), .width(32), .disabled("Z"), .enable("false")) multiplexer_13 (
    .in0({MDout[31:8], MDin[7:0]}), .in1({MDout[31:16], MDin[7:0], MDout[7:0]}),
    .in2({MDout[31:24], MDin[7:0], MDout[15:0]}), .in3({MDin[7:0], MDout[23:0]}), .out(SBin),
    .sel(MEM_ALUresult[1:0]));
  Counter #(.width(16), .max('hffff), .ongoal("wrap"), .trigger("rising"), .behavior("old")) counter_6 (
    .count(and_10_out), .Q(\LoadUse次数 ), .clk(CLK));  // open: load, D, carry, clr, preset
  MEM_WB MEM_WB (
    .result(MEM_ALUresult), .result_2(MEM_WB_result_2), .MemToReg(EX_MEM_memtoreg_2), .ReadData(MDout),
    .MemToReg_2(MEM_WB_memtoreg_2[0]), .ReadData_2(MEM_WB_readdata_2), .PC(M_PC), .RegWrite(MEM_RegWrite),
    .PC_2(WB_PC), .RegWrite_2(RegWrite), .Jal(EX_MEM_jal_2), .Jal_2(MEM_WB_jal_2), .PC_4(EX_MEM_pc_4_2),
    .Jalr(EX_MEM_jalr_2), .PC_4_2(MEM_WB_pc_4_2), .Jalr_2(MEM_WB_jalr_2), .IR(MEM_IR), .IR_2(WB_IR),
    .rd(EX_MEM_rd_2), .rd_2(WB_rd), .Reset(RST), .En(or_5_out), .CLK(CLK), .halt(EX_MEM_halt_2),
    .halt_2(MEM_WB_halt_2));
  or or_9 (MEM_WB_memtoreg_2[1], MEM_WB_jal_2, MEM_WB_jalr_2);
  Multiplexer #(.select(2), .width(32), .disabled("Z"), .enable("false")) multiplexer_14 (
    .in0(MEM_WB_result_2), .in1(MEM_WB_readdata_2), .in2(MEM_WB_pc_4_2), .out(RDin), .sel(MEM_WB_memtoreg_2));  // open: in3
  D_Flip_Flop #(.trigger("rising"), .Pre_Clr_Positions("ABOVE_BELOW"), .NegatePresetClear("false"), .enable("true"), .NewFFLayout("true")) d_ff_2 (
    .clk(MEM_WB_halt_2), .D(1'b1), .Q(halt), .en(1'b1), .reset(Go));  // open: Qn, preset

  // Other names for the same wires on the sheet: SB_sel[1:0] = MEM_ALUresult[1:0]; MEM_PC[31:0] = M_PC;
  //   SelJmp[1:0] = {EX_Jal, EX_Jalr}; WB_RegWrite = RegWrite

  // Notes on the sheet:
  //   中断源
  //   时空图监测，可删除
  //   中断等待指示
  //   数码管输出
  //   contents of 指令存储器 (hex, n*v repeats v):
  //   100493 100006f 100493 200913 300993 100006f 100493 200913 300993 100006f 100493 200913 300993
  //   100006f 100493 200913 300993 29c000ef 100413 100493 1f49493 900533 2200893 73 24d493 48463 fedff06f
  //   900533 2200893 73 100493 249493 900533 2200893 73 48463 fedff06f 100493 1f49493 900533 2200893 73
  //   4034d493 900533 2200893 73 4044d493 900533 2200893 73 4044d493 900533 2200893 73 4044d493 900533
  //   2200893 73 4044d493 900533 2200893 73 4044d493 900533 2200893 73 4044d493 900533 2200893 73 4044d493
  //   900533 2200893 73 100413 1f41993 41f9d993 433 c00913 300b13 140413 f47413 800293 100313 499993
  //   89e9b3 1300533 2200893 73 406282b3 fe0294e3 140413 f00f93 1f47433 1c41413 800293 100313 49d993
  //   89e9b3 1300533 2200893 73 406282b3 fe0294e3 1c45413 406b0b33 b0463 f95ff06f 2b3 fff2c293 829293
  //   ff2e293 500533 2200893 73 fff00413 493 84a023 140413 448493 84a023 140413 448493 84a023 140413
  //   448493 84a023 140413 448493 84a023 140413 448493 84a023 140413 448493 84a023 140413 448493 84a023
  //   140413 448493 84a023 140413 448493 84a023 140413 448493 84a023 140413 448493 84a023 140413 448493
  //   84a023 140413 448493 84a023 140413 448493 84a023 140413 448493 84a023 140413 448493 140413 433
  //   3c00493 42983 4aa03 149a2b3 28663 134a023 1442023 ffc48493 fe9412e3 800533 2200893 73 440413 3c00493
  //   fc9416e3 a00893 73 413 140413 800533 2200893 73 240413 800533 2200893 73 340413 800533 2200893 73
  //   440413 800533 2200893 73 540413 800533 2200893 73 640413 800533 2200893 73 740413 800533 2200893 73
  //   840413 800533 2200893 2200893 73 8067
  //   JAL
  //   JALR
  //   SB
  //   指令字
  //   B.Inst. Imm
  //   rd
  //   Beq
  //   Bge
  //   Bne
  //   URET
  //   J.Inst. Imm
  //   MemToReg
  //   MemWrite
  //   AluOP
  //   AluSrcB
  //   RegWrite
  //   控制位
  //   暂停节拍，不能为0
  //   流水调试日志用
  //   戳工具置1进入计数暂停模式，ctrl+k时钟自动运行到对应节拍暂停
  //   ctrl+k关闭时钟连续运行，将控制位置零，进入单步调试模式调试
  //   可计数暂停的时钟源
  //   为方便自动评测，需要输出流水线各段保存的PC值，注意是PC不是PC+4，另外ID段寄存器写入信息，Mem段内存写入信息也要输出
  //   SB指令模块
endmodule
